// Logisim project cpu24-lb&bgtz-中断.circ as structural Verilog: 24 circuits, main circuit ◇单周期MIPS
module \单周期MIPS  (
  input  IR1,
  input  IR2,
  input  IR3,
  output RegWrite,
  output MemWrite,
  output [31:0] PC,
  output [31:0] IR,
  output [31:0] RDin,
  output [31:0] MDin,
  output [31:0] LedData
);

  wire AluSrcB, and_1_out, and_2_out, and_4_out, and_5_out, and_6_out, and_7_out, Beq, BGTZ, Bne, CLK,
       clock_2_out, comparator_1_eq, comparator_1_lt, comparator_2_gt, comparator_3_eq, comparator_4_eq,
       d_ff_1_q, Go, IR1_t, IR2_t, IR3_t, IRA, IRB, IRC, JAL, LB, MemToReg, mips_alu_1_equal,
       multiplexer_4_out, nand_1_out, not_2_out, NotEqual, or_4_out, RegDst, SignedExt, Syscall, W1, W2, W3;
  wire [1:0] \单周期硬布线控制器_1_jr ;
  wire [3:0] AluOP;
  wire [4:0] multiplexer_5_out, multiplexer_6_out, multiplexer_8_out, multiplexer_9_out, multiplexer_12_out,
       Shamt;
  wire [7:0] multiplexer_16_out;
  wire [12:0] CNT_num;
  wire [15:0] \总周期数 ;
  wire [27:0] shifter_1_out;
  wire [31:0] adder_2_out, bit_extender_1_out, bit_extender_2_out, bit_extender_3_out, mips_alu_1_result,
       multiplexer_1_out, multiplexer_2_out, multiplexer_3_out, multiplexer_7_out, multiplexer_10_out,
       multiplexer_11_out, multiplexer_14_out, multiplexer_15_out, PC_4, PC_q, ram_1_data, shifter_2_out;
  wire [31:5] mips_regifile_1_r1;

  Clock #(.highDuration(1), .lowDuration(1)) clock_1 ();  // open: out
  Button _1 (.out(IRA));
  Button _2 (.out(IRB));
  Button _3 (.out(IRC));
  Button \u_继续运行  (.out(Go));
  LED #(.active("true")) led_1 (.in(W1));
  LED #(.active("true")) led_2 (.in(W2));
  LED #(.active("true")) led_3 (.in(W3));
  Multiplexer #(.select(1), .width(32), .disabled("Z"), .enable("false")) multiplexer_1 (
    .in0(PC_4), .in1(adder_2_out), .out(multiplexer_1_out), .sel(or_4_out));
  Hex_Digit_Display hex_digit_display_1 (.value(LedData[31:28]));  // open: dp
  D_Flip_Flop #(.trigger("high"), .Pre_Clr_Positions("LEGACY"), .NegatePresetClear("false"), .enable("true"), .NewFFLayout("false")) d_ff_1 (.Q(d_ff_1_q));  // open: clk, D, Qn, preset, en, reset
  // Probe on 13'h299
  Multiplexer #(.select(1), .width(32), .disabled("Z"), .enable("false")) multiplexer_2 (
    .in0(multiplexer_3_out), .in1(adder_2_out), .out(multiplexer_2_out), .sel(and_1_out));
  Register #(.width(32), .trigger("rising"), .Select("low")) u_PC (
    .D(multiplexer_2_out), .en(multiplexer_4_out), .Q(PC_q), .clk(CLK), .clr(1'b0));
  Multiplexer #(.select(2), .width(32), .disabled("Z"), .enable("false")) multiplexer_3 (
    .in0(multiplexer_1_out), .in1({mips_regifile_1_r1, Shamt}), .in2({PC_4[31:28], shifter_1_out}),
    .in3({mips_regifile_1_r1, Shamt}), .out(multiplexer_3_out), .sel(\单周期硬布线控制器_1_jr ));
  Multiplexer #(.select(1), .width(1), .disabled("Z"), .enable("false")) multiplexer_4 (
    .in0(1'b1), .in1(Go), .out(multiplexer_4_out), .sel(and_2_out));
  Hex_Digit_Display hex_digit_display_2 (.value(LedData[27:24]));  // open: dp
  Hex_Digit_Display hex_digit_display_3 (.value(LedData[23:20]));  // open: dp
  Comparator #(.width(13), .mode("twosComplement")) comparator_1 (
    .a(CNT_num), .b(13'h299), .eq(comparator_1_eq), .lt(comparator_1_lt));  // open: gt
  Clock #(.highDuration(1), .lowDuration(1)) clock_2 (.out(clock_2_out));
  Comparator #(.width(32), .mode("twosComplement")) comparator_2 (
    .a({mips_regifile_1_r1, Shamt}), .b({32{1'b0}}), .gt(comparator_2_gt));  // open: eq, lt
  and and_1 (and_1_out, comparator_2_gt, BGTZ);
  Adder #(.width(32)) adder_1 (.a(PC_q), .b(32'h4), .out(PC_4));  // open: cin, cout
  Counter #(.width(16), .max('hffff), .ongoal("wrap"), .trigger("rising"), .behavior("old")) counter_1 (
    .load(1'b0), .count(multiplexer_4_out), .Q(\总周期数 ), .clk(CLK), .clr(1'b0));  // open: D, carry, preset
  and and_2 (and_2_out, Syscall, NotEqual);
  Hex_Digit_Display hex_digit_display_4 (.value(LedData[19:16]));  // open: dp
  Hex_Digit_Display hex_digit_display_5 (.value(LedData[15:12]));  // open: dp
  nand nand_1 (nand_1_out, d_ff_1_q, comparator_1_eq);
  Counter #(.width(13), .max('h1fff), .ongoal("stay"), .trigger("rising"), .behavior("old")) counter_2 (
    .count(comparator_1_lt), .Q(CNT_num), .clk(clock_2_out));  // open: load, D, carry, clr, preset
  assign PC = PC_q & 32'hffff;  // AND_Gate and_3, 32 bits wide
  Hex_Digit_Display hex_digit_display_6 (.value(LedData[11:8]));  // open: dp
  Hex_Digit_Display hex_digit_display_7 (.value(LedData[7:4]));  // open: dp
  // Probe on \总周期数 
  ROM #(.addrWidth(10), .dataWidth(32), .Select("high")) rom_1 (.addr(PC_q[11:2]));  // open: data
  ROM #(.addrWidth(10), .dataWidth(32), .Select("high")) rom_2 (.addr(PC_q[11:2]), .data(IR));
  Hex_Digit_Display hex_digit_display_8 (.value(LedData[3:0]));  // open: dp
  assign CLK = nand_1_out ? clock_2_out : 1'bz;  // Controlled_Buffer controlled_buffer_1
  Pull_Resistor #(.pull(1)) pull_resistor_1 (.node(CLK));
  // Mips_Probe mips_probe_1: pin names not known; wires that end beside it: IR
  Multiplexer #(.select(1), .width(5), .disabled("Z"), .enable("false")) multiplexer_5 (
    .in0(IR[25:21]), .in1(5'b00010), .out(multiplexer_5_out), .sel(Syscall));
  assign bit_extender_1_out = {{16{1'b0}}, IR[15:0]};  // Bit_Extender bit_extender_1
  assign bit_extender_2_out = {{16{IR[15]}}, IR[15:0]};  // Bit_Extender bit_extender_2
  Shifter #(.width(28), .shift("ll")) shifter_1 (.in(IR[27:0]), .\dist (5'b00010), .out(shifter_1_out));
  or or_1 (IR1_t, IR1, IRA);
  \单周期硬布线控制器  \u_单周期硬布线控制器_1  (
    .Func(IR[5:0]), .OP(IR[31:26]), .ALU_OP(AluOP), .MemToReg(MemToReg), .MemWrite(MemWrite),
    .ALU_SRC(AluSrcB), .RegWrite(RegWrite), .SysCALL(Syscall), .SignedExt(SignedExt), .RegDst(RegDst),
    .JR(\单周期硬布线控制器_1_jr [0]), .JMP(\单周期硬布线控制器_1_jr [1]), .Beq(Beq), .JAL(JAL), .Bne(Bne), .LB(LB), .BGTZ(BGTZ));
  Multiplexer #(.select(1), .width(5), .disabled("Z"), .enable("false")) multiplexer_6 (
    .in0(IR[20:16]), .in1(IR[15:11]), .out(multiplexer_6_out), .sel(RegDst));
  Multiplexer #(.select(1), .width(32), .disabled("Z"), .enable("false")) multiplexer_7 (
    .in0(bit_extender_1_out), .in1(bit_extender_2_out), .out(multiplexer_7_out), .sel(SignedExt));
  or or_2 (IR2_t, IR2, IRB);
  Multiplexer #(.select(1), .width(5), .disabled("Z"), .enable("false")) multiplexer_8 (
    .in0(IR[20:16]), .in1(5'b00100), .out(multiplexer_8_out), .sel(Syscall));
  Multiplexer #(.select(1), .width(5), .disabled("Z"), .enable("false")) multiplexer_9 (
    .in0(multiplexer_6_out), .in1({5{1'b1}}), .out(multiplexer_9_out), .sel(JAL));
  Shifter #(.width(32), .shift("ll")) shifter_2 (.in(multiplexer_7_out), .\dist (5'b00010), .out(shifter_2_out));
  Adder #(.width(32)) adder_2 (.a(shifter_2_out), .b(PC_4), .out(adder_2_out));  // open: cin, cout
  or or_3 (IR3_t, IR3, IRC);
  or or_4 (or_4_out, and_6_out, and_4_out);
  MIPS_Regifile mips_regifile_1 (
    .Din(RDin), .Clk(CLK), .R1({mips_regifile_1_r1, Shamt}), .R2(MDin), .WE(RegWrite),
    .W_num(multiplexer_9_out), .R1_num(multiplexer_5_out), .R2_num(multiplexer_8_out));
  and and_4 (and_4_out, Beq, mips_alu_1_equal);
  Multiplexer #(.select(1), .width(32), .disabled("Z"), .enable("false")) multiplexer_10 (
    .in0(MDin), .in1(multiplexer_7_out), .out(multiplexer_10_out), .sel(AluSrcB));
  Comparator #(.width(6), .mode("twosComplement")) comparator_3 (
    .a(IR[31:26]), .b({6{1'b0}}), .eq(comparator_3_eq));  // open: gt, lt
  and and_5 (and_5_out, comparator_3_eq, comparator_4_eq);
  Comparator #(.width(6), .mode("twosComplement")) comparator_4 (
    .a(IR[5:0]), .b(6'b000100), .eq(comparator_4_eq));  // open: gt, lt
  not not_1 (NotEqual, mips_alu_1_equal);
  and and_6 (and_6_out, Bne, not_2_out);
  not not_2 (not_2_out, mips_alu_1_equal);
  Multiplexer #(.select(1), .width(32), .disabled("Z"), .enable("false")) multiplexer_11 (
    .in0(multiplexer_10_out), .in1(32'h22), .out(multiplexer_11_out), .sel(Syscall));
  Multiplexer #(.select(1), .width(5), .disabled("Z"), .enable("false")) multiplexer_12 (
    .in0(IR[10:6]), .in1(Shamt), .out(multiplexer_12_out), .sel(and_5_out));
  and and_7 (and_7_out, mips_alu_1_equal, Syscall);
  MIPS_ALU mips_alu_1 (
    .X({mips_regifile_1_r1, Shamt}), .Y(multiplexer_11_out), .AluOP(AluOP), .Equal(mips_alu_1_equal),
    .Result(mips_alu_1_result), .shamt(multiplexer_12_out));  // open: Result_2
  Multiplexer #(.select(1), .width(32), .disabled("Z"), .enable("false")) multiplexer_13 (
    .in0(multiplexer_14_out), .in1(PC_4), .out(RDin), .sel(JAL));
  Register #(.width(32), .trigger("rising"), .Select("low")) register_1 (
    .D(MDin), .en(and_7_out), .Q(LedData), .clk(CLK), .clr(1'b0));
  RAM #(.addrWidth(10), .dataWidth(32), .bus("separate"), .Select("high")) ram_1 (
    .addr(mips_alu_1_result[11:2]), .din(MDin), .data(ram_1_data), .str(MemWrite), .clk(CLK), .clr(1'b0));  // open: sel, ld
  Multiplexer #(.select(1), .width(32), .disabled("Z"), .enable("false")) multiplexer_14 (
    .in0(multiplexer_15_out), .in1(bit_extender_3_out), .out(multiplexer_14_out), .sel(LB));
  Multiplexer #(.select(1), .width(32), .disabled("Z"), .enable("false")) multiplexer_15 (
    .in0(mips_alu_1_result), .in1(ram_1_data), .out(multiplexer_15_out), .sel(MemToReg));
  Multiplexer #(.select(2), .width(8), .disabled("Z"), .enable("false")) multiplexer_16 (
    .in0(multiplexer_15_out[7:0]), .in1(multiplexer_15_out[15:8]), .in2(multiplexer_15_out[23:16]),
    .in3(multiplexer_15_out[31:24]), .out(multiplexer_16_out), .sel(mips_alu_1_result[1:0]));
  assign bit_extender_3_out = {{24{multiplexer_16_out[7]}}, multiplexer_16_out};  // Bit_Extender bit_extender_3

  // Notes on the sheet:
  //   中断源
  //   中断等待指示
  //   总复位信号应将除ROM以外所有存储组件全部清零
  //   控制位
  //   暂停节拍，不能为0
  //   戳工具置1进入计数暂停模式，ctrl+k时钟自动运行到对应节拍暂停
  //   ctrl+k关闭时钟连续运行，将控制位置零，进入单步调试模式调试
  //   用这个时钟源需要去掉电路中的其他时钟源
  //   数码管输出
  //   指令存储器
  //   数码管输出应该用寄存器锁存，否则显示数据只能一闪而过
  //   可计数暂停的时钟源
  //   contents of rom_1 (hex, n*v repeats v):
  //   2011000f 112020 20020022 c 2231ffff 1e20fffb 2002000a c
  //   指令字
  //   contents of rom_2 (hex, n*v repeats v):
  //   20110001 8000c05 20110001 20120002 20130003 8000c09 20110001 20120002 20130003 8000c0d 20110001
  //   20120002 20130003 8000c11 20110001 20120002 20130003 c000cb8 20100001 20110001 118fc0 112020
  //   20020022 c 118882 12200001 8000c15 112020 20020022 c 20110001 118880 112020 20020022 c 12200001
  //   8000c1f 20110001 118fc0 112020 20020022 c 1188c3 112020 20020022 c 118903 112020 20020022 c 118903
  //   112020 20020022 c 118903 112020 20020022 c 118903 112020 20020022 c 118903 112020 20020022 c 118903
  //   112020 20020022 c 118903 112020 20020022 c 20100001 109fc0 139fc3 8021 2012000c 24160003 26100001
  //   3210000f 20080008 20090001 139900 2709825 132020 20020022 c 1094022 1500fff9 22100001 2018000f
  //   2188024 108700 20080008 20090001 139902 2709825 132021 20020022 c 1094022 1500fff9 108702 2c9b022
  //   12c00001 8000c50 4020 1084027 84400 3508ffff 82021 20020022 c 2010ffff 20110000 ae300000 22100001
  //   22310004 ae300000 22100001 22310004 ae300000 22100001 22310004 ae300000 22100001 22310004 ae300000
  //   22100001 22310004 ae300000 22100001 22310004 ae300000 22100001 22310004 ae300000 22100001 22310004
  //   ae300000 22100001 22310004 ae300000 22100001 22310004 ae300000 22100001 22310004 ae300000 22100001
  //   22310004 ae300000 22100001 22310004 ae300000 22100001 22310004 ae300000 22100001 22310004 ae300000
  //   22100001 22310004 22100001 8020 2011003c 8e130000 8e340000 274402a 11000002 ae330000 ae140000
  //   2231fffc 1611fff8 102020 20020022 c 22100004 2011003c 1611fff2 20020032 c 20100000 22100001 102020
  //   20020022 c 22100002 102020 20020022 c 22100003 102020 20020022 c 22100004 102020 20020022 c 22100005
  //   102020 20020022 c 22100006 102020 20020022 c 22100007 102020 20020022 c 22100008 102020 20020022
  //   20020022 c 3e00008
  //   OP
  //   Func
  //   rs
  //   rt
  //   rd
  //   JMP
  //   JR
  //   LB
  //   BGTZ
  //   OP
  //   Func
  //   Beq
  //   Bne
  //   MemToReg
  //   MemWrite
  //   AluOP
  //   AluSrcB
  //   RegWrite
  //   JAL
  //   RegDst
  //   Syscall
  //   为方便自动评测，需要输出PC，IR，寄存器堆写如数据RDin
  //   RAM写使能MemWrite、RAM写入数据MDin等信号
endmodule

// 单周期硬布线控制器
module \单周期硬布线控制器  (
  input  [5:0] OP,
  input  [5:0] Func,
  output [3:0] ALU_OP,
  output MemToReg,
  output MemWrite,
  output ALU_SRC,
  output RegWrite,
  output SysCALL,
  output SignedExt,
  output RegDst,
  output Beq,
  output Bne,
  output JR,
  output JMP,
  output JAL,
  output LB,
  output BGTZ
);

  \运算控制器自动生成  \u_运算控制器自动生成_1  (
    .OP0(OP[0]), .OP1(OP[1]), .OP2(OP[2]), .OP3(OP[3]), .OP4(OP[4]), .OP5(OP[5]), .F0(Func[0]), .F1(Func[1]),
    .F2(Func[2]), .F3(Func[3]), .F4(Func[4]), .F5(Func[5]), .S0(ALU_OP[0]), .S1(ALU_OP[1]), .S2(ALU_OP[2]),
    .S3(ALU_OP[3]));
  \控制信号自动生成  \u_控制信号自动生成_1  (
    .OP0(OP[0]), .OP1(OP[1]), .OP2(OP[2]), .OP3(OP[3]), .OP4(OP[4]), .OP5(OP[5]), .F0(Func[0]), .F1(Func[1]),
    .F2(Func[2]), .F3(Func[3]), .F4(Func[4]), .F5(Func[5]), .MemToReg(MemToReg), .MemWrite(MemWrite),
    .ALU_SRC(ALU_SRC), .RegWrite(RegWrite), .SysCALL(SysCALL), .SignedExt(SignedExt), .RegDst(RegDst),
    .BEQ(Beq), .BNE(Bne), .JR(JR), .JUMP(JMP), .JAL(JAL));
  \LB_BGTZ控制信号生成  \lb_bgtz控制信号生成_1  (
    .OP1(OP[0]), .OP0(OP[1]), .OP2(OP[2]), .OP3(OP[3]), .OP4(OP[4]), .OP5(OP[5]), .F0(Func[0]), .F1(Func[1]),
    .F2(Func[2]), .F3(Func[3]), .F4(Func[4]), .F5(Func[5]), .LB(LB), .BGTZ(BGTZ));

  // Other names for the same wires on the sheet: OP_CODE[5:0] = OP

  // Notes on the sheet:
  //   运算器控制器，根据指令生成运算器功能选择信号
  //   控制信号生成，产生数据通路需要的其他控制信号
endmodule

// 运算器控制器
module \运算控制器自动生成  (
  input  OP0,
  input  OP1,
  input  OP2,
  input  OP3,
  input  OP4,
  input  OP5,
  input  F0,
  input  F1,
  input  F2,
  input  F3,
  input  F4,
  input  F5,
  output S0,
  output S1,
  output S2,
  output S3
);

  wire and_1_out, and_2_out, and_3_out, and_4_out, and_5_out, and_6_out, and_7_out, and_8_out, and_9_out,
       and_10_out, and_11_out, and_12_out, and_13_out, and_14_out, and_15_out, and_16_out, and_17_out,
       and_18_out, and_19_out, and_20_out, and_21_out, and_22_out, and_23_out, and_24_out, and_25_out,
       and_26_out, and_27_out, and_28_out, and_29_out, and_30_out, and_31_out, and_32_out, and_33_out,
       and_34_out, and_35_out, and_36_out, and_37_out, and_38_out, and_39_out, and_40_out, and_41_out,
       and_42_out, not_1_out, not_2_out, not_3_out, not_4_out, not_5_out, not_6_out, not_7_out, not_8_out,
       not_9_out, not_10_out, not_11_out, not_12_out, not_13_out, not_14_out, not_15_out, not_16_out,
       not_17_out, not_18_out, not_19_out, not_20_out, not_21_out, not_22_out, not_23_out, not_24_out,
       not_25_out, not_26_out, not_27_out, not_28_out, not_29_out, not_30_out, not_31_out, not_32_out,
       not_33_out, not_34_out, not_35_out, not_36_out, not_37_out, not_38_out, not_39_out, not_40_out,
       not_41_out, not_42_out, not_43_out, not_44_out, not_45_out, not_46_out, not_47_out, not_48_out,
       not_49_out, not_50_out, not_51_out, not_52_out, not_53_out, not_54_out, not_55_out, not_56_out,
       not_57_out, not_58_out, not_59_out, not_60_out, not_61_out, not_62_out, not_63_out, not_64_out,
       not_65_out, not_66_out, not_67_out, not_68_out, not_69_out, not_70_out, not_71_out, not_72_out,
       not_73_out, not_74_out, not_75_out, not_76_out, not_77_out, not_78_out, not_79_out, not_80_out,
       not_81_out, not_82_out, not_83_out, not_84_out, not_85_out, not_86_out, not_87_out, not_88_out,
       not_89_out, not_90_out, not_91_out, not_92_out, not_93_out, not_94_out, not_95_out, not_96_out,
       not_97_out, not_98_out, not_99_out, not_100_out, not_101_out, not_102_out, not_103_out, not_104_out,
       not_105_out, not_106_out, not_107_out, not_108_out, not_109_out, not_110_out, not_111_out,
       not_112_out, not_113_out, not_114_out, not_115_out, not_116_out, not_117_out, not_118_out,
       not_119_out, not_120_out, not_121_out, not_122_out, not_123_out, not_124_out, not_125_out,
       not_126_out, not_127_out, not_128_out, not_129_out, not_130_out, not_131_out, not_132_out,
       not_133_out, not_134_out, not_135_out, not_136_out, not_137_out, not_138_out, not_139_out,
       not_140_out, not_141_out, not_142_out, not_143_out, not_144_out, not_145_out, not_146_out,
       not_147_out, not_148_out, not_149_out, not_150_out, not_151_out, not_152_out, not_153_out,
       not_154_out, not_155_out, not_156_out, not_157_out, not_158_out, not_159_out, not_160_out,
       not_161_out, not_162_out, not_163_out, not_164_out, not_165_out, not_166_out, not_167_out,
       not_168_out, not_169_out, not_170_out, not_171_out, not_172_out, not_173_out, not_174_out,
       not_175_out, not_176_out, not_177_out, not_178_out, not_179_out, not_180_out, not_181_out,
       not_182_out, not_183_out, not_184_out, not_185_out, not_186_out, not_187_out, not_188_out,
       not_189_out, not_190_out, not_191_out, not_192_out, not_193_out, not_194_out, not_195_out,
       not_196_out, not_197_out, not_198_out, not_199_out, not_200_out, not_201_out, not_202_out,
       not_203_out, not_204_out, not_205_out, not_206_out, not_207_out, not_208_out, not_209_out,
       not_210_out, not_211_out, not_212_out, not_213_out, not_214_out, not_215_out, not_216_out,
       not_217_out, not_218_out, not_219_out, not_220_out, not_221_out, not_222_out, not_223_out,
       not_224_out, not_225_out, not_226_out, not_227_out, not_228_out, not_229_out, not_230_out,
       not_231_out, not_232_out, not_233_out, not_234_out, not_235_out, not_236_out, not_237_out,
       not_238_out, not_239_out, not_240_out, not_241_out, not_242_out, not_243_out, not_244_out,
       not_245_out, not_246_out, not_247_out, not_248_out, not_249_out, not_250_out, not_251_out,
       not_252_out, not_253_out, not_254_out, not_255_out, not_256_out, not_257_out, not_258_out,
       not_259_out, not_260_out, not_261_out;

  not not_1 (not_1_out, OP0);
  not not_2 (not_2_out, OP1);
  not not_3 (not_3_out, OP2);
  not not_4 (not_4_out, OP3);
  not not_5 (not_5_out, OP4);
  not not_6 (not_6_out, OP5);
  not not_7 (not_7_out, F2);
  not not_8 (not_8_out, F3);
  not not_9 (not_9_out, F4);
  not not_10 (not_10_out, F5);
  not not_11 (not_11_out, OP0);
  not not_12 (not_12_out, OP1);
  not not_13 (not_13_out, OP2);
  not not_14 (not_14_out, OP3);
  not not_15 (not_15_out, OP4);
  not not_16 (not_16_out, OP5);
  not not_17 (not_17_out, F0);
  not not_18 (not_18_out, F1);
  not not_19 (not_19_out, F2);
  not not_20 (not_20_out, F3);
  not not_21 (not_21_out, F4);
  not not_22 (not_22_out, OP0);
  not not_23 (not_23_out, OP1);
  not not_24 (not_24_out, OP2);
  not not_25 (not_25_out, OP3);
  not not_26 (not_26_out, OP4);
  not not_27 (not_27_out, OP5);
  not not_28 (not_28_out, F1);
  not not_29 (not_29_out, F2);
  not not_30 (not_30_out, F3);
  not not_31 (not_31_out, F4);
  not not_32 (not_32_out, OP0);
  not not_33 (not_33_out, OP1);
  not not_34 (not_34_out, OP2);
  not not_35 (not_35_out, OP3);
  not not_36 (not_36_out, OP4);
  not not_37 (not_37_out, OP5);
  not not_38 (not_38_out, F0);
  not not_39 (not_39_out, F1);
  not not_40 (not_40_out, F3);
  not not_41 (not_41_out, F4);
  not not_42 (not_42_out, OP0);
  not not_43 (not_43_out, OP1);
  not not_44 (not_44_out, OP2);
  not not_45 (not_45_out, OP3);
  not not_46 (not_46_out, OP4);
  not not_47 (not_47_out, OP5);
  not not_48 (not_48_out, F0);
  not not_49 (not_49_out, F2);
  not not_50 (not_50_out, F4);
  not not_51 (not_51_out, OP0);
  not not_52 (not_52_out, OP1);
  not not_53 (not_53_out, OP2);
  not not_54 (not_54_out, OP4);
  not not_55 (not_55_out, OP5);
  not not_56 (not_56_out, OP0);
  not not_57 (not_57_out, OP1);
  not not_58 (not_58_out, OP4);
  not not_59 (not_59_out, OP5);
  not not_60 (not_60_out, OP1);
  not not_61 (not_61_out, OP2);
  not not_62 (not_62_out, OP4);
  not not_63 (not_63_out, OP5);
  not not_64 (not_64_out, OP0);
  not not_65 (not_65_out, OP2);
  not not_66 (not_66_out, OP4);
  not not_67 (not_67_out, OP5);
  not not_68 (not_68_out, OP2);
  not not_69 (not_69_out, OP3);
  not not_70 (not_70_out, OP4);
  not not_71 (not_71_out, OP2);
  not not_72 (not_72_out, OP4);
  not not_73 (not_73_out, OP4);
  not not_74 (not_74_out, OP5);
  not not_75 (not_75_out, OP0);
  not not_76 (not_76_out, OP1);
  not not_77 (not_77_out, OP2);
  not not_78 (not_78_out, OP3);
  not not_79 (not_79_out, OP4);
  not not_80 (not_80_out, OP3);
  not not_81 (not_81_out, OP4);
  not not_82 (not_82_out, OP5);
  not not_83 (not_83_out, OP0);
  not not_84 (not_84_out, OP1);
  not not_85 (not_85_out, OP2);
  not not_86 (not_86_out, OP3);
  not not_87 (not_87_out, OP4);
  not not_88 (not_88_out, OP5);
  not not_89 (not_89_out, F0);
  not not_90 (not_90_out, F2);
  not not_91 (not_91_out, F3);
  not not_92 (not_92_out, F4);
  not not_93 (not_93_out, F5);
  not not_94 (not_94_out, OP0);
  not not_95 (not_95_out, OP1);
  not not_96 (not_96_out, OP2);
  not not_97 (not_97_out, OP3);
  not not_98 (not_98_out, OP4);
  not not_99 (not_99_out, OP5);
  not not_100 (not_100_out, F0);
  not not_101 (not_101_out, F2);
  not not_102 (not_102_out, F3);
  not not_103 (not_103_out, F4);
  not not_104 (not_104_out, OP0);
  not not_105 (not_105_out, OP1);
  not not_106 (not_106_out, OP2);
  not not_107 (not_107_out, OP3);
  not not_108 (not_108_out, OP4);
  not not_109 (not_109_out, OP5);
  not not_110 (not_110_out, F0);
  not not_111 (not_111_out, F1);
  not not_112 (not_112_out, F3);
  not not_113 (not_113_out, F4);
  not not_114 (not_114_out, OP0);
  not not_115 (not_115_out, OP1);
  not not_116 (not_116_out, OP2);
  not not_117 (not_117_out, OP3);
  not not_118 (not_118_out, OP4);
  not not_119 (not_119_out, OP5);
  not not_120 (not_120_out, F3);
  not not_121 (not_121_out, F4);
  not not_122 (not_122_out, OP0);
  not not_123 (not_123_out, OP1);
  not not_124 (not_124_out, OP2);
  not not_125 (not_125_out, OP3);
  not not_126 (not_126_out, OP4);
  not not_127 (not_127_out, OP5);
  not not_128 (not_128_out, F0);
  not not_129 (not_129_out, F2);
  not not_130 (not_130_out, F4);
  not not_131 (not_131_out, OP0);
  not not_132 (not_132_out, OP1);
  not not_133 (not_133_out, OP4);
  not not_134 (not_134_out, OP5);
  not not_135 (not_135_out, OP0);
  not not_136 (not_136_out, OP2);
  not not_137 (not_137_out, OP4);
  not not_138 (not_138_out, OP5);
  not not_139 (not_139_out, OP3);
  not not_140 (not_140_out, OP4);
  not not_141 (not_141_out, OP5);
  not not_142 (not_142_out, OP0);
  not not_143 (not_143_out, OP1);
  not not_144 (not_144_out, OP2);
  not not_145 (not_145_out, OP3);
  not not_146 (not_146_out, OP4);
  not not_147 (not_147_out, OP5);
  not not_148 (not_148_out, F0);
  not not_149 (not_149_out, F1);
  not not_150 (not_150_out, F2);
  not not_151 (not_151_out, F3);
  not not_152 (not_152_out, F4);
  not not_153 (not_153_out, OP0);
  not not_154 (not_154_out, OP1);
  not not_155 (not_155_out, OP2);
  not not_156 (not_156_out, OP3);
  not not_157 (not_157_out, OP4);
  not not_158 (not_158_out, OP5);
  not not_159 (not_159_out, F1);
  not not_160 (not_160_out, F2);
  not not_161 (not_161_out, F3);
  not not_162 (not_162_out, F4);
  not not_163 (not_163_out, OP0);
  not not_164 (not_164_out, OP1);
  not not_165 (not_165_out, OP2);
  not not_166 (not_166_out, OP3);
  not not_167 (not_167_out, OP4);
  not not_168 (not_168_out, OP5);
  not not_169 (not_169_out, F0);
  not not_170 (not_170_out, F2);
  not not_171 (not_171_out, F3);
  not not_172 (not_172_out, F4);
  not not_173 (not_173_out, OP0);
  not not_174 (not_174_out, OP1);
  not not_175 (not_175_out, OP2);
  not not_176 (not_176_out, OP3);
  not not_177 (not_177_out, OP4);
  not not_178 (not_178_out, OP5);
  not not_179 (not_179_out, F0);
  not not_180 (not_180_out, F1);
  not not_181 (not_181_out, F3);
  not not_182 (not_182_out, F4);
  not not_183 (not_183_out, OP0);
  not not_184 (not_184_out, OP1);
  not not_185 (not_185_out, OP2);
  not not_186 (not_186_out, OP3);
  not not_187 (not_187_out, OP4);
  not not_188 (not_188_out, OP5);
  not not_189 (not_189_out, F2);
  not not_190 (not_190_out, F4);
  not not_191 (not_191_out, OP0);
  not not_192 (not_192_out, OP1);
  not not_193 (not_193_out, OP2);
  not not_194 (not_194_out, OP4);
  not not_195 (not_195_out, OP5);
  not not_196 (not_196_out, OP0);
  not not_197 (not_197_out, OP1);
  not not_198 (not_198_out, OP4);
  not not_199 (not_199_out, OP5);
  not not_200 (not_200_out, OP1);
  not not_201 (not_201_out, OP2);
  not not_202 (not_202_out, OP4);
  not not_203 (not_203_out, OP5);
  not not_204 (not_204_out, OP2);
  not not_205 (not_205_out, OP3);
  not not_206 (not_206_out, OP4);
  not not_207 (not_207_out, OP2);
  not not_208 (not_208_out, OP4);
  not not_209 (not_209_out, OP4);
  not not_210 (not_210_out, OP5);
  not not_211 (not_211_out, OP0);
  not not_212 (not_212_out, OP1);
  not not_213 (not_213_out, OP2);
  not not_214 (not_214_out, OP3);
  not not_215 (not_215_out, OP4);
  not not_216 (not_216_out, OP0);
  not not_217 (not_217_out, OP1);
  not not_218 (not_218_out, OP2);
  not not_219 (not_219_out, OP3);
  not not_220 (not_220_out, OP4);
  not not_221 (not_221_out, OP5);
  not not_222 (not_222_out, F1);
  not not_223 (not_223_out, F3);
  not not_224 (not_224_out, F4);
  not not_225 (not_225_out, OP0);
  not not_226 (not_226_out, OP1);
  not not_227 (not_227_out, OP2);
  not not_228 (not_228_out, OP3);
  not not_229 (not_229_out, OP4);
  not not_230 (not_230_out, OP5);
  not not_231 (not_231_out, F3);
  not not_232 (not_232_out, F4);
  not not_233 (not_233_out, OP0);
  not not_234 (not_234_out, OP1);
  not not_235 (not_235_out, OP2);
  not not_236 (not_236_out, OP3);
  not not_237 (not_237_out, OP4);
  not not_238 (not_238_out, OP5);
  not not_239 (not_239_out, F0);
  not not_240 (not_240_out, F2);
  not not_241 (not_241_out, F4);
  not not_242 (not_242_out, OP0);
  not not_243 (not_243_out, OP1);
  not not_244 (not_244_out, OP2);
  not not_245 (not_245_out, OP3);
  not not_246 (not_246_out, OP4);
  not not_247 (not_247_out, OP5);
  not not_248 (not_248_out, F2);
  not not_249 (not_249_out, F4);
  not not_250 (not_250_out, OP0);
  not not_251 (not_251_out, OP2);
  not not_252 (not_252_out, OP4);
  not not_253 (not_253_out, OP5);
  not not_254 (not_254_out, OP1);
  not not_255 (not_255_out, OP4);
  not not_256 (not_256_out, OP5);
  not not_257 (not_257_out, OP4);
  not not_258 (not_258_out, OP5);
  not not_259 (not_259_out, OP3);
  not not_260 (not_260_out, OP4);
  not not_261 (not_261_out, OP5);
  and and_1 (and_1_out, not_1_out, not_2_out, not_3_out, not_4_out, not_5_out, not_6_out, F0, F1, not_7_out, not_8_out, not_9_out, not_10_out);
  and and_2 (and_2_out, not_11_out, not_12_out, not_13_out, not_14_out, not_15_out, not_16_out, not_17_out, not_18_out, not_19_out, not_20_out, not_21_out, F5);
  and and_3 (and_3_out, not_22_out, not_23_out, not_24_out, not_25_out, not_26_out, not_27_out, F0, not_28_out, not_29_out, not_30_out, not_31_out, F5);
  and and_4 (and_4_out, not_32_out, not_33_out, not_34_out, not_35_out, not_36_out, not_37_out, not_38_out, not_39_out, F2, not_40_out, not_41_out, F5);
  and and_5 (and_5_out, not_42_out, not_43_out, not_44_out, not_45_out, not_46_out, not_47_out, not_48_out, F1, not_49_out, F3, not_50_out, F5);
  and and_6 (and_6_out, not_51_out, not_52_out, not_53_out, OP3, not_54_out, not_55_out);
  and and_7 (and_7_out, not_56_out, not_57_out, OP2, OP3, not_58_out, not_59_out);
  and and_8 (and_8_out, OP0, not_60_out, not_61_out, OP3, not_62_out, not_63_out);
  and and_9 (and_9_out, not_64_out, OP1, not_65_out, OP3, not_66_out, not_67_out);
  and and_10 (and_10_out, OP0, OP1, not_68_out, not_69_out, not_70_out, OP5);
  and and_11 (and_11_out, OP0, OP1, not_71_out, OP3, not_72_out, OP5);
  and and_12 (and_12_out, OP0, OP1, OP2, OP3, not_73_out, not_74_out);
  and and_13 (and_13_out, not_75_out, not_76_out, not_77_out, not_78_out, not_79_out, OP5);
  and and_14 (and_14_out, OP0, OP1, OP2, not_80_out, not_81_out, not_82_out);
  and and_15 (and_15_out, not_83_out, not_84_out, not_85_out, not_86_out, not_87_out, not_88_out, not_89_out, F1, not_90_out, not_91_out, not_92_out, not_93_out);
  and and_16 (and_16_out, not_94_out, not_95_out, not_96_out, not_97_out, not_98_out, not_99_out, not_100_out, F1, not_101_out, not_102_out, not_103_out, F5);
  and and_17 (and_17_out, not_104_out, not_105_out, not_106_out, not_107_out, not_108_out, not_109_out, not_110_out, not_111_out, F2, not_112_out, not_113_out, F5);
  and and_18 (and_18_out, not_114_out, not_115_out, not_116_out, not_117_out, not_118_out, not_119_out, F0, F1, F2, not_120_out, not_121_out, F5);
  and and_19 (and_19_out, not_122_out, not_123_out, not_124_out, not_125_out, not_126_out, not_127_out, not_128_out, F1, not_129_out, F3, not_130_out, F5);
  and and_20 (and_20_out, not_131_out, not_132_out, OP2, OP3, not_133_out, not_134_out);
  and and_21 (and_21_out, not_135_out, OP1, not_136_out, OP3, not_137_out, not_138_out);
  and and_22 (and_22_out, OP0, OP1, OP2, not_139_out, not_140_out, not_141_out);
  and and_23 (and_23_out, not_142_out, not_143_out, not_144_out, not_145_out, not_146_out, not_147_out, not_148_out, not_149_out, not_150_out, not_151_out, not_152_out, F5);
  and and_24 (and_24_out, not_153_out, not_154_out, not_155_out, not_156_out, not_157_out, not_158_out, F0, not_159_out, not_160_out, not_161_out, not_162_out, F5);
  and and_25 (and_25_out, not_163_out, not_164_out, not_165_out, not_166_out, not_167_out, not_168_out, not_169_out, F1, not_170_out, not_171_out, not_172_out, F5);
  and and_26 (and_26_out, not_173_out, not_174_out, not_175_out, not_176_out, not_177_out, not_178_out, not_179_out, not_180_out, F2, not_181_out, not_182_out, F5);
  and and_27 (and_27_out, not_183_out, not_184_out, not_185_out, not_186_out, not_187_out, not_188_out, F0, F1, not_189_out, F3, not_190_out, F5);
  and and_28 (and_28_out, not_191_out, not_192_out, not_193_out, OP3, not_194_out, not_195_out);
  and and_29 (and_29_out, not_196_out, not_197_out, OP2, OP3, not_198_out, not_199_out);
  and and_30 (and_30_out, OP0, not_200_out, not_201_out, OP3, not_202_out, not_203_out);
  and and_31 (and_31_out, OP0, OP1, not_204_out, not_205_out, not_206_out, OP5);
  and and_32 (and_32_out, OP0, OP1, not_207_out, OP3, not_208_out, OP5);
  and and_33 (and_33_out, OP0, OP1, OP2, OP3, not_209_out, not_210_out);
  and and_34 (and_34_out, not_211_out, not_212_out, not_213_out, not_214_out, not_215_out, OP5);
  and and_35 (and_35_out, not_216_out, not_217_out, not_218_out, not_219_out, not_220_out, not_221_out, F0, not_222_out, F2, not_223_out, not_224_out, F5);
  and and_36 (and_36_out, not_225_out, not_226_out, not_227_out, not_228_out, not_229_out, not_230_out, F0, F1, F2, not_231_out, not_232_out, F5);
  and and_37 (and_37_out, not_233_out, not_234_out, not_235_out, not_236_out, not_237_out, not_238_out, not_239_out, F1, not_240_out, F3, not_241_out, F5);
  and and_38 (and_38_out, not_242_out, not_243_out, not_244_out, not_245_out, not_246_out, not_247_out, F0, F1, not_248_out, F3, not_249_out, F5);
  and and_39 (and_39_out, not_250_out, OP1, not_251_out, OP3, not_252_out, not_253_out);
  and and_40 (and_40_out, OP0, not_254_out, OP2, OP3, not_255_out, not_256_out);
  and and_41 (and_41_out, OP0, OP1, OP2, OP3, not_257_out, not_258_out);
  and and_42 (and_42_out, OP0, OP1, OP2, not_259_out, not_260_out, not_261_out);
  or or_1 (S1, and_15_out, and_16_out, and_17_out, and_18_out, and_19_out, and_20_out, and_21_out, and_22_out);
  or or_2 (S3, and_35_out, and_36_out, and_37_out, and_38_out, and_39_out, and_40_out, and_41_out, and_42_out);
  or or_3 (S0, and_1_out, and_2_out, and_3_out, and_4_out, and_5_out, and_6_out, and_7_out, and_8_out, and_9_out, and_10_out, and_11_out, and_12_out, and_13_out, and_14_out);
  or or_4 (S2, and_23_out, and_24_out, and_25_out, and_26_out, and_27_out, and_28_out, and_29_out, and_30_out, and_31_out, and_32_out, and_33_out, and_34_out);
endmodule

// 控制信号生成
module \控制信号自动生成  (
  input  OP0,
  input  OP1,
  input  OP2,
  input  OP3,
  input  OP4,
  input  OP5,
  input  F0,
  input  F1,
  input  F2,
  input  F3,
  input  F4,
  input  F5,
  output MemToReg,
  output MemWrite,
  output ALU_SRC,
  output RegWrite,
  output SysCALL,
  output SignedExt,
  output RegDst,
  output BEQ,
  output BNE,
  output JR,
  output JUMP,
  output JAL
);

  wire and_1_out, and_2_out, and_4_out, and_5_out, and_6_out, and_7_out, and_8_out, and_9_out, and_10_out,
       and_11_out, and_12_out, and_13_out, and_14_out, and_15_out, and_16_out, and_17_out, and_18_out,
       and_19_out, and_20_out, and_21_out, and_22_out, and_23_out, and_25_out, and_26_out, and_27_out,
       and_28_out, and_29_out, and_30_out, and_31_out, and_32_out, and_33_out, and_37_out, and_38_out,
       not_1_out, not_2_out, not_3_out, not_4_out, not_5_out, not_6_out, not_7_out, not_8_out, not_9_out,
       not_10_out, not_11_out, not_12_out, not_13_out, not_14_out, not_15_out, not_16_out, not_17_out,
       not_18_out, not_19_out, not_20_out, not_21_out, not_22_out, not_23_out, not_24_out, not_25_out,
       not_26_out, not_27_out, not_28_out, not_29_out, not_30_out, not_31_out, not_32_out, not_33_out,
       not_34_out, not_35_out, not_36_out, not_37_out, not_38_out, not_39_out, not_40_out, not_41_out,
       not_42_out, not_43_out, not_44_out, not_45_out, not_46_out, not_47_out, not_48_out, not_49_out,
       not_50_out, not_51_out, not_52_out, not_53_out, not_54_out, not_55_out, not_56_out, not_57_out,
       not_58_out, not_59_out, not_60_out, not_61_out, not_62_out, not_63_out, not_64_out, not_65_out,
       not_66_out, not_67_out, not_68_out, not_69_out, not_70_out, not_71_out, not_72_out, not_73_out,
       not_74_out, not_75_out, not_76_out, not_77_out, not_78_out, not_79_out, not_80_out, not_81_out,
       not_82_out, not_83_out, not_84_out, not_85_out, not_86_out, not_87_out, not_88_out, not_89_out,
       not_90_out, not_91_out, not_92_out, not_93_out, not_94_out, not_95_out, not_96_out, not_97_out,
       not_98_out, not_99_out, not_100_out, not_101_out, not_102_out, not_103_out, not_104_out, not_105_out,
       not_106_out, not_107_out, not_108_out, not_109_out, not_110_out, not_111_out, not_112_out,
       not_113_out, not_114_out, not_115_out, not_116_out, not_117_out, not_118_out, not_119_out,
       not_120_out, not_121_out, not_122_out, not_123_out, not_124_out, not_125_out, not_126_out,
       not_127_out, not_128_out, not_129_out, not_130_out, not_131_out, not_132_out, not_133_out,
       not_134_out, not_135_out, not_136_out, not_137_out, not_138_out, not_139_out, not_140_out,
       not_141_out, not_142_out, not_143_out, not_144_out, not_145_out, not_146_out, not_147_out,
       not_148_out, not_149_out, not_150_out, not_151_out, not_152_out, not_153_out, not_154_out,
       not_155_out, not_156_out, not_157_out, not_158_out, not_159_out, not_160_out, not_161_out,
       not_162_out, not_163_out, not_164_out, not_165_out, not_166_out, not_167_out, not_168_out,
       not_169_out, not_170_out, not_171_out, not_172_out, not_173_out, not_174_out, not_175_out,
       not_176_out, not_177_out, not_178_out, not_179_out, not_180_out, not_181_out, not_182_out,
       not_183_out, not_184_out, not_185_out, not_186_out, not_187_out, not_188_out, not_189_out,
       not_190_out, not_191_out, not_192_out, not_193_out, not_194_out, not_195_out, not_196_out,
       not_197_out, not_198_out, not_199_out, not_200_out, not_201_out, not_202_out, not_203_out,
       not_204_out, not_205_out, not_206_out, not_207_out, not_208_out, not_209_out, not_210_out,
       not_211_out, not_212_out, not_213_out, not_214_out, not_215_out, not_216_out, not_217_out,
       not_218_out, not_219_out, not_220_out, not_221_out, not_222_out, not_223_out, not_224_out;

  not not_1 (not_1_out, OP0);
  not not_2 (not_2_out, OP1);
  not not_3 (not_3_out, OP2);
  not not_4 (not_4_out, OP3);
  not not_5 (not_5_out, OP4);
  not not_6 (not_6_out, OP2);
  not not_7 (not_7_out, OP3);
  not not_8 (not_8_out, OP4);
  not not_9 (not_9_out, OP2);
  not not_10 (not_10_out, OP4);
  not not_11 (not_11_out, OP0);
  not not_12 (not_12_out, OP1);
  not not_13 (not_13_out, OP2);
  not not_14 (not_14_out, OP4);
  not not_15 (not_15_out, OP5);
  not not_16 (not_16_out, OP0);
  not not_17 (not_17_out, OP1);
  not not_18 (not_18_out, OP4);
  not not_19 (not_19_out, OP5);
  not not_20 (not_20_out, OP1);
  not not_21 (not_21_out, OP2);
  not not_22 (not_22_out, OP4);
  not not_23 (not_23_out, OP5);
  not not_24 (not_24_out, OP0);
  not not_25 (not_25_out, OP2);
  not not_26 (not_26_out, OP4);
  not not_27 (not_27_out, OP5);
  not not_28 (not_28_out, OP1);
  not not_29 (not_29_out, OP4);
  not not_30 (not_30_out, OP5);
  not not_31 (not_31_out, OP2);
  not not_32 (not_32_out, OP3);
  not not_33 (not_33_out, OP4);
  not not_34 (not_34_out, OP2);
  not not_35 (not_35_out, OP4);
  not not_36 (not_36_out, OP4);
  not not_37 (not_37_out, OP5);
  not not_38 (not_38_out, OP0);
  not not_39 (not_39_out, OP1);
  not not_40 (not_40_out, OP2);
  not not_41 (not_41_out, OP3);
  not not_42 (not_42_out, OP4);
  not not_43 (not_43_out, OP0);
  not not_44 (not_44_out, OP1);
  not not_45 (not_45_out, OP2);
  not not_46 (not_46_out, OP3);
  not not_47 (not_47_out, OP4);
  not not_48 (not_48_out, F0);
  not not_49 (not_49_out, F1);
  not not_50 (not_50_out, F3);
  not not_51 (not_51_out, F4);
  not not_52 (not_52_out, OP0);
  not not_53 (not_53_out, OP1);
  not not_54 (not_54_out, OP2);
  not not_55 (not_55_out, OP3);
  not not_56 (not_56_out, OP4);
  not not_57 (not_57_out, F0);
  not not_58 (not_58_out, F2);
  not not_59 (not_59_out, F3);
  not not_60 (not_60_out, F4);
  not not_61 (not_61_out, OP0);
  not not_62 (not_62_out, OP1);
  not not_63 (not_63_out, OP2);
  not not_64 (not_64_out, OP3);
  not not_65 (not_65_out, OP4);
  not not_66 (not_66_out, F1);
  not not_67 (not_67_out, F3);
  not not_68 (not_68_out, F4);
  not not_69 (not_69_out, OP0);
  not not_70 (not_70_out, OP1);
  not not_71 (not_71_out, OP2);
  not not_72 (not_72_out, OP3);
  not not_73 (not_73_out, OP4);
  not not_74 (not_74_out, F2);
  not not_75 (not_75_out, F3);
  not not_76 (not_76_out, F4);
  not not_77 (not_77_out, F5);
  not not_78 (not_78_out, OP0);
  not not_79 (not_79_out, OP1);
  not not_80 (not_80_out, OP2);
  not not_81 (not_81_out, OP3);
  not not_82 (not_82_out, OP4);
  not not_83 (not_83_out, F2);
  not not_84 (not_84_out, F4);
  not not_85 (not_85_out, OP0);
  not not_86 (not_86_out, OP1);
  not not_87 (not_87_out, OP2);
  not not_88 (not_88_out, OP3);
  not not_89 (not_89_out, OP4);
  not not_90 (not_90_out, F3);
  not not_91 (not_91_out, F4);
  not not_92 (not_92_out, OP0);
  not not_93 (not_93_out, OP1);
  not not_94 (not_94_out, OP2);
  not not_95 (not_95_out, OP3);
  not not_96 (not_96_out, OP4);
  not not_97 (not_97_out, OP0);
  not not_98 (not_98_out, OP2);
  not not_99 (not_99_out, OP4);
  not not_100 (not_100_out, OP5);
  not not_101 (not_101_out, OP1);
  not not_102 (not_102_out, OP4);
  not not_103 (not_103_out, OP5);
  not not_104 (not_104_out, OP4);
  not not_105 (not_105_out, OP5);
  not not_106 (not_106_out, OP2);
  not not_107 (not_107_out, OP3);
  not not_108 (not_108_out, OP4);
  not not_109 (not_109_out, OP0);
  not not_110 (not_110_out, OP1);
  not not_111 (not_111_out, OP2);
  not not_112 (not_112_out, OP3);
  not not_113 (not_113_out, OP4);
  not not_114 (not_114_out, OP5);
  not not_115 (not_115_out, F0);
  not not_116 (not_116_out, F1);
  not not_117 (not_117_out, F4);
  not not_118 (not_118_out, F5);
  not not_119 (not_119_out, OP0);
  not not_120 (not_120_out, OP1);
  not not_121 (not_121_out, OP2);
  not not_122 (not_122_out, OP3);
  not not_123 (not_123_out, OP4);
  not not_124 (not_124_out, OP0);
  not not_125 (not_125_out, OP2);
  not not_126 (not_126_out, OP4);
  not not_127 (not_127_out, OP5);
  not not_128 (not_128_out, OP1);
  not not_129 (not_129_out, OP2);
  not not_130 (not_130_out, OP4);
  not not_131 (not_131_out, OP5);
  not not_132 (not_132_out, OP0);
  not not_133 (not_133_out, OP1);
  not not_134 (not_134_out, OP2);
  not not_135 (not_135_out, OP3);
  not not_136 (not_136_out, OP4);
  not not_137 (not_137_out, OP5);
  not not_138 (not_138_out, F0);
  not not_139 (not_139_out, F2);
  not not_140 (not_140_out, F3);
  not not_141 (not_141_out, F4);
  not not_142 (not_142_out, OP0);
  not not_143 (not_143_out, OP1);
  not not_144 (not_144_out, OP2);
  not not_145 (not_145_out, OP3);
  not not_146 (not_146_out, OP4);
  not not_147 (not_147_out, OP5);
  not not_148 (not_148_out, F1);
  not not_149 (not_149_out, F3);
  not not_150 (not_150_out, F4);
  not not_151 (not_151_out, OP0);
  not not_152 (not_152_out, OP1);
  not not_153 (not_153_out, OP2);
  not not_154 (not_154_out, OP3);
  not not_155 (not_155_out, OP4);
  not not_156 (not_156_out, OP5);
  not not_157 (not_157_out, F0);
  not not_158 (not_158_out, F1);
  not not_159 (not_159_out, F4);
  not not_160 (not_160_out, F5);
  not not_161 (not_161_out, OP0);
  not not_162 (not_162_out, OP1);
  not not_163 (not_163_out, OP2);
  not not_164 (not_164_out, OP3);
  not not_165 (not_165_out, OP4);
  not not_166 (not_166_out, OP5);
  not not_167 (not_167_out, F2);
  not not_168 (not_168_out, F3);
  not not_169 (not_169_out, F4);
  not not_170 (not_170_out, F5);
  not not_171 (not_171_out, OP0);
  not not_172 (not_172_out, OP1);
  not not_173 (not_173_out, OP2);
  not not_174 (not_174_out, OP3);
  not not_175 (not_175_out, OP4);
  not not_176 (not_176_out, OP5);
  not not_177 (not_177_out, F2);
  not not_178 (not_178_out, F4);
  not not_179 (not_179_out, OP0);
  not not_180 (not_180_out, OP1);
  not not_181 (not_181_out, OP2);
  not not_182 (not_182_out, OP3);
  not not_183 (not_183_out, OP4);
  not not_184 (not_184_out, OP5);
  not not_185 (not_185_out, F3);
  not not_186 (not_186_out, F4);
  not not_187 (not_187_out, OP0);
  not not_188 (not_188_out, OP1);
  not not_189 (not_189_out, OP3);
  not not_190 (not_190_out, OP4);
  not not_191 (not_191_out, OP5);
  not not_192 (not_192_out, OP1);
  not not_193 (not_193_out, OP3);
  not not_194 (not_194_out, OP4);
  not not_195 (not_195_out, OP5);
  not not_196 (not_196_out, OP0);
  not not_197 (not_197_out, OP1);
  not not_198 (not_198_out, OP2);
  not not_199 (not_199_out, OP3);
  not not_200 (not_200_out, OP4);
  not not_201 (not_201_out, OP5);
  not not_202 (not_202_out, F0);
  not not_203 (not_203_out, F1);
  not not_204 (not_204_out, F2);
  not not_205 (not_205_out, F4);
  not not_206 (not_206_out, F5);
  not not_207 (not_207_out, OP0);
  not not_208 (not_208_out, OP2);
  not not_209 (not_209_out, OP3);
  not not_210 (not_210_out, OP4);
  not not_211 (not_211_out, OP5);
  not not_212 (not_212_out, F0);
  not not_213 (not_213_out, F1);
  not not_214 (not_214_out, F2);
  not not_215 (not_215_out, F4);
  not not_216 (not_216_out, F5);
  not not_217 (not_217_out, OP2);
  not not_218 (not_218_out, OP3);
  not not_219 (not_219_out, OP4);
  not not_220 (not_220_out, OP5);
  not not_221 (not_221_out, OP2);
  not not_222 (not_222_out, OP3);
  not not_223 (not_223_out, OP4);
  not not_224 (not_224_out, OP5);
  and and_1 (and_1_out, not_1_out, not_2_out, not_3_out, not_4_out, not_5_out, OP5);
  and and_2 (and_2_out, OP0, OP1, not_6_out, not_7_out, not_8_out, OP5);
  and and_3 (MemWrite, OP0, OP1, not_9_out, OP3, not_10_out, OP5);
  and and_4 (and_4_out, not_11_out, not_12_out, not_13_out, OP3, not_14_out, not_15_out);
  and and_5 (and_5_out, not_16_out, not_17_out, OP2, OP3, not_18_out, not_19_out);
  and and_6 (and_6_out, OP0, not_20_out, not_21_out, OP3, not_22_out, not_23_out);
  and and_7 (and_7_out, not_24_out, OP1, not_25_out, OP3, not_26_out, not_27_out);
  and and_8 (and_8_out, OP0, not_28_out, OP2, OP3, not_29_out, not_30_out);
  and and_9 (and_9_out, OP0, OP1, not_31_out, not_32_out, not_33_out, OP5);
  and and_10 (and_10_out, OP0, OP1, not_34_out, OP3, not_35_out, OP5);
  and and_11 (and_11_out, OP0, OP1, OP2, OP3, not_36_out, not_37_out);
  and and_12 (and_12_out, not_38_out, not_39_out, not_40_out, not_41_out, not_42_out, OP5);
  and and_13 (and_13_out, not_43_out, not_44_out, not_45_out, not_46_out, not_47_out, not_48_out, not_49_out, not_50_out, not_51_out);
  and and_14 (and_14_out, not_52_out, not_53_out, not_54_out, not_55_out, not_56_out, not_57_out, not_58_out, not_59_out, not_60_out);
  and and_15 (and_15_out, not_61_out, not_62_out, not_63_out, not_64_out, not_65_out, not_66_out, not_67_out, not_68_out, F5);
  and and_16 (and_16_out, not_69_out, not_70_out, not_71_out, not_72_out, not_73_out, F1, not_74_out, not_75_out, not_76_out, not_77_out);
  and and_17 (and_17_out, not_78_out, not_79_out, not_80_out, not_81_out, not_82_out, F1, not_83_out, F3, not_84_out, F5);
  and and_18 (and_18_out, not_85_out, not_86_out, not_87_out, not_88_out, not_89_out, F0, F2, not_90_out, not_91_out, F5);
  and and_19 (and_19_out, not_92_out, not_93_out, not_94_out, not_95_out, not_96_out, OP5);
  and and_20 (and_20_out, not_97_out, not_98_out, OP3, not_99_out, not_100_out);
  and and_21 (and_21_out, not_101_out, OP3, not_102_out, not_103_out);
  and and_22 (and_22_out, OP0, OP2, OP3, not_104_out, not_105_out);
  and and_23 (and_23_out, OP0, OP1, not_106_out, not_107_out, not_108_out);
  and and_24 (SysCALL, not_109_out, not_110_out, not_111_out, not_112_out, not_113_out, not_114_out, not_115_out, not_116_out, F2, F3, not_117_out, not_118_out);
  and and_25 (and_25_out, not_119_out, not_120_out, not_121_out, not_122_out, not_123_out, OP5);
  and and_26 (and_26_out, not_124_out, not_125_out, OP3, not_126_out, not_127_out);
  and and_27 (and_27_out, not_128_out, not_129_out, OP3, not_130_out, not_131_out);
  and and_28 (and_28_out, not_132_out, not_133_out, not_134_out, not_135_out, not_136_out, not_137_out, not_138_out, not_139_out, not_140_out, not_141_out);
  and and_29 (and_29_out, not_142_out, not_143_out, not_144_out, not_145_out, not_146_out, not_147_out, not_148_out, not_149_out, not_150_out, F5);
  and and_30 (and_30_out, not_151_out, not_152_out, not_153_out, not_154_out, not_155_out, not_156_out, not_157_out, not_158_out, F2, not_159_out, not_160_out);
  and and_31 (and_31_out, not_161_out, not_162_out, not_163_out, not_164_out, not_165_out, not_166_out, F1, not_167_out, not_168_out, not_169_out, not_170_out);
  and and_32 (and_32_out, not_171_out, not_172_out, not_173_out, not_174_out, not_175_out, not_176_out, F1, not_177_out, F3, not_178_out, F5);
  and and_33 (and_33_out, not_179_out, not_180_out, not_181_out, not_182_out, not_183_out, not_184_out, F0, F2, not_185_out, not_186_out, F5);
  and and_34 (BEQ, not_187_out, not_188_out, OP2, not_189_out, not_190_out, not_191_out);
  and and_35 (BNE, OP0, not_192_out, OP2, not_193_out, not_194_out, not_195_out);
  and and_36 (JR, not_196_out, not_197_out, not_198_out, not_199_out, not_200_out, not_201_out, not_202_out, not_203_out, not_204_out, F3, not_205_out, not_206_out);
  and and_37 (and_37_out, not_207_out, not_208_out, not_209_out, not_210_out, not_211_out, not_212_out, not_213_out, not_214_out, F3, not_215_out, not_216_out);
  and and_38 (and_38_out, OP1, not_217_out, not_218_out, not_219_out, not_220_out);
  and and_39 (JAL, OP0, OP1, not_221_out, not_222_out, not_223_out, not_224_out);
  or or_1 (MemToReg, and_1_out, and_2_out);
  or or_2 (ALU_SRC, and_4_out, and_5_out, and_6_out, and_7_out, and_8_out, and_9_out, and_10_out, and_11_out, and_12_out);
  or or_3 (RegWrite, and_13_out, and_14_out, and_15_out, and_16_out, and_17_out, and_18_out, and_19_out, and_20_out, and_21_out, and_22_out, and_23_out);
  or or_4 (SignedExt, and_25_out, and_26_out, and_27_out);
  or or_5 (RegDst, and_28_out, and_29_out, and_30_out, and_31_out, and_32_out, and_33_out);
  or or_6 (JUMP, and_37_out, and_38_out);
endmodule

// ALU
module MIPS_ALU (
  input  [4:0] shamt,
  input  [31:0] X,
  input  [31:0] Y,
  input  [3:0] AluOP,
  output Equal,
  output [31:0] Result,
  output [31:0] Result_2
);

  wire [0:0] comparator_1_lt, comparator_2_lt;
  wire [31:0] adder_1_out, AND_out, divider_1_out, divider_1_rem, multiplier_1_cout, multiplier_1_out,
       NOR_out, OR_out, shifter_1_out, shifter_2_out, shifter_3_out, shifter_4_out, subtractor_1_out, XOR_out;

  assign AND_out = X & Y;  // AND_Gate AND, 32 bits wide
  assign OR_out = X | Y;  // OR_Gate OR, 32 bits wide
  Shifter #(.width(32), .shift("ll")) shifter_1 (.in(Y), .\dist (shamt), .out(shifter_1_out));
  Shifter #(.width(32), .shift("ar")) shifter_2 (.in(Y), .\dist (shamt), .out(shifter_2_out));
  Shifter #(.width(32), .shift("lr")) shifter_3 (.in(Y), .\dist (shamt), .out(shifter_3_out));
  Multiplier #(.width(32)) multiplier_1 (.a(X), .b(Y), .out(multiplier_1_out), .cout(multiplier_1_cout));  // open: cin
  Divider #(.width(32)) divider_1 (.a(X), .b(Y), .out(divider_1_out), .rem(divider_1_rem));  // open: upper
  Adder #(.width(32)) adder_1 (.a(X), .b(Y), .out(adder_1_out));  // open: cin, cout
  Subtractor #(.width(32)) subtractor_1 (.a(X), .b(Y), .out(subtractor_1_out));  // open: bin, bout
  assign XOR_out = X ^ Y;  // XOR_Gate XOR, 32 bits wide
  assign NOR_out = ~(X | Y);  // NOR_Gate NOR, 32 bits wide
  Comparator #(.width(32), .mode("twosComplement")) comparator_1 (
    .a(X), .b(Y), .eq(Equal), .lt(comparator_1_lt[0]));  // open: gt
  Comparator #(.width(32), .mode("unsigned")) comparator_2 (.a(X), .b(Y), .lt(comparator_2_lt[0]));  // open: gt, eq
  Shifter #(.width(32), .shift("ll")) shifter_4 (.in(Y), .\dist (5'b10000), .out(shifter_4_out));
  Multiplexer #(.select(4), .width(32), .disabled("Z"), .enable("false")) multiplexer_1 (
    .in0(shifter_1_out), .in1(shifter_2_out), .in2(shifter_3_out), .in3(multiplier_1_out),
    .in4(divider_1_out), .in5(adder_1_out), .in6(subtractor_1_out), .in7(AND_out), .in8(OR_out),
    .in9(XOR_out), .in10(NOR_out), .in11({{31{1'b0}}, comparator_1_lt[0]}),
    .in12({{31{1'b0}}, comparator_2_lt[0]}), .in13(shifter_4_out), .in14({32{1'b0}}), .in15({32{1'b0}}),
    .out(Result), .sel(AluOP));
  Multiplexer #(.select(4), .width(32), .disabled("Z"), .enable("false")) multiplexer_2 (
    .in0({32{1'b0}}), .in1({32{1'b0}}), .in2({32{1'b0}}), .in3(multiplier_1_cout), .in4(divider_1_rem),
    .in5({32{1'b0}}), .in6({32{1'b0}}), .in7({32{1'b0}}), .in8({32{1'b0}}), .in9({32{1'b0}}),
    .in10({32{1'b0}}), .in11({32{1'b0}}), .in12({32{1'b0}}), .in13({32{1'b0}}), .in14({32{1'b0}}),
    .in15({32{1'b0}}), .out(Result_2), .sel(AluOP));

  // Other names for the same wires on the sheet: Result2[31:0] = Result_2; S[3:0] = AluOP

  // Notes on the sheet:
  //   不要改变此引脚区域内容，也不要改变ALU封装形式
  //   输入引脚
  //   输出引脚
endmodule

module MIPS_Regifile (
  input  [31:0] Din,
  input  Clk,
  input  WE,
  input  [4:0] R1_num,
  input  [4:0] W_num,
  input  [4:0] R2_num,
  output [31:0] R1,
  output [31:0] R2
);

  // RegisterFile registerfile_1: pin names not known; wires that end beside it: Din, Clk, WE, W_num, R1_num, R2_num, R1, R2
endmodule

module \理想流水线  (
  output RegWrite,
  output MemWrite,
  output [31:0] IF_PC,
  output [31:0] ID_PC,
  output [31:0] EX_PC,
  output [31:0] M_PC,
  output [31:0] WB_PC,
  output [31:0] RDin,
  output [31:0] MDin,
  output [31:0] LedData
);

  wire _BGTZ, _Equal, _JMP, _JR, _LB, _Syscall, AluSrc, AluSrcB, and_1_out, and_2_out, and_3_out, and_4_out,
       Beq, BGTZ, Bne, CLK, clock_1_out, clock_2_out, comparator_1_gt, comparator_2_eq, comparator_2_lt,
       d_ff_1_q, ex_mem_1_equal_out, ex_mem_1_jal_out, ex_mem_1_lb_out, ex_mem_1_memtoreg_out,
       ex_mem_1_pause_out, ex_mem_1_regdst_out, ex_mem_1_regwrite_out, ex_mem_1_syscall_out, Flag, Go,
       id_ex_1_beq_out, id_ex_1_bne_out, id_ex_1_jal_out, id_ex_1_memtoreg_out, id_ex_1_memwrite_out,
       id_ex_1_regdst_out, id_ex_1_regwrite_out, IR1, IR2, IR3, J, JAL, JMP, JR, LB, mem_wb_1_equal_out,
       mem_wb_1_jal_out, mem_wb_1_memtoreg_out, mem_wb_1_regdst_out, mem_wb_1_syscall_out, MemToReg,
       MemWrite_, multiplexer_4_out, nand_2_out, not_1_out, not_2_out, not_3_out, Pause, RegDst, RegWrite_,
       RST, SignedExt, Syscall, W1, W2, W3, Write;
  wire [3:0] _AluOP, AluOP;
  wire [4:0] multiplexer_5_out, multiplexer_7_out, multiplexer_10_out, W_num;
  wire [12:0] CNT_num;
  wire [15:0] \LoadUse次数 , \总周期数 , \插入气泡数 , \无条件分支数 , \条件分支成功数 ;
  wire [27:0] shifter_2_out;
  wire [31:0] _IR, _PC_4, _R1, _R2, adder_1_out, adder_2_out, bit_extender_1_out, bit_extender_2_out, EX_IR,
       ex_mem_1_aluresult_out, ex_mem_1_ir_out, ex_mem_1_pc_out, ID_IR, if_id_1_ir_out, if_id_1_pc_out,
       IF_IR, IMM, IR, MEM_IR, mem_wb_1_aluresult_out, mem_wb_1_ir_out, mem_wb_1_memorydata_out,
       mem_wb_1_pc_out, mips_alu_1_result, mips_regifile_1_r1, mips_regifile_1_r2, multiplexer_1_out,
       multiplexer_2_out, multiplexer_3_out, multiplexer_6_out, multiplexer_8_out, multiplexer_9_out,
       multiplexer_12_out, ram_1_data, shifter_1_out, WB_IR;

  Button \u_总复位  (.out(RST));
  Button _1 (.out(IR1));
  Button _2 (.out(IR2));
  Button _3 (.out(IR3));
  // Probe on \总周期数 
  // Probe on \总周期数 
  Button \u_继续运行  (.out(Go));
  LED #(.active("true")) led_1 (.in(W1));
  LED #(.active("true")) led_2 (.in(W2));
  LED #(.active("true")) led_3 (.in(W3));
  Multiplexer #(.select(1), .width(32), .disabled("Z"), .enable("false")) multiplexer_1 (
    .in0(adder_2_out), .in1(adder_1_out), .out(multiplexer_1_out), .sel(Flag));
  Shifter #(.width(32), .shift("ll")) shifter_1 (.in(IMM), .\dist (5'b00010), .out(shifter_1_out));
  Hex_Digit_Display hex_digit_display_1 (.value(LedData[31:28]));  // open: dp
  // Probe on IF_PC[19:0]
  // Mips_Probe mips_probe_1: pin names not known; wires that end beside it: IF_IR
  not not_1 (not_1_out, Go);
  nand nand_1 (Write, not_1_out, Pause);
  Multiplexer #(.select(1), .width(32), .disabled("Z"), .enable("false")) multiplexer_2 (
    .in0(multiplexer_3_out), .in1(adder_1_out), .out(multiplexer_2_out), .sel(and_1_out));
  Register #(.width(32), .trigger("rising"), .Select("low")) PC (
    .D(multiplexer_2_out), .en(multiplexer_4_out), .Q(IF_PC), .clk(CLK), .clr(RST));
  Multiplexer #(.select(2), .width(32), .disabled("Z"), .enable("false")) multiplexer_3 (
    .in0(multiplexer_1_out), .in1(_R1), .in2({_PC_4[31:28], shifter_2_out}), .in3(_R1),
    .out(multiplexer_3_out), .sel({_JMP, _JR}));
  Multiplexer #(.select(1), .width(1), .disabled("Z"), .enable("false")) multiplexer_4 (
    .in0(1'b1), .in1(Go), .out(multiplexer_4_out), .sel(Pause));
  Adder #(.width(32)) adder_1 (.a(shifter_1_out), .b(_PC_4), .out(adder_1_out));  // open: cin, cout
  Hex_Digit_Display hex_digit_display_2 (.value(LedData[27:24]));  // open: dp
  Hex_Digit_Display hex_digit_display_3 (.value(LedData[23:20]));  // open: dp
  // Probe on ID_PC[19:0]
  // Mips_Probe mips_probe_2: pin names not known; wires that end beside it: ID_IR
  Comparator #(.width(32), .mode("twosComplement")) comparator_1 (
    .a(_R1), .b({32{1'b0}}), .gt(comparator_1_gt));  // open: eq, lt
  and and_1 (and_1_out, comparator_1_gt, BGTZ);
  Adder #(.width(32)) adder_2 (.a(IF_PC), .b(32'h4), .out(adder_2_out));  // open: cin, cout
  Counter #(.width(16), .max('hffff), .ongoal("wrap"), .trigger("rising"), .behavior("old")) counter_1 (
    .load(1'b0), .count(multiplexer_4_out), .Q(\总周期数 ), .clk(CLK), .clr(RST));  // open: D, carry, preset
  Hex_Digit_Display hex_digit_display_4 (.value(LedData[15:12]));  // open: dp
  Hex_Digit_Display hex_digit_display_5 (.value(LedData[19:16]));  // open: dp
  Hex_Digit_Display hex_digit_display_6 (.value(LedData[7:4]));  // open: dp
  Hex_Digit_Display hex_digit_display_7 (.value(LedData[11:8]));  // open: dp
  Clock #(.highDuration(1), .lowDuration(1)) clock_1 (.out(clock_1_out));
  // Probe on EX_PC[19:0]
  // Mips_Probe mips_probe_3: pin names not known; wires that end beside it: clock_1_out, EX_IR, CLK
  ROM #(.addrWidth(10), .dataWidth(32), .Select("high")) rom_1 (.addr(IF_PC[11:2]), .data(IR));
  Hex_Digit_Display hex_digit_display_8 (.value(LedData[3:0]));  // open: dp
  // Mips_Probe mips_probe_4: pin names not known; wires that end beside it: IR
  IF_ID if_id_1 (
    .IR_in(IR), .PC_in(adder_2_out), .\气泡_高电平时有效 (J), .clk(CLK), .clear(RST), .enable(Write),
    .IR_out(if_id_1_ir_out), .PC_out(if_id_1_pc_out), .OldPC_in(IF_PC), .OldPC_out(ID_PC));
  Shifter #(.width(28), .shift("ll")) shifter_2 (.in(_IR[27:0]), .\dist (5'b00010), .out(shifter_2_out));
  // Probe on \总周期数 
  // Probe on M_PC[19:0]
  // Mips_Probe mips_probe_5: pin names not known; wires that end beside it: MEM_IR
  // Probe on \总周期数 
  // Probe on \无条件分支数 
  // Probe on \条件分支成功数 
  // Probe on \插入气泡数 
  // Probe on \LoadUse次数 
  Multiplexer #(.select(1), .width(5), .disabled("Z"), .enable("false")) multiplexer_5 (
    .in0(if_id_1_ir_out[25:21]), .in1(5'b00010), .out(multiplexer_5_out), .sel(Syscall));
  assign bit_extender_1_out = {{16{1'b0}}, if_id_1_ir_out[15:0]};  // Bit_Extender bit_extender_1
  assign bit_extender_2_out = {{16{if_id_1_ir_out[15]}}, if_id_1_ir_out[15:0]};  // Bit_Extender bit_extender_2
  // Probe on IF_PC[11:0]
  // Probe on WB_PC[19:0]
  // Mips_Probe mips_probe_6: pin names not known; wires that end beside it: WB_IR
  \单周期硬布线控制器  \u_单周期硬布线控制器_1  (
    .Func(if_id_1_ir_out[5:0]), .OP(if_id_1_ir_out[31:26]), .ALU_OP(AluOP), .MemToReg(MemToReg),
    .MemWrite(MemWrite_), .ALU_SRC(AluSrcB), .RegWrite(RegWrite_), .SysCALL(Syscall), .SignedExt(SignedExt),
    .RegDst(RegDst), .JR(JR), .JMP(JMP), .Beq(Beq), .JAL(JAL), .Bne(Bne), .LB(LB), .BGTZ(BGTZ));
  Multiplexer #(.select(1), .width(32), .disabled("Z"), .enable("false")) multiplexer_6 (
    .in0(bit_extender_1_out), .in1(bit_extender_2_out), .out(multiplexer_6_out), .sel(SignedExt));
  // Probe on EX_PC[11:0]
  // Probe on ID_PC[11:0]
  // Probe on M_PC[11:0]
  D_Flip_Flop #(.trigger("high"), .Pre_Clr_Positions("LEGACY"), .NegatePresetClear("false"), .enable("true"), .NewFFLayout("false")) d_ff_1 (.Q(d_ff_1_q));  // open: clk, D, Qn, preset, en, reset
  // Probe on 13'h250
  Multiplexer #(.select(1), .width(5), .disabled("Z"), .enable("false")) multiplexer_7 (
    .in0(if_id_1_ir_out[20:16]), .in1(5'b00100), .out(multiplexer_7_out), .sel(Syscall));
  // Probe on WB_PC[11:0]
  Comparator #(.width(13), .mode("twosComplement")) comparator_2 (
    .a(CNT_num), .b(13'h250), .eq(comparator_2_eq), .lt(comparator_2_lt));  // open: gt
  Clock #(.highDuration(1), .lowDuration(1)) clock_2 (.out(clock_2_out));
  MIPS_Regifile mips_regifile_1 (
    .Din(RDin), .Clk(CLK), .R1(mips_regifile_1_r1), .R2(mips_regifile_1_r2), .WE(RegWrite), .W_num(W_num),
    .R1_num(multiplexer_5_out), .R2_num(multiplexer_7_out));
  nand nand_2 (nand_2_out, d_ff_1_q, comparator_2_eq);
  Counter #(.width(13), .max('h1fff), .ongoal("stay"), .trigger("rising"), .behavior("old")) counter_2 (
    .count(comparator_2_lt), .Q(CNT_num), .clk(clock_2_out));  // open: load, D, carry, clr, preset
  assign CLK = nand_2_out ? clock_2_out : 1'bz;  // Controlled_Buffer controlled_buffer_1
  Pull_Resistor #(.pull(1)) pull_resistor_1 (.node(CLK));
  ID_EX id_ex_1 (
    .Beq_in(Beq), .Bne_in(Bne), .MemToReg_in(MemToReg), .MemWrite_in(MemWrite_), .AluOP_in(AluOP),
    .AluSrc_in(AluSrcB), .RegWrite_in(RegWrite_), .JAL_in(JAL), .RegDst_in(RegDst), .Syscall_in(Syscall),
    .JMP_in(JMP), .JR_in(JR), .SignedExt_in(SignedExt), .LB_in(LB), .BGTZ_in(BGTZ), .IR_in(if_id_1_ir_out),
    .PC_in(if_id_1_pc_out), .R1_in(mips_regifile_1_r1), .R2_in(mips_regifile_1_r2),
    .Imm_in(multiplexer_6_out), .Beq_out(id_ex_1_beq_out), .Bne_out(id_ex_1_bne_out),
    .MemToReg_out(id_ex_1_memtoreg_out), .MemWrite_out(id_ex_1_memwrite_out), .AluOP_out(_AluOP),
    .AluSrc_out(AluSrc), .RegWrite_out(id_ex_1_regwrite_out), .JAL_out(id_ex_1_jal_out),
    .RegDst_out(id_ex_1_regdst_out), .Syscall_out(_Syscall), .JMP_out(_JMP), .JR_out(_JR), .LB_out(_LB),
    .BGTZ_out(_BGTZ), .IR_out(_IR), .PC_out(_PC_4), .R1_out(_R1), .R2_out(_R2), .Imm_out(IMM), .clk(CLK),
    .clear(RST), .enable(Write), .\气泡_高电平时有效 (J), .OldPC_in(ID_PC), .OldPC_out(EX_PC));  // open: SignedExt_out
  or or_1 (Flag, and_2_out, _BGTZ, and_3_out);
  and and_2 (and_2_out, id_ex_1_beq_out, _Equal);
  Multiplexer #(.select(1), .width(32), .disabled("Z"), .enable("false")) multiplexer_8 (
    .in0(_R2), .in1(IMM), .out(multiplexer_8_out), .sel(AluSrc));
  Counter #(.width(16), .max('hffff), .ongoal("wrap"), .trigger("rising"), .behavior("new")) counter_3 (
    .load(1'b0), .Q(\条件分支成功数 ), .clk(CLK), .clr(RST), .down(Flag));  // open: D, count, carry, preset
  and and_3 (and_3_out, id_ex_1_bne_out, not_2_out);
  not not_2 (not_2_out, _Equal);
  MIPS_ALU mips_alu_1 (
    .X(_R1), .Y(multiplexer_9_out), .AluOP(_AluOP), .Equal(_Equal), .Result(mips_alu_1_result),
    .shamt(_IR[10:6]));  // open: Result_2
  Multiplexer #(.select(1), .width(32), .disabled("Z"), .enable("false")) multiplexer_9 (
    .in0(multiplexer_8_out), .in1(32'h22), .out(multiplexer_9_out), .sel(_Syscall));
  or or_2 (J, Flag, _JR, _JMP);
  Counter #(.width(16), .max('hffff), .ongoal("wrap"), .trigger("rising"), .behavior("new")) counter_4 (
    .load(1'b0), .Q(\无条件分支数 ), .clk(CLK), .clr(RST), .down(_JMP));  // open: D, count, carry, preset
  EX_MEM ex_mem_1 (
    .\气泡_高电平时有效 (1'b0), .clk(CLK), .clear(RST), .enable(Write), .MemToReg_in(id_ex_1_memtoreg_out),
    .MemToReg_out(ex_mem_1_memtoreg_out), .MemWrite_in(id_ex_1_memwrite_out), .MemWrite_out(MemWrite),
    .RegWrite_in(id_ex_1_regwrite_out), .RegWrite_out(ex_mem_1_regwrite_out), .JAL_in(id_ex_1_jal_out),
    .JAL_out(ex_mem_1_jal_out), .LB_in(_LB), .LB_out(ex_mem_1_lb_out), .IR_in(_IR), .IR_out(ex_mem_1_ir_out),
    .PC_in(_PC_4), .PC_out(ex_mem_1_pc_out), .ALUResult_in(mips_alu_1_result),
    .ALUResult_out(ex_mem_1_aluresult_out), .R2_in(_R2), .R2_out(MDin), .RegDst_in(id_ex_1_regdst_out),
    .RegDst_out(ex_mem_1_regdst_out), .Syscall_in(_Syscall), .Syscall_out(ex_mem_1_syscall_out),
    .equal_in(_Equal), .equal_out(ex_mem_1_equal_out), .OldPC_in(EX_PC), .OldPC_out(M_PC),
    .pause_out(ex_mem_1_pause_out));  // open: pause_in
  RAM #(.addrWidth(10), .dataWidth(32), .bus("separate"), .Select("high")) ram_1 (
    .addr(ex_mem_1_aluresult_out[11:2]), .din(MDin), .data(ram_1_data), .str(MemWrite), .clk(CLK), .clr(RST));  // open: sel, ld
  MEM_WB mem_wb_1 (
    .\气泡_高电平时有效 (1'b0), .clk(CLK), .clear(RST), .enable(Write), .MemToReg_in(ex_mem_1_memtoreg_out),
    .MemToReg_out(mem_wb_1_memtoreg_out), .MemWrite_in(MemWrite), .RegWrite_in(ex_mem_1_regwrite_out),
    .RegWrite_out(RegWrite), .JAL_in(ex_mem_1_jal_out), .JAL_out(mem_wb_1_jal_out), .LB_in(ex_mem_1_lb_out),
    .IR_in(ex_mem_1_ir_out), .IR_out(mem_wb_1_ir_out), .PC_in(ex_mem_1_pc_out), .PC_out(mem_wb_1_pc_out),
    .ALUResult_in(ex_mem_1_aluresult_out), .ALUResult_out(mem_wb_1_aluresult_out),
    .Memorydata_in(ram_1_data), .Memorydata_out(mem_wb_1_memorydata_out), .RegDst_in(ex_mem_1_regdst_out),
    .RegDst_out(mem_wb_1_regdst_out), .Syscall_in(ex_mem_1_syscall_out), .Syscall_out(mem_wb_1_syscall_out),
    .equal_in(ex_mem_1_equal_out), .equal_out(mem_wb_1_equal_out), .OldPC_in(M_PC), .OldPC_out(WB_PC),
    .pause_in(ex_mem_1_pause_out));  // open: MemWrite_out, LB_out, pause_out
  and and_4 (and_4_out, _Syscall, mem_wb_1_equal_out);
  and and_5 (Pause, mem_wb_1_syscall_out, not_3_out);
  not not_3 (not_3_out, mem_wb_1_equal_out);
  Register #(.width(32), .trigger("rising"), .Select("low")) register_1 (
    .D(_R2), .Q(LedData), .clk(and_4_out), .clr(RST));  // open: en
  Multiplexer #(.select(1), .width(5), .disabled("Z"), .enable("false")) multiplexer_10 (
    .in0(mem_wb_1_ir_out[20:16]), .in1(mem_wb_1_ir_out[15:11]), .out(multiplexer_10_out),
    .sel(mem_wb_1_regdst_out));
  Multiplexer #(.select(1), .width(5), .disabled("Z"), .enable("false")) multiplexer_11 (
    .in0(multiplexer_10_out), .in1({5{1'b1}}), .out(W_num), .sel(mem_wb_1_jal_out));
  Multiplexer #(.select(1), .width(32), .disabled("Z"), .enable("false")) multiplexer_12 (
    .in0(mem_wb_1_aluresult_out), .in1(mem_wb_1_memorydata_out), .out(multiplexer_12_out),
    .sel(mem_wb_1_memtoreg_out));
  Multiplexer #(.select(1), .width(32), .disabled("Z"), .enable("false")) multiplexer_13 (
    .in0(multiplexer_12_out), .in1(mem_wb_1_pc_out), .out(RDin), .sel(mem_wb_1_jal_out));
  // also tied to GND on the sheet: RST

  // Other names for the same wires on the sheet: MEM_PC[31:0] = M_PC

  // Notes on the sheet:
  //   中断源
  //   时空图监测，可删除
  //   中断等待指示
  //   数码管输出
  //   指令存储器
  //   contents of rom_1 (hex, n*v repeats v):
  //   20100000 20110000 20120000 20130000 36100000 36310001 36520002 36730003 ae100000 ae110004 ae120008
  //   ae13000c 2002000a 20110000 20120000 20130000 c
  //   OP
  //   rs
  //   指令字
  //   rt
  //   Func
  //   Beq
  //   JMP
  //   JR
  //   Bne
  //   LB
  //   BGTZ
  //   OP
  //   JAL
  //   Func
  //   Syscall
  //   控制位
  //   MemToReg
  //   MemWrite
  //   AluOP
  //   AluSrcB
  //   RegWrite
  //   RegDst
  //   流水调试日志用
  //   暂停节拍，不能为0
  //   戳工具置1进入计数暂停模式，ctrl+k时钟自动运行到对应节拍暂停
  //   ctrl+k关闭时钟连续运行，将控制位置零，进入单步调试模式调试
  //   用这个时钟源需要去掉电路中的其他时钟源
  //   可计数暂停的时钟源
  //   为方便自动评测，需要输出流水线各段保存的PC值，注意是PC不是PC+4，另外ID段寄存器写入信息，Mem段内存写入信息也要输出
endmodule

module \气泡流水线  (
  output RegWrite,
  output MemWrite,
  output [31:0] IF_PC,
  output [31:0] ID_PC,
  output [31:0] EX_PC,
  output [31:0] M_PC,
  output [31:0] WB_PC,
  output [31:0] RDin,
  output [31:0] MDin,
  output [31:0] LedData
);

  wire _BGTZ, _Equal, _JMP, _JR, _LB, _RegW, _Syscall, AluSrc, AluSrcB, and_1_out, and_2_out, and_3_out,
       and_4_out, and_5_out, and_6_out, and_7_out, and_8_out, Beq, BGTZ, Bne, CLK, clock_1_out, clock_2_out,
       comparator_1_gt, comparator_2_eq, comparator_2_lt, comparator_3_eq, comparator_4_eq, d_ff_1_q, Data,
       ex_mem_1_equal_out, ex_mem_1_jal_out, ex_mem_1_lb_out, ex_mem_1_memtoreg_out, ex_mem_1_pause_out,
       ex_mem_1_regdst_out, ex_mem_1_syscall_out, Flag, Go, id_ex_1_beq_out, id_ex_1_bne_out,
       id_ex_1_jal_out, id_ex_1_memtoreg_out, id_ex_1_memwrite_out, id_ex_1_regdst_out, IR1, IR2, IR3, J,
       JAL, JMP, JR, LB, mem_wb_1_equal_out, mem_wb_1_jal_out, mem_wb_1_memtoreg_out, mem_wb_1_regdst_out,
       mem_wb_1_syscall_out, MemRegWrite, MemToReg, MemWrite_, multiplexer_4_out, nand_2_out, not_1_out,
       not_2_out, not_3_out, not_4_out, not_5_out, or_1_out, Pause, RegDst, RegWrite_, RST, SignedExt,
       Syscall, W1, W2, W3, WBLB, Write;
  wire [3:0] _AluOP, AluOP;
  wire [4:0] EXW_num, MEMW_num, multiplexer_8_out, multiplexer_10_out, multiplexer_13_out,
       multiplexer_15_out, R1, R2, W_num;
  wire [5:0] Func;
  wire [7:0] multiplexer_16_out, multiplexer_18_out, multiplexer_18_out_2, multiplexer_18_out_3,
       multiplexer_18_out_4;
  wire [12:0] CNT_num;
  wire [15:0] \LoadUse次数 , \总周期数 , \插入气泡数 , \无条件分支数 , \条件分支成功数 ;
  wire [27:0] shifter_2_out;
  wire [31:0] _IR, _PC_4, _R1, _R2, adder_1_out, adder_2_out, bit_extender_1_out, bit_extender_2_out,
       bit_extender_3_out, ex_mem_1_aluresult_out, ex_mem_1_pc_out, EX_PC_t, ID_PC_t, if_id_1_pc_out, IF_IR,
       IF_PC_t, IMM, MEM_IR, MEM_PC, mem_wb_1_aluresult_out, mem_wb_1_memorydata_out, mem_wb_1_pc_out,
       mips_alu_1_result, multiplexer_1_out, multiplexer_2_out, multiplexer_3_out, multiplexer_6_out,
       multiplexer_9_out, multiplexer_12_out, multiplexer_20_out, ram_1_data, regifile2_1_r1, regifile2_1_r2,
       shifter_1_out, WB_IR, WB_PC_t;
  wire [31:6] ID_IR;

  Button \u_总复位  (.out(RST));
  Button _1 (.out(IR1));
  Button _2 (.out(IR2));
  Button _3 (.out(IR3));
  // Probe on \总周期数 
  // Probe on \总周期数 
  Button \u_继续运行  (.out(Go));
  LED #(.active("true")) led_1 (.in(W1));
  LED #(.active("true")) led_2 (.in(W2));
  LED #(.active("true")) led_3 (.in(W3));
  \数据相关检测  \u_数据相关检测_1  (
    .OP(ID_IR[31:26]), .EX_WriteReg_num(EXW_num), .EX_RegWrite(_RegW), .MEM_WriteReg_num(MEMW_num),
    .MEM_RegWrite(MemRegWrite), .\数据相关 (Data), .Func(Func), .ID_R1_num(R1), .ID_R2_num(R2));
  Multiplexer #(.select(1), .width(32), .disabled("Z"), .enable("false")) multiplexer_1 (
    .in0(adder_2_out), .in1(adder_1_out), .out(multiplexer_1_out), .sel(Flag));
  Shifter #(.width(32), .shift("ll")) shifter_1 (.in(IMM), .\dist (5'b00010), .out(shifter_1_out));
  Hex_Digit_Display hex_digit_display_1 (.value(LedData[31:28]));  // open: dp
  // Probe on IF_PC_t[19:0]
  // Mips_Probe mips_probe_1: pin names not known; wires that end beside it: IF_IR
  nand nand_1 (Write, not_2_out, Pause);
  Multiplexer #(.select(1), .width(32), .disabled("Z"), .enable("false")) multiplexer_2 (
    .in0(multiplexer_3_out), .in1(adder_1_out), .out(multiplexer_2_out), .sel(and_3_out));
  Register #(.width(32), .trigger("rising"), .Select("low")) PC (
    .D(multiplexer_2_out), .en(and_1_out), .Q(IF_PC_t), .clk(CLK), .clr(RST));
  Multiplexer #(.select(2), .width(32), .disabled("Z"), .enable("false")) multiplexer_3 (
    .in0(multiplexer_1_out), .in1(_R1), .in2({_PC_4[31:28], shifter_2_out}), .in3(_R1),
    .out(multiplexer_3_out), .sel({_JMP, _JR}));
  and and_1 (and_1_out, not_1_out, multiplexer_4_out);
  not not_1 (not_1_out, Data);
  Multiplexer #(.select(1), .width(1), .disabled("Z"), .enable("false")) multiplexer_4 (
    .in0(1'b1), .in1(Go), .out(multiplexer_4_out), .sel(Pause));
  Adder #(.width(32)) adder_1 (.a(shifter_1_out), .b(_PC_4), .out(adder_1_out));  // open: cin, cout
  Hex_Digit_Display hex_digit_display_2 (.value(LedData[27:24]));  // open: dp
  Hex_Digit_Display hex_digit_display_3 (.value(LedData[23:20]));  // open: dp
  // Probe on ID_PC_t[19:0]
  // Mips_Probe mips_probe_2: pin names not known; wires that end beside it: {ID_IR, Func}
  and and_2 (and_2_out, Data, Write);
  not not_2 (not_2_out, Go);
  Comparator #(.width(32), .mode("twosComplement")) comparator_1 (
    .a(_R1), .b({32{1'b0}}), .gt(comparator_1_gt));  // open: eq, lt
  and and_3 (and_3_out, comparator_1_gt, BGTZ);
  Adder #(.width(32)) adder_2 (.a(IF_PC_t), .b(32'h4), .out(adder_2_out));  // open: cin, cout
  Counter #(.width(16), .max('hffff), .ongoal("wrap"), .trigger("rising"), .behavior("old")) counter_1 (
    .load(1'b0), .count(multiplexer_4_out), .Q(\总周期数 ), .clk(CLK), .clr(RST));  // open: D, carry, preset
  Hex_Digit_Display hex_digit_display_4 (.value(LedData[19:16]));  // open: dp
  Hex_Digit_Display hex_digit_display_5 (.value(LedData[15:12]));  // open: dp
  Counter #(.width(16), .max('hffff), .ongoal("wrap"), .trigger("rising"), .behavior("old")) counter_2 (
    .D({16{1'b0}}), .count(and_2_out), .Q(\插入气泡数 ), .clk(CLK), .clr(RST));  // open: load, carry, preset
  Hex_Digit_Display hex_digit_display_6 (.value(LedData[11:8]));  // open: dp
  Hex_Digit_Display hex_digit_display_7 (.value(LedData[7:4]));  // open: dp
  Clock #(.highDuration(1), .lowDuration(1)) clock_1 (.out(clock_1_out));
  // Probe on EX_PC_t[19:0]
  // Mips_Probe mips_probe_3: pin names not known; wires that end beside it: clock_1_out, _IR, CLK
  ROM #(.addrWidth(10), .dataWidth(32), .Select("high")) rom_1 (.addr(IF_PC_t[11:2]), .data(IF_IR));
  Hex_Digit_Display hex_digit_display_8 (.value(LedData[3:0]));  // open: dp
  D_Flip_Flop #(.trigger("high"), .Pre_Clr_Positions("LEGACY"), .NegatePresetClear("false"), .enable("true"), .NewFFLayout("false")) d_ff_1 (.Q(d_ff_1_q));  // open: clk, D, Qn, preset, en, reset
  // Mips_Probe mips_probe_4: pin names not known; wires that end beside it: IF_IR
  not not_3 (not_3_out, Data);
  and and_4 (and_4_out, not_3_out, Write);
  IF_ID if_id_1 (
    .IR_in(IF_IR), .PC_in(adder_2_out), .\气泡_高电平时有效 (J), .clk(CLK), .clear(RST), .enable(and_4_out),
    .IR_out({ID_IR, Func}), .PC_out(if_id_1_pc_out), .OldPC_in(IF_PC_t), .OldPC_out(ID_PC_t));
  Shifter #(.width(28), .shift("ll")) shifter_2 (.in(_IR[27:0]), .\dist (5'b00010), .out(shifter_2_out));
  // Probe on \总周期数 
  // Probe on MEM_PC[19:0]
  // Mips_Probe mips_probe_5: pin names not known; wires that end beside it: MEM_IR
  // Probe on 13'h250
  // Probe on \总周期数 
  // Probe on \无条件分支数 
  // Probe on \条件分支成功数 
  // Probe on \插入气泡数 
  // Probe on \LoadUse次数 
  Comparator #(.width(13), .mode("twosComplement")) comparator_2 (
    .a(CNT_num), .b(13'h250), .eq(comparator_2_eq), .lt(comparator_2_lt));  // open: gt
  Clock #(.highDuration(1), .lowDuration(1)) clock_2 (.out(clock_2_out));
  Multiplexer #(.select(1), .width(5), .disabled("Z"), .enable("false")) multiplexer_5 (
    .in0(ID_IR[25:21]), .in1(5'b00010), .out(R1), .sel(Syscall));
  assign bit_extender_1_out = {{16{1'b0}}, {ID_IR[15:6], Func}};  // Bit_Extender bit_extender_1
  assign bit_extender_2_out = {{16{ID_IR[15]}}, {ID_IR[15:6], Func}};  // Bit_Extender bit_extender_2
  // Probe on IF_PC_t[11:0]
  // Probe on WB_PC_t[19:0]
  // Mips_Probe mips_probe_6: pin names not known; wires that end beside it: WB_IR
  nand nand_2 (nand_2_out, d_ff_1_q, comparator_2_eq);
  Counter #(.width(13), .max('h1fff), .ongoal("stay"), .trigger("rising"), .behavior("old")) counter_3 (
    .count(comparator_2_lt), .Q(CNT_num), .clk(clock_2_out));  // open: load, D, carry, clr, preset
  \单周期硬布线控制器  \u_单周期硬布线控制器_1  (
    .Func(Func), .OP(ID_IR[31:26]), .ALU_OP(AluOP), .MemToReg(MemToReg), .MemWrite(MemWrite_),
    .ALU_SRC(AluSrcB), .RegWrite(RegWrite_), .SysCALL(Syscall), .SignedExt(SignedExt), .RegDst(RegDst),
    .JR(JR), .JMP(JMP), .Beq(Beq), .JAL(JAL), .Bne(Bne), .LB(LB), .BGTZ(BGTZ));
  Multiplexer #(.select(1), .width(32), .disabled("Z"), .enable("false")) multiplexer_6 (
    .in0(bit_extender_1_out), .in1(bit_extender_2_out), .out(multiplexer_6_out), .sel(SignedExt));
  // Probe on EX_PC_t[11:0]
  // Probe on ID_PC_t[11:0]
  assign CLK = nand_2_out ? clock_2_out : 1'bz;  // Controlled_Buffer controlled_buffer_1
  Pull_Resistor #(.pull(1)) pull_resistor_1 (.node(CLK));
  // Probe on MEM_PC[11:0]
  Multiplexer #(.select(1), .width(5), .disabled("Z"), .enable("false")) multiplexer_7 (
    .in0(ID_IR[20:16]), .in1(5'b00100), .out(R2), .sel(Syscall));
  ResetPC resetpc_1 (.in_1(IF_PC_t), .out_2(IF_PC));
  // Probe on WB_PC_t[11:0]
  Regifile2 regifile2_1 (
    .Din(RDin), .Clk(CLK), .R1(regifile2_1_r1), .R2(regifile2_1_r2), .WE(RegWrite), .W_num(W_num),
    .R1_num(R1), .R2_num(R2));
  ResetPC resetpc_2 (.in_1(ID_PC_t), .out_2(ID_PC));
  or or_1 (or_1_out, Data, J);
  ResetPC resetpc_3 (.in_1(EX_PC_t), .out_2(EX_PC));
  ID_EX id_ex_1 (
    .Beq_in(Beq), .Bne_in(Bne), .MemToReg_in(MemToReg), .MemWrite_in(MemWrite_), .AluOP_in(AluOP),
    .AluSrc_in(AluSrcB), .RegWrite_in(RegWrite_), .JAL_in(JAL), .RegDst_in(RegDst), .Syscall_in(Syscall),
    .JMP_in(JMP), .JR_in(JR), .SignedExt_in(SignedExt), .LB_in(LB), .BGTZ_in(BGTZ), .IR_in({ID_IR, Func}),
    .PC_in(if_id_1_pc_out), .R1_in(regifile2_1_r1), .R2_in(regifile2_1_r2), .Imm_in(multiplexer_6_out),
    .Beq_out(id_ex_1_beq_out), .Bne_out(id_ex_1_bne_out), .MemToReg_out(id_ex_1_memtoreg_out),
    .MemWrite_out(id_ex_1_memwrite_out), .AluOP_out(_AluOP), .AluSrc_out(AluSrc), .RegWrite_out(_RegW),
    .JAL_out(id_ex_1_jal_out), .RegDst_out(id_ex_1_regdst_out), .Syscall_out(_Syscall), .JMP_out(_JMP),
    .JR_out(_JR), .LB_out(_LB), .BGTZ_out(_BGTZ), .IR_out(_IR), .PC_out(_PC_4), .R1_out(_R1), .R2_out(_R2),
    .Imm_out(IMM), .clk(CLK), .clear(RST), .enable(Write), .\气泡_高电平时有效 (or_1_out), .OldPC_in(ID_PC_t),
    .OldPC_out(EX_PC_t));  // open: SignedExt_out
  ResetPC resetpc_4 (.in_1(MEM_PC), .out_2(M_PC));
  Comparator #(.width(6), .mode("twosComplement")) comparator_3 (
    .a(_IR[31:26]), .b({6{1'b0}}), .eq(comparator_3_eq));  // open: gt, lt
  Comparator #(.width(6), .mode("twosComplement")) comparator_4 (
    .a(_IR[5:0]), .b(6'b000100), .eq(comparator_4_eq));  // open: gt, lt
  or or_2 (Flag, and_5_out, _BGTZ, and_7_out);
  and and_5 (and_5_out, id_ex_1_beq_out, _Equal);
  Multiplexer #(.select(1), .width(5), .disabled("Z"), .enable("false")) multiplexer_8 (
    .in0(_IR[20:16]), .in1(_IR[15:11]), .out(multiplexer_8_out), .sel(id_ex_1_regdst_out));
  Multiplexer #(.select(1), .width(32), .disabled("Z"), .enable("false")) multiplexer_9 (
    .in0(_R2), .in1(IMM), .out(multiplexer_9_out), .sel(AluSrc));
  Multiplexer #(.select(1), .width(5), .disabled("Z"), .enable("false")) multiplexer_10 (
    .in0(_IR[10:6]), .in1(_R1[4:0]), .out(multiplexer_10_out), .sel(and_6_out));
  and and_6 (and_6_out, comparator_3_eq, comparator_4_eq);
  ResetPC resetpc_5 (.in_1(WB_PC_t), .out_2(WB_PC));
  Counter #(.width(16), .max('hffff), .ongoal("wrap"), .trigger("rising"), .behavior("old")) counter_4 (
    .load(1'b0), .count(Flag), .Q(\条件分支成功数 ), .clk(CLK), .clr(RST));  // open: D, carry, preset
  and and_7 (and_7_out, id_ex_1_bne_out, not_4_out);
  not not_4 (not_4_out, _Equal);
  Multiplexer #(.select(1), .width(5), .disabled("Z"), .enable("false")) multiplexer_11 (
    .in0(multiplexer_8_out), .in1({5{1'b1}}), .out(EXW_num), .sel(id_ex_1_jal_out));
  MIPS_ALU mips_alu_1 (
    .X(_R1), .Y(multiplexer_12_out), .AluOP(_AluOP), .Equal(_Equal), .Result(mips_alu_1_result),
    .shamt(multiplexer_10_out));  // open: Result_2
  Multiplexer #(.select(1), .width(32), .disabled("Z"), .enable("false")) multiplexer_12 (
    .in0(multiplexer_9_out), .in1(32'h22), .out(multiplexer_12_out), .sel(_Syscall));
  or or_3 (J, Flag, _JR, _JMP);
  Counter #(.width(16), .max('hffff), .ongoal("wrap"), .trigger("rising"), .behavior("old")) counter_5 (
    .load(1'b0), .count(_JMP), .Q(\无条件分支数 ), .clk(CLK), .clr(RST));  // open: D, carry, preset
  EX_MEM ex_mem_1 (
    .\气泡_高电平时有效 (1'b0), .clk(CLK), .clear(RST), .enable(Write), .MemToReg_in(id_ex_1_memtoreg_out),
    .MemToReg_out(ex_mem_1_memtoreg_out), .MemWrite_in(id_ex_1_memwrite_out), .MemWrite_out(MemWrite),
    .RegWrite_in(_RegW), .RegWrite_out(MemRegWrite), .JAL_in(id_ex_1_jal_out), .JAL_out(ex_mem_1_jal_out),
    .LB_in(_LB), .LB_out(ex_mem_1_lb_out), .IR_in(_IR), .IR_out(MEM_IR), .PC_in(_PC_4),
    .PC_out(ex_mem_1_pc_out), .ALUResult_in(mips_alu_1_result), .ALUResult_out(ex_mem_1_aluresult_out),
    .R2_in(_R2), .R2_out(MDin), .RegDst_in(id_ex_1_regdst_out), .RegDst_out(ex_mem_1_regdst_out),
    .Syscall_in(_Syscall), .Syscall_out(ex_mem_1_syscall_out), .equal_in(_Equal),
    .equal_out(ex_mem_1_equal_out), .OldPC_in(EX_PC_t), .OldPC_out(MEM_PC), .pause_out(ex_mem_1_pause_out));  // open: pause_in
  Multiplexer #(.select(1), .width(5), .disabled("Z"), .enable("false")) multiplexer_13 (
    .in0(MEM_IR[20:16]), .in1(MEM_IR[15:11]), .out(multiplexer_13_out), .sel(ex_mem_1_regdst_out));
  Multiplexer #(.select(1), .width(5), .disabled("Z"), .enable("false")) multiplexer_14 (
    .in0(multiplexer_13_out), .in1({5{1'b1}}), .out(MEMW_num), .sel(ex_mem_1_jal_out));
  RAM #(.addrWidth(10), .dataWidth(32), .bus("separate"), .Select("high")) ram_1 (
    .addr(ex_mem_1_aluresult_out[11:2]), .din(MDin), .data(ram_1_data), .str(MemWrite), .clk(CLK), .clr(RST));  // open: sel, ld
  MEM_WB mem_wb_1 (
    .\气泡_高电平时有效 (1'b0), .clk(CLK), .clear(RST), .enable(Write), .MemToReg_in(ex_mem_1_memtoreg_out),
    .MemToReg_out(mem_wb_1_memtoreg_out), .MemWrite_in(MemWrite), .RegWrite_in(MemRegWrite),
    .RegWrite_out(RegWrite), .JAL_in(ex_mem_1_jal_out), .JAL_out(mem_wb_1_jal_out), .LB_in(ex_mem_1_lb_out),
    .LB_out(WBLB), .IR_in(MEM_IR), .IR_out(WB_IR), .PC_in(ex_mem_1_pc_out), .PC_out(mem_wb_1_pc_out),
    .ALUResult_in(ex_mem_1_aluresult_out), .ALUResult_out(mem_wb_1_aluresult_out),
    .Memorydata_in(ram_1_data), .Memorydata_out(mem_wb_1_memorydata_out), .RegDst_in(ex_mem_1_regdst_out),
    .RegDst_out(mem_wb_1_regdst_out), .Syscall_in(ex_mem_1_syscall_out), .Syscall_out(mem_wb_1_syscall_out),
    .equal_in(ex_mem_1_equal_out), .equal_out(mem_wb_1_equal_out), .OldPC_in(MEM_PC), .OldPC_out(WB_PC_t),
    .pause_in(ex_mem_1_pause_out));  // open: MemWrite_out, pause_out
  and and_8 (and_8_out, _Syscall, mem_wb_1_equal_out);
  and and_9 (Pause, mem_wb_1_syscall_out, not_5_out);
  not not_5 (not_5_out, mem_wb_1_equal_out);
  Register #(.width(32), .trigger("rising"), .Select("low")) register_1 (
    .D(_R2), .Q(LedData), .clk(and_8_out), .clr(RST));  // open: en
  Multiplexer #(.select(1), .width(5), .disabled("Z"), .enable("false")) multiplexer_15 (
    .in0(WB_IR[20:16]), .in1(WB_IR[15:11]), .out(multiplexer_15_out), .sel(mem_wb_1_regdst_out));
  Multiplexer #(.select(2), .width(8), .disabled("Z"), .enable("false")) multiplexer_16 (
    .in0(multiplexer_18_out), .in1(multiplexer_18_out_2), .in2(multiplexer_18_out_3),
    .in3(multiplexer_18_out_4), .out(multiplexer_16_out), .sel(mem_wb_1_aluresult_out[1:0]));
  Multiplexer #(.select(1), .width(5), .disabled("Z"), .enable("false")) multiplexer_17 (
    .in0(multiplexer_15_out), .in1({5{1'b1}}), .out(W_num), .sel(mem_wb_1_jal_out));
  Multiplexer #(.select(1), .width(32), .disabled("Z"), .enable("false")) multiplexer_18 (
    .in0(mem_wb_1_aluresult_out), .in1(mem_wb_1_memorydata_out),
    .out({multiplexer_18_out_4, multiplexer_18_out_3, multiplexer_18_out_2, multiplexer_18_out}),
    .sel(mem_wb_1_memtoreg_out));
  assign bit_extender_3_out = {{24{multiplexer_16_out[7]}}, multiplexer_16_out};  // Bit_Extender bit_extender_3
  Multiplexer #(.select(1), .width(32), .disabled("Z"), .enable("false")) multiplexer_19 (
    .in0(multiplexer_20_out), .in1(mem_wb_1_pc_out), .out(RDin), .sel(mem_wb_1_jal_out));
  Multiplexer #(.select(1), .width(32), .disabled("Z"), .enable("false")) multiplexer_20 (
    .in0({multiplexer_18_out_4, multiplexer_18_out_3, multiplexer_18_out_2, multiplexer_18_out}),
    .in1(bit_extender_3_out), .out(multiplexer_20_out), .sel(WBLB));
  // also tied to GND on the sheet: RST

  // Other names for the same wires on the sheet: EX_IR[31:0] = _IR; ID_IR[5:0] = Func; OP[5:0] = ID_IR[31:26];
  //   IR[31:0] = IF_IR

  // Notes on the sheet:
  //   中断源
  //   时空图监测，可删除
  //   中断等待指示
  //   数码管输出
  //   指令存储器
  //   contents of rom_1 (hex, n*v repeats v):
  //   20110001 8000c05 20110001 20120002 20130003 8000c09 20110001 20120002 20130003 8000c0d 20110001
  //   20120002 20130003 8000c11 20110001 20120002 20130003 c000cb8 20100001 20110001 118fc0 112020
  //   20020022 c 118882 12200001 8000c15 112020 20020022 c 20110001 118880 112020 20020022 c 12200001
  //   8000c1f 20110001 118fc0 112020 20020022 c 1188c3 112020 20020022 c 118903 112020 20020022 c 118903
  //   112020 20020022 c 118903 112020 20020022 c 118903 112020 20020022 c 118903 112020 20020022 c 118903
  //   112020 20020022 c 118903 112020 20020022 c 20100001 109fc0 139fc3 8021 2012000c 24160003 26100001
  //   3210000f 20080008 20090001 139900 2709825 132020 20020022 c 1094022 1500fff9 22100001 2018000f
  //   2188024 108700 20080008 20090001 139902 2709825 132021 20020022 c 1094022 1500fff9 108702 2c9b022
  //   12c00001 8000c50 4020 1084027 84400 3508ffff 82021 20020022 c 2010ffff 20110000 ae300000 22100001
  //   22310004 ae300000 22100001 22310004 ae300000 22100001 22310004 ae300000 22100001 22310004 ae300000
  //   22100001 22310004 ae300000 22100001 22310004 ae300000 22100001 22310004 ae300000 22100001 22310004
  //   ae300000 22100001 22310004 ae300000 22100001 22310004 ae300000 22100001 22310004 ae300000 22100001
  //   22310004 ae300000 22100001 22310004 ae300000 22100001 22310004 ae300000 22100001 22310004 ae300000
  //   22100001 22310004 22100001 8020 2011003c 8e130000 8e340000 274402a 11000002 ae330000 ae140000
  //   2231fffc 1611fff8 102020 20020022 c 22100004 2011003c 1611fff2 20020032 c 20100000 22100001 102020
  //   20020022 c 22100002 102020 20020022 c 22100003 102020 20020022 c 22100004 102020 20020022 c 22100005
  //   102020 20020022 c 22100006 102020 20020022 c 22100007 102020 20020022 c 22100008 102020 20020022
  //   20020022 c 3e00008
  //   控制位
  //   暂停节拍，不能为0
  //   用这个时钟源需要去掉电路中的其他时钟源
  //   OP
  //   rs
  //   指令字
  //   rt
  //   戳工具置1进入计数暂停模式，ctrl+k时钟自动运行到对应节拍暂停
  //   ctrl+k关闭时钟连续运行，将控制位置零，进入单步调试模式调试
  //   Func
  //   Beq
  //   JMP
  //   JR
  //   Bne
  //   LB
  //   BGTZ
  //   OP
  //   JAL
  //   Func
  //   Syscall
  //   可计数暂停的时钟源
  //   MemToReg
  //   MemWrite
  //   AluOP
  //   AluSrcB
  //   RegWrite
  //   RegDst
  //   流水调试日志用
  //   OP
  //   Func
  //   为方便自动评测，需要输出流水线各段保存的PC值，注意是PC不是PC+4，另外ID段寄存器写入信息，Mem段内存写入信息也要输出
endmodule
module \重定向流水线  (
  output RegWrite,
  output MemWrite,
  output [31:0] IF_PC,
  output [31:0] ID_PC,
  output [31:0] EX_PC,
  output [31:0] M_PC,
  output [31:0] WB_PC,
  output [31:0] RDin,
  output [31:0] MDin,
  output [31:0] LedData
);

  wire _0x22, _BGTZ, _Equal, _JMP, _JR, _LB, _RegW, _Syscall, AluSrc, AluSrcB, and_1_out, and_2_out,
       and_3_out, and_4_out, and_5_out, and_6_out, and_7_out, and_8_out, Beq, BGTZ, Bne, CLK, clock_1_out,
       clock_2_out, comparator_1_gt, comparator_2_eq, comparator_2_lt, comparator_3_eq, comparator_4_eq,
       d_ff_1_q, ex_mem_1_equal_out, ex_mem_1_jal_out, ex_mem_1_lb_out, ex_mem_1_pause_out,
       ex_mem_1_regdst_out, ex_mem_1_syscall_out, Flag, Go, id_ex_1_beq_out, id_ex_1_bne_out,
       id_ex_1_jal_out, id_ex_1_memtoreg_out, id_ex_1_memwrite_out, id_ex_1_regdst_out, IR1, IR2, IR3, J,
       JAL, JMP, JR, LB, LoadUse, MEM_MemToReg, mem_wb_1_jal_out, mem_wb_1_memtoreg_out, mem_wb_1_regdst_out,
       MemRegWrite, MemToReg, MemWrite_, multiplexer_3_out, nand_2_out, not_1_out, not_2_out, not_3_out,
       not_4_out, not_5_out, OLDPause, or_1_out, or_2_out, Pause, RegDst, RegWrite_, RST, SignedExt, Syscall,
       W1, W2, W3, WBLB, Write;
  wire [1:0] CR1, CR2, loaduse_1_choose_r1, loaduse_1_choose_r2, multiplexer_5_out, multiplexer_6_out;
  wire [3:0] _AluOP, AluOP;
  wire [4:0] EXW_num, MEMW_num, multiplexer_12_out, multiplexer_13_out, multiplexer_16_out,
       multiplexer_19_out, R1, R2, W_num;
  wire [5:0] Func;
  wire [7:0] multiplexer_22_out;
  wire [12:0] CNT_num;
  wire [15:0] \LoadUse次数 , \总周期数 , \插入气泡数 , \无条件分支数 , \条件分支成功数 ;
  wire [27:0] shifter_2_out;
  wire [31:0] _IR, _PC_4, _R1, _R2, adder_1_out, adder_2_out, bit_extender_1_out, bit_extender_2_out,
       bit_extender_3_out, ex_mem_1_pc_out, EX_PC_t, ID_PC_t, if_id_1_pc_out, IF_IR, IF_PC_t, IMM, MEM_IR,
       MEM_MemData, MEM_PC, mem_wb_1_pc_out, mips_alu_1_result, multiplexer_1_out, multiplexer_2_out,
       multiplexer_4_out, multiplexer_8_out, multiplexer_10_out, multiplexer_15_out, multiplexer_21_out,
       NEWALUResult, NEWR1, NEWR2, OLDALUResult, OLDMEMData, ram_1_data, regifile2_1_r1, regifile2_1_r2,
       shifter_1_out, WB_IR, WB_PC_t;
  wire [31:6] ID_IR;

  Button \u_总复位  (.out(RST));
  Button _1 (.out(IR1));
  Button _2 (.out(IR2));
  Button _3 (.out(IR3));
  // Probe on \总周期数 
  // Probe on \总周期数 
  Button \u_继续运行  (.out(Go));
  LED #(.active("true")) led_1 (.in(W1));
  LED #(.active("true")) led_2 (.in(W2));
  LED #(.active("true")) led_3 (.in(W3));
  Multiplexer #(.select(1), .width(32), .disabled("Z"), .enable("false")) multiplexer_1 (
    .in0(adder_2_out), .in1(adder_1_out), .out(multiplexer_1_out), .sel(Flag));
  Hex_Digit_Display hex_digit_display_1 (.value(LedData[31:28]));  // open: dp
  // Probe on IF_PC_t[19:0]
  // Mips_Probe mips_probe_1: pin names not known; wires that end beside it: IF_IR
  nand nand_1 (Write, not_2_out, Pause);
  Multiplexer #(.select(2), .width(32), .disabled("Z"), .enable("false")) multiplexer_2 (
    .in0(multiplexer_1_out), .in1(_R1), .in2({_PC_4[31:28], shifter_2_out}), .in3(_R1),
    .out(multiplexer_2_out), .sel({_JMP, _JR}));
  and and_1 (and_1_out, not_1_out, multiplexer_3_out);
  not not_1 (not_1_out, LoadUse);
  Multiplexer #(.select(1), .width(1), .disabled("Z"), .enable("false")) multiplexer_3 (
    .in0(1'b1), .in1(Go), .out(multiplexer_3_out), .sel(Pause));
  Shifter #(.width(32), .shift("ll")) shifter_1 (.in(IMM), .\dist (5'b00010), .out(shifter_1_out));
  Adder #(.width(32)) adder_1 (.a(shifter_1_out), .b(_PC_4), .out(adder_1_out));  // open: cin, cout
  Hex_Digit_Display hex_digit_display_2 (.value(LedData[23:20]));  // open: dp
  Hex_Digit_Display hex_digit_display_3 (.value(LedData[27:24]));  // open: dp
  // Probe on ID_PC_t[19:0]
  // Mips_Probe mips_probe_2: pin names not known; wires that end beside it: {ID_IR, Func}
  not not_2 (not_2_out, Go);
  Comparator #(.width(32), .mode("twosComplement")) comparator_1 (
    .a(_R1), .b({32{1'b0}}), .gt(comparator_1_gt));  // open: eq, lt
  and and_2 (and_2_out, comparator_1_gt, BGTZ);
  Multiplexer #(.select(1), .width(32), .disabled("Z"), .enable("false")) multiplexer_4 (
    .in0(multiplexer_2_out), .in1(adder_1_out), .out(multiplexer_4_out), .sel(and_2_out));
  Register #(.width(32), .trigger("rising"), .Select("low")) PC (
    .D(multiplexer_4_out), .en(and_1_out), .Q(IF_PC_t), .clk(CLK), .clr(RST));
  Counter #(.width(16), .max('hffff), .ongoal("wrap"), .trigger("rising"), .behavior("old")) counter_1 (
    .load(1'b0), .count(multiplexer_3_out), .Q(\总周期数 ), .clk(CLK), .clr(RST));  // open: D, carry, preset
  Hex_Digit_Display hex_digit_display_4 (.value(LedData[15:12]));  // open: dp
  Hex_Digit_Display hex_digit_display_5 (.value(LedData[19:16]));  // open: dp
  LoadUse loaduse_1 (
    .load_use(LoadUse), .Choose_R1(loaduse_1_choose_r1), .Ex_OP(_IR[31:26]), .Choose_R2(loaduse_1_choose_r2),
    .Ex_WriteReg_num(EXW_num), .Mem_WriteReg_num(MEMW_num), .Ex_RegWrite_num(_RegW), .OP(ID_IR[31:26]),
    .Mem_RegWrite_num(MemRegWrite), .FUNC(Func), .MemToReg(MEM_MemToReg), .ID_R2_num(R2), .ID_R1_num(R1));
  Adder #(.width(32)) adder_2 (.a(IF_PC_t), .b(32'h4), .out(adder_2_out));  // open: cin, cout
  Hex_Digit_Display hex_digit_display_6 (.value(LedData[7:4]));  // open: dp
  Hex_Digit_Display hex_digit_display_7 (.value(LedData[11:8]));  // open: dp
  Clock #(.highDuration(1), .lowDuration(1)) clock_1 (.out(clock_1_out));
  // Probe on EX_PC_t[19:0]
  // Mips_Probe mips_probe_3: pin names not known; wires that end beside it: clock_1_out, _IR, CLK
  ROM #(.addrWidth(10), .dataWidth(32), .Select("high")) rom_1 (.addr(IF_PC_t[11:2]), .data(IF_IR));
  Hex_Digit_Display hex_digit_display_8 (.value(LedData[3:0]));  // open: dp
  or or_1 (or_1_out, J, LoadUse);
  Multiplexer #(.select(1), .width(2), .disabled("Z"), .enable("false")) multiplexer_5 (
    .in0(loaduse_1_choose_r1), .in1(2'b00), .out(multiplexer_5_out), .sel(or_1_out));
  Multiplexer #(.select(1), .width(2), .disabled("Z"), .enable("false")) multiplexer_6 (
    .in0(loaduse_1_choose_r2), .in1(2'b00), .out(multiplexer_6_out), .sel(or_1_out));
  // Mips_Probe mips_probe_4: pin names not known; wires that end beside it: IF_IR
  not not_3 (not_3_out, LoadUse);
  Shifter #(.width(28), .shift("ll")) shifter_2 (.in(_IR[27:0]), .\dist (5'b00010), .out(shifter_2_out));
  // Probe on \总周期数 
  // Probe on MEM_PC[19:0]
  // Mips_Probe mips_probe_5: pin names not known; wires that end beside it: MEM_IR
  and and_3 (and_3_out, not_3_out, Write);
  IF_ID if_id_1 (
    .IR_in(IF_IR), .PC_in(adder_2_out), .\气泡_高电平时有效 (J), .clk(CLK), .clear(RST), .enable(and_3_out),
    .IR_out({ID_IR, Func}), .PC_out(if_id_1_pc_out), .OldPC_in(IF_PC_t), .OldPC_out(ID_PC_t));
  // Probe on \总周期数 
  // Probe on \无条件分支数 
  // Probe on \条件分支成功数 
  // Probe on \插入气泡数 
  // Probe on \LoadUse次数 
  Register #(.width(2), .trigger("rising"), .Select("low")) register_1 (
    .D(multiplexer_5_out), .en(Write), .Q(CR1), .clk(CLK), .clr(RST));
  Register #(.width(2), .trigger("rising"), .Select("low")) register_2 (
    .D(multiplexer_6_out), .en(Write), .Q(CR2), .clk(CLK), .clr(RST));
  Multiplexer #(.select(1), .width(5), .disabled("Z"), .enable("false")) multiplexer_7 (
    .in0(ID_IR[25:21]), .in1(5'b00010), .out(R1), .sel(Syscall));
  // Probe on IF_PC_t[11:0]
  // Probe on WB_PC_t[19:0]
  // Mips_Probe mips_probe_6: pin names not known; wires that end beside it: WB_IR
  \单周期硬布线控制器  \u_单周期硬布线控制器_1  (
    .Func(Func), .OP(ID_IR[31:26]), .ALU_OP(AluOP), .MemToReg(MemToReg), .MemWrite(MemWrite_),
    .ALU_SRC(AluSrcB), .RegWrite(RegWrite_), .SysCALL(Syscall), .SignedExt(SignedExt), .RegDst(RegDst),
    .JR(JR), .JMP(JMP), .Beq(Beq), .JAL(JAL), .Bne(Bne), .LB(LB), .BGTZ(BGTZ));
  assign bit_extender_1_out = {{16{1'b0}}, {ID_IR[15:6], Func}};  // Bit_Extender bit_extender_1
  assign bit_extender_2_out = {{16{ID_IR[15]}}, {ID_IR[15:6], Func}};  // Bit_Extender bit_extender_2
  // Probe on EX_PC_t[11:0]
  // Probe on ID_PC_t[11:0]
  Multiplexer #(.select(1), .width(32), .disabled("Z"), .enable("false")) multiplexer_8 (
    .in0(bit_extender_1_out), .in1(bit_extender_2_out), .out(multiplexer_8_out), .sel(SignedExt));
  // Probe on MEM_PC[11:0]
  D_Flip_Flop #(.trigger("high"), .Pre_Clr_Positions("LEGACY"), .NegatePresetClear("false"), .enable("true"), .NewFFLayout("false")) d_ff_1 (.Q(d_ff_1_q));  // open: clk, D, Qn, preset, en, reset
  // Probe on 13'h376
  and and_4 (and_4_out, LoadUse, Write);
  Multiplexer #(.select(1), .width(5), .disabled("Z"), .enable("false")) multiplexer_9 (
    .in0(ID_IR[20:16]), .in1(5'b00100), .out(R2), .sel(Syscall));
  ResetPC resetpc_1 (.in_1(IF_PC_t), .out_2(IF_PC));
  // Probe on WB_PC_t[11:0]
  Comparator #(.width(13), .mode("twosComplement")) comparator_2 (
    .a(CNT_num), .b(13'h376), .eq(comparator_2_eq), .lt(comparator_2_lt));  // open: gt
  Clock #(.highDuration(1), .lowDuration(1)) clock_2 (.out(clock_2_out));
  Regifile2 regifile2_1 (
    .Din(RDin), .Clk(CLK), .R1(regifile2_1_r1), .R2(regifile2_1_r2), .WE(RegWrite), .W_num(W_num),
    .R1_num(R1), .R2_num(R2));
  nand nand_2 (nand_2_out, d_ff_1_q, comparator_2_eq);
  Counter #(.width(13), .max('h1fff), .ongoal("stay"), .trigger("rising"), .behavior("old")) counter_2 (
    .count(comparator_2_lt), .Q(CNT_num), .clk(clock_2_out));  // open: load, D, carry, clr, preset
  ResetPC resetpc_2 (.in_1(ID_PC_t), .out_2(ID_PC));
  assign CLK = nand_2_out ? clock_2_out : 1'bz;  // Controlled_Buffer controlled_buffer_1
  Counter #(.width(16), .max('hffff), .ongoal("wrap"), .trigger("rising"), .behavior("old")) counter_3 (
    .D({16{1'b0}}), .count(and_4_out), .Q(\LoadUse次数 ), .clk(CLK), .clr(RST));  // open: load, carry, preset
  Pull_Resistor #(.pull(1)) pull_resistor_1 (.node(CLK));
  or or_2 (or_2_out, LoadUse, J);
  ResetPC resetpc_3 (.in_1(EX_PC_t), .out_2(EX_PC));
  ID_EX id_ex_1 (
    .Beq_in(Beq), .Bne_in(Bne), .MemToReg_in(MemToReg), .MemWrite_in(MemWrite_), .AluOP_in(AluOP),
    .AluSrc_in(AluSrcB), .RegWrite_in(RegWrite_), .JAL_in(JAL), .RegDst_in(RegDst), .Syscall_in(Syscall),
    .JMP_in(JMP), .JR_in(JR), .SignedExt_in(SignedExt), .LB_in(LB), .BGTZ_in(BGTZ), .IR_in({ID_IR, Func}),
    .PC_in(if_id_1_pc_out), .R1_in(regifile2_1_r1), .R2_in(regifile2_1_r2), .Imm_in(multiplexer_8_out),
    .Beq_out(id_ex_1_beq_out), .Bne_out(id_ex_1_bne_out), .MemToReg_out(id_ex_1_memtoreg_out),
    .MemWrite_out(id_ex_1_memwrite_out), .AluOP_out(_AluOP), .AluSrc_out(AluSrc), .RegWrite_out(_RegW),
    .JAL_out(id_ex_1_jal_out), .RegDst_out(id_ex_1_regdst_out), .Syscall_out(_Syscall), .JMP_out(_JMP),
    .JR_out(_JR), .LB_out(_LB), .BGTZ_out(_BGTZ), .IR_out(_IR), .PC_out(_PC_4), .R1_out(_R1), .R2_out(_R2),
    .Imm_out(IMM), .clk(CLK), .clear(RST), .enable(Write), .\气泡_高电平时有效 (or_2_out), .OldPC_in(ID_PC_t),
    .OldPC_out(EX_PC_t));  // open: SignedExt_out
  ResetPC resetpc_4 (.in_1(MEM_PC), .out_2(M_PC));
  Comparator #(.width(6), .mode("twosComplement")) comparator_3 (
    .a(_IR[31:26]), .b({6{1'b0}}), .eq(comparator_3_eq));  // open: gt, lt
  Comparator #(.width(6), .mode("twosComplement")) comparator_4 (
    .a(_IR[5:0]), .b(6'b000100), .eq(comparator_4_eq));  // open: gt, lt
  or or_3 (Flag, and_5_out, _BGTZ, and_7_out);
  and and_5 (and_5_out, id_ex_1_beq_out, _Equal);
  Multiplexer #(.select(2), .width(32), .disabled("Z"), .enable("false")) multiplexer_10 (
    .in0(_R1), .in1(NEWALUResult), .in2(OLDALUResult), .in3(MEM_MemData), .out(multiplexer_10_out), .sel(CR1));
  Multiplexer #(.select(2), .width(32), .disabled("Z"), .enable("false")) multiplexer_11 (
    .in0(_R2), .in1(NEWALUResult), .in2(OLDALUResult), .in3(MEM_MemData), .out(NEWR2), .sel(CR2));
  Multiplexer #(.select(1), .width(5), .disabled("Z"), .enable("false")) multiplexer_12 (
    .in0(_IR[10:6]), .in1(_R1[4:0]), .out(multiplexer_12_out), .sel(and_6_out));
  and and_6 (and_6_out, comparator_3_eq, comparator_4_eq);
  ResetPC resetpc_5 (.in_1(WB_PC_t), .out_2(WB_PC));
  Counter #(.width(16), .max('hffff), .ongoal("wrap"), .trigger("rising"), .behavior("old")) counter_4 (
    .load(1'b0), .count(Flag), .Q(\条件分支成功数 ), .clk(CLK), .clr(RST));  // open: D, carry, preset
  and and_7 (and_7_out, id_ex_1_bne_out, not_4_out);
  not not_4 (not_4_out, _Equal);
  Multiplexer #(.select(1), .width(5), .disabled("Z"), .enable("false")) multiplexer_13 (
    .in0(_IR[20:16]), .in1(_IR[15:11]), .out(multiplexer_13_out), .sel(id_ex_1_regdst_out));
  Multiplexer #(.select(1), .width(5), .disabled("Z"), .enable("false")) multiplexer_14 (
    .in0(multiplexer_13_out), .in1({5{1'b1}}), .out(EXW_num), .sel(id_ex_1_jal_out));
  Multiplexer #(.select(1), .width(32), .disabled("Z"), .enable("false")) multiplexer_15 (
    .in0(NEWR2), .in1(IMM), .out(multiplexer_15_out), .sel(AluSrc));
  or or_4 (J, Flag, _JR, _JMP);
  MIPS_ALU mips_alu_1 (
    .X(multiplexer_10_out), .Y(multiplexer_15_out), .AluOP(_AluOP), .Equal(_Equal),
    .Result(mips_alu_1_result), .shamt(multiplexer_12_out));  // open: Result_2
  Counter #(.width(16), .max('hffff), .ongoal("wrap"), .trigger("rising"), .behavior("old")) counter_5 (
    .load(1'b0), .count(_JMP), .Q(\无条件分支数 ), .clk(CLK), .clr(RST));  // open: D, carry, preset
  EX_MEM ex_mem_1 (
    .\气泡_高电平时有效 (1'b0), .clk(CLK), .clear(RST), .enable(Write), .MemToReg_in(id_ex_1_memtoreg_out),
    .MemToReg_out(MEM_MemToReg), .MemWrite_in(id_ex_1_memwrite_out), .MemWrite_out(MemWrite),
    .RegWrite_in(_RegW), .RegWrite_out(MemRegWrite), .JAL_in(id_ex_1_jal_out), .JAL_out(ex_mem_1_jal_out),
    .LB_in(_LB), .LB_out(ex_mem_1_lb_out), .IR_in(_IR), .IR_out(MEM_IR), .PC_in(_PC_4),
    .PC_out(ex_mem_1_pc_out), .ALUResult_in(mips_alu_1_result), .ALUResult_out(NEWALUResult), .R2_in(NEWR2),
    .R2_out(MDin), .RegDst_in(id_ex_1_regdst_out), .RegDst_out(ex_mem_1_regdst_out), .Syscall_in(_Syscall),
    .Syscall_out(ex_mem_1_syscall_out), .equal_in(_Equal), .equal_out(ex_mem_1_equal_out),
    .OldPC_in(EX_PC_t), .OldPC_out(MEM_PC), .pause_in(OLDPause), .pause_out(ex_mem_1_pause_out));
  Multiplexer #(.select(1), .width(5), .disabled("Z"), .enable("false")) multiplexer_16 (
    .in0(MEM_IR[20:16]), .in1(MEM_IR[15:11]), .out(multiplexer_16_out), .sel(ex_mem_1_regdst_out));
  Multiplexer #(.select(1), .width(5), .disabled("Z"), .enable("false")) multiplexer_17 (
    .in0(multiplexer_16_out), .in1({5{1'b1}}), .out(MEMW_num), .sel(ex_mem_1_jal_out));
  RAM #(.addrWidth(10), .dataWidth(32), .bus("separate"), .Select("high")) ram_1 (
    .addr(NEWALUResult[11:2]), .din(MDin), .data(ram_1_data), .str(MemWrite), .clk(CLK), .clr(RST));  // open: sel, ld
  MEM_WB mem_wb_1 (
    .\气泡_高电平时有效 (1'b0), .clk(CLK), .clear(RST), .enable(Write), .MemToReg_in(MEM_MemToReg),
    .MemToReg_out(mem_wb_1_memtoreg_out), .MemWrite_in(MemWrite), .RegWrite_in(MemRegWrite),
    .RegWrite_out(RegWrite), .JAL_in(ex_mem_1_jal_out), .JAL_out(mem_wb_1_jal_out), .LB_in(ex_mem_1_lb_out),
    .LB_out(WBLB), .IR_in(MEM_IR), .IR_out(WB_IR), .PC_in(ex_mem_1_pc_out), .PC_out(mem_wb_1_pc_out),
    .ALUResult_in(NEWALUResult), .ALUResult_out(OLDALUResult), .Memorydata_in(ram_1_data),
    .Memorydata_out(OLDMEMData), .RegDst_in(ex_mem_1_regdst_out), .RegDst_out(mem_wb_1_regdst_out),
    .Syscall_in(ex_mem_1_syscall_out), .equal_in(ex_mem_1_equal_out), .OldPC_in(MEM_PC), .OldPC_out(WB_PC_t),
    .pause_in(ex_mem_1_pause_out), .pause_out(Pause));  // open: MemWrite_out, Syscall_out, equal_out
  Multiplexer #(.select(2), .width(32), .disabled("Z"), .enable("false")) multiplexer_18 (
    .in0(_R1), .in1(NEWALUResult), .in2(OLDALUResult), .in3(MEM_MemData), .out(NEWR1), .sel(CR1));
  and and_8 (and_8_out, _0x22, _Syscall);
  and and_9 (OLDPause, _Syscall, not_5_out);
  not not_5 (not_5_out, _0x22);
  Multiplexer #(.select(1), .width(5), .disabled("Z"), .enable("false")) multiplexer_19 (
    .in0(WB_IR[20:16]), .in1(WB_IR[15:11]), .out(multiplexer_19_out), .sel(mem_wb_1_regdst_out));
  Multiplexer #(.select(1), .width(5), .disabled("Z"), .enable("false")) multiplexer_20 (
    .in0(multiplexer_19_out), .in1({5{1'b1}}), .out(W_num), .sel(mem_wb_1_jal_out));
  Comparator #(.width(32), .mode("twosComplement")) comparator_5 (.a(NEWR1), .b(32'h22), .eq(_0x22));  // open: gt, lt
  Register #(.width(32), .trigger("rising"), .Select("low")) register_3 (
    .D(NEWR2), .Q(LedData), .clk(and_8_out), .clr(RST));  // open: en
  Multiplexer #(.select(1), .width(32), .disabled("Z"), .enable("false")) multiplexer_21 (
    .in0(OLDALUResult), .in1(MEM_MemData), .out(multiplexer_21_out), .sel(mem_wb_1_memtoreg_out));
  Multiplexer #(.select(2), .width(8), .disabled("Z"), .enable("false")) multiplexer_22 (
    .in0(OLDMEMData[7:0]), .in1(OLDMEMData[15:8]), .in2(OLDMEMData[23:16]), .in3(OLDMEMData[31:24]),
    .out(multiplexer_22_out), .sel(OLDALUResult[1:0]));
  Multiplexer #(.select(1), .width(32), .disabled("Z"), .enable("false")) multiplexer_23 (
    .in0(multiplexer_21_out), .in1(mem_wb_1_pc_out), .out(RDin), .sel(mem_wb_1_jal_out));
  assign bit_extender_3_out = {{24{multiplexer_22_out[7]}}, multiplexer_22_out};  // Bit_Extender bit_extender_3
  Multiplexer #(.select(1), .width(32), .disabled("Z"), .enable("false")) multiplexer_24 (
    .in0(OLDMEMData), .in1(bit_extender_3_out), .out(MEM_MemData), .sel(WBLB));
  // also tied to GND on the sheet: RST

  // Other names for the same wires on the sheet: EX_IR[31:0] = _IR; ID_IR[5:0] = Func; OP[5:0] = ID_IR[31:26];
  //   IR[31:0] = IF_IR

  // Notes on the sheet:
  //   中断源
  //   时空图监测，可删除
  //   中断等待指示
  //   数码管输出
  //   指令存储器
  //   contents of rom_1 (hex, n*v repeats v):
  //   20110001 8000c05 20110001 20120002 20130003 8000c09 20110001 20120002 20130003 8000c0d 20110001
  //   20120002 20130003 8000c11 20110001 20120002 20130003 c000cb8 20100001 20110001 118fc0 112020
  //   20020022 c 118882 12200001 8000c15 112020 20020022 c 20110001 118880 112020 20020022 c 12200001
  //   8000c1f 20110001 118fc0 112020 20020022 c 1188c3 112020 20020022 c 118903 112020 20020022 c 118903
  //   112020 20020022 c 118903 112020 20020022 c 118903 112020 20020022 c 118903 112020 20020022 c 118903
  //   112020 20020022 c 118903 112020 20020022 c 20100001 109fc0 139fc3 8021 2012000c 24160003 26100001
  //   3210000f 20080008 20090001 139900 2709825 132020 20020022 c 1094022 1500fff9 22100001 2018000f
  //   2188024 108700 20080008 20090001 139902 2709825 132021 20020022 c 1094022 1500fff9 108702 2c9b022
  //   12c00001 8000c50 4020 1084027 84400 3508ffff 82021 20020022 c 2010ffff 20110000 ae300000 22100001
  //   22310004 ae300000 22100001 22310004 ae300000 22100001 22310004 ae300000 22100001 22310004 ae300000
  //   22100001 22310004 ae300000 22100001 22310004 ae300000 22100001 22310004 ae300000 22100001 22310004
  //   ae300000 22100001 22310004 ae300000 22100001 22310004 ae300000 22100001 22310004 ae300000 22100001
  //   22310004 ae300000 22100001 22310004 ae300000 22100001 22310004 ae300000 22100001 22310004 ae300000
  //   22100001 22310004 22100001 8020 2011003c 8e130000 8e340000 274402a 11000002 ae330000 ae140000
  //   2231fffc 1611fff8 102020 20020022 c 22100004 2011003c 1611fff2 20020032 c 20100000 22100001 102020
  //   20020022 c 22100002 102020 20020022 c 22100003 102020 20020022 c 22100004 102020 20020022 c 22100005
  //   102020 20020022 c 22100006 102020 20020022 c 22100007 102020 20020022 c 22100008 102020 20020022
  //   20020022 c 3e00008
  //   指令字
  //   OP
  //   Func
  //   rs
  //   rt
  //   JMP
  //   JR
  //   LB
  //   BGTZ
  //   OP
  //   Func
  //   Syscall
  //   控制位
  //   Beq
  //   Bne
  //   MemToReg
  //   MemWrite
  //   AluOP
  //   AluSrcB
  //   RegWrite
  //   JAL
  //   RegDst
  //   流水调试日志用
  //   暂停节拍，不能为0
  //   戳工具置1进入计数暂停模式，ctrl+k时钟自动运行到对应节拍暂停
  //   ctrl+k关闭时钟连续运行，将控制位置零，进入单步调试模式调试
  //   可计数暂停的时钟源
  //   OP
  //   Func
  //   为方便自动评测，需要输出流水线各段保存的PC值，注意是PC不是PC+4，另外ID段寄存器写入信息，Mem段内存写入信息也要输出
endmodule

module \中断按键参考电路  (
  input  \同步清零信号 ,
  output \与中断屏蔽位与 
);

  wire \_1号中断_out , and_1_out, clock_1_out, d_ff_1_q, or_1_out, or_2_out;

  Clock #(.highDuration(1), .lowDuration(1)) clock_1 (.out(clock_1_out));
  Button \_1号中断  (.out(\_1号中断_out ));
  LED #(.active("true")) \_1号中断等待指示灯  (.in(or_1_out));
  or or_1 (or_1_out, \与中断屏蔽位与 , d_ff_1_q);
  D_Flip_Flop #(.trigger("rising"), .Pre_Clr_Positions("LEGACY"), .NegatePresetClear("false"), .enable("true"), .NewFFLayout("false")) d_ff_1 (
    .clk(\_1号中断_out ), .D(1'b1), .Q(d_ff_1_q), .reset(\与中断屏蔽位与 ));  // open: Qn, preset, en
  or or_2 (or_2_out, d_ff_1_q, \与中断屏蔽位与 );
  and and_1 (and_1_out, or_2_out, ~\同步清零信号 );  // AND_Gate
  D_Flip_Flop #(.trigger("rising"), .Pre_Clr_Positions("LEGACY"), .NegatePresetClear("false"), .enable("true"), .NewFFLayout("false")) IR1 (
    .clk(clock_1_out), .D(and_1_out), .Q(\与中断屏蔽位与 ));  // open: Qn, preset, en, reset
  \单周期硬布线控制器  \u_单周期硬布线控制器_1  ();  // open: Func, OP, ALU_OP, MemToReg, MemWrite, ALU_SRC, RegWrite, SysCALL, SignedExt, RegDst, JR, JMP, Beq, JAL, Bne, LB, BGTZ

  // Notes on the sheet:
  //   中断信号采样参考电路
  //   Reset 
endmodule

module \单周期MIPS_单级中断  (
  input  IR1,
  input  IR2,
  input  IR3,
  output RegWrite,
  output MemWrite,
  output [31:0] PC,
  output [31:0] IR,
  output [31:0] RDin,
  output [31:0] MDin,
  output [31:0] LedData
);

  wire AluSrcB, and_1_out, and_2_out, and_3_out, and_4_out, and_5_out, and_6_out, and_7_out, and_8_out,
       and_10_out, and_12_out, and_13_out, and_14_out, and_15_out, Beq, BGTZ, Bne, CLK, clock_2_out,
       comparator_1_eq, comparator_2_eq, comparator_3_eq, comparator_4_eq, comparator_5_gt, comparator_6_eq,
       comparator_6_lt, comparator_7_eq, comparator_8_eq, comparator_9_eq, comparator_10_eq,
       controlled_inverter_1_out, controlled_inverter_2_out, controlled_inverter_3_out, d_ff_1_q, d_ff_2_q,
       d_ff_3_q, d_ff_4_q, ERET, Go, IR1_2_q, IR1_3_q, IR1_q, IR1_t, IR2_t, IR3_t, IRA, IRB, IRC, JAL, LB,
       MemToReg, mips_alu_1_equal, multiplexer_3_out, multiplexer_5_out, nand_1_out, not_2_out, NotEqual,
       or_3_out, or_5_out, or_6_out, or_7_out, or_11_out, or_12_out, priority_encoder_1_gs, RegDst,
       register_2_q, SignedExt, Syscall, W1, W2, W3;
  wire [1:0] IRnow, mips_alu_1_result, multiplexer_13_out, priority_encoder_1_out, \单周期硬布线控制器_1_jr ;
  wire [3:0] AluOP;
  wire [4:0] multiplexer_7_out, multiplexer_9_out, multiplexer_10_out, multiplexer_14_out,
       multiplexer_17_out, Shamt;
  wire [7:0] multiplexer_21_out;
  wire [9:0] mips_alu_1_result_2;
  wire [12:0] CNT_num;
  wire [15:0] \总周期数 ;
  wire [27:0] shifter_1_out;
  wire [31:0] adder_2_out, bit_extender_1_out, bit_extender_2_out, bit_extender_3_out, multiplexer_1_out,
       multiplexer_2_out, multiplexer_6_out, multiplexer_8_out, multiplexer_11_out, multiplexer_15_out,
       multiplexer_16_out, multiplexer_19_out, multiplexer_20_out, PC_4, PC_q, PCin, PCnext, ram_1_data,
       register_1_q, shifter_2_out;
  wire [31:5] mips_regifile_1_r1;
  wire [31:12] mips_alu_1_result_3;

  Clock #(.highDuration(1), .lowDuration(1)) clock_1 ();  // open: out
  Button _1 (.out(IRA));
  Button _2 (.out(IRB));
  Button _3 (.out(IRC));
  Button \u_继续运行  (.out(Go));
  LED #(.active("true")) led_1 (.in(W1));
  LED #(.active("true")) led_2 (.in(W2));
  LED #(.active("true")) led_3 (.in(W3));
  Hex_Digit_Display hex_digit_display_1 (.value(LedData[31:28]));  // open: dp
  Comparator #(.width(16), .mode("twosComplement")) comparator_1 (
    .a(16'h23b), .b(\总周期数 ), .eq(comparator_1_eq));  // open: gt, lt
  Comparator #(.width(16), .mode("twosComplement")) comparator_2 (
    .a(\总周期数 ), .b(16'h1), .eq(comparator_2_eq));  // open: gt, lt
  Comparator #(.width(16), .mode("twosComplement")) comparator_3 (
    .a(\总周期数 ), .b(16'h4), .eq(comparator_3_eq));  // open: gt, lt
  Comparator #(.width(16), .mode("twosComplement")) comparator_4 (
    .a(\总周期数 ), .b(16'h7), .eq(comparator_4_eq));  // open: gt, lt
  or or_1 (W2, IR1_2_q, d_ff_2_q);
  or or_2 (W3, IR1_3_q, d_ff_3_q);
  Hex_Digit_Display hex_digit_display_2 (.value(LedData[27:24]));  // open: dp
  Hex_Digit_Display hex_digit_display_3 (.value(LedData[23:20]));  // open: dp
  or or_3 (or_3_out, comparator_1_eq, comparator_2_eq);
  assign controlled_inverter_1_out = or_3_out ? ~CLK : 1'bz;  // Controlled_Inverter controlled_inverter_1
  assign controlled_inverter_2_out = comparator_3_eq ? ~CLK : 1'bz;  // Controlled_Inverter controlled_inverter_2
  assign controlled_inverter_3_out = comparator_4_eq ? ~CLK : 1'bz;  // Controlled_Inverter controlled_inverter_3
  D_Flip_Flop #(.trigger("rising"), .Pre_Clr_Positions("LEGACY"), .NegatePresetClear("false"), .enable("true"), .NewFFLayout("false")) d_ff_1 (
    .clk(IR1_t), .D(1'b1), .Q(d_ff_1_q), .reset(IR1_q));  // open: Qn, preset, en
  or or_4 (W1, IR1_q, d_ff_1_q);
  D_Flip_Flop #(.trigger("rising"), .Pre_Clr_Positions("LEGACY"), .NegatePresetClear("false"), .enable("true"), .NewFFLayout("false")) d_ff_2 (
    .clk(IR2_t), .D(1'b1), .Q(d_ff_2_q), .reset(IR1_2_q));  // open: Qn, preset, en
  D_Flip_Flop #(.trigger("rising"), .Pre_Clr_Positions("LEGACY"), .NegatePresetClear("false"), .enable("true"), .NewFFLayout("false")) d_ff_3 (
    .clk(IR3_t), .D(1'b1), .Q(d_ff_3_q), .reset(IR1_3_q));  // open: Qn, preset, en
  Hex_Digit_Display hex_digit_display_4 (.value(LedData[15:12]));  // open: dp
  Hex_Digit_Display hex_digit_display_5 (.value(LedData[19:16]));  // open: dp
  Pull_Resistor #(.pull(0)) pull_resistor_1 (.node(controlled_inverter_1_out));
  Pull_Resistor #(.pull(0)) pull_resistor_2 (.node(controlled_inverter_2_out));
  Pull_Resistor #(.pull(0)) pull_resistor_3 (.node(controlled_inverter_3_out));
  or or_5 (or_5_out, d_ff_1_q, IR1_q);
  or or_6 (or_6_out, d_ff_2_q, IR1_2_q);
  or or_7 (or_7_out, d_ff_3_q, IR1_3_q);
  Hex_Digit_Display hex_digit_display_6 (.value(LedData[7:4]));  // open: dp
  Hex_Digit_Display hex_digit_display_7 (.value(LedData[11:8]));  // open: dp
  // Probe on \总周期数 
  Hex_Digit_Display hex_digit_display_8 (.value(LedData[3:0]));  // open: dp
  Multiplexer #(.select(1), .width(32), .disabled("Z"), .enable("false")) multiplexer_1 (
    .in0(PC_4), .in1(adder_2_out), .out(multiplexer_1_out), .sel(or_12_out));
  and and_1 (and_1_out, or_5_out, ~and_2_out);  // AND_Gate
  and and_2 (and_2_out, ERET, IRnow[0], ~IRnow[1]);  // AND_Gate
  and and_3 (and_3_out, or_6_out, ~and_4_out);  // AND_Gate
  and and_4 (and_4_out, ERET, ~IRnow[0], IRnow[1]);  // AND_Gate
  and and_5 (and_5_out, or_7_out, ~and_6_out);  // AND_Gate
  and and_6 (and_6_out, ERET, IRnow[0], IRnow[1]);
  D_Flip_Flop #(.trigger("high"), .Pre_Clr_Positions("LEGACY"), .NegatePresetClear("false"), .enable("true"), .NewFFLayout("false")) d_ff_4 (.Q(d_ff_4_q));  // open: clk, D, Qn, preset, en, reset
  Multiplexer #(.select(2), .width(32), .disabled("Z"), .enable("false")) multiplexer_2 (
    .in0(multiplexer_1_out), .in1({mips_regifile_1_r1, Shamt}), .in2({PC_4[31:28], shifter_1_out}),
    .in3({mips_regifile_1_r1, Shamt}), .out(multiplexer_2_out), .sel(\单周期硬布线控制器_1_jr ));
  Multiplexer #(.select(1), .width(1), .disabled("Z"), .enable("false")) multiplexer_3 (
    .in0(1'b1), .in1(Go), .out(multiplexer_3_out), .sel(and_8_out));
  D_Flip_Flop #(.trigger("rising"), .Pre_Clr_Positions("LEGACY"), .NegatePresetClear("false"), .enable("true"), .NewFFLayout("false")) u_IR1 (
    .clk(CLK), .D(and_1_out), .Q(IR1_q));  // open: Qn, preset, en, reset
  D_Flip_Flop #(.trigger("rising"), .Pre_Clr_Positions("LEGACY"), .NegatePresetClear("false"), .enable("true"), .NewFFLayout("false")) IR1_2 (
    .clk(CLK), .D(and_3_out), .Q(IR1_2_q));  // open: Qn, preset, en, reset
  D_Flip_Flop #(.trigger("rising"), .Pre_Clr_Positions("LEGACY"), .NegatePresetClear("false"), .enable("true"), .NewFFLayout("false")) IR1_3 (
    .clk(CLK), .D(and_5_out), .Q(IR1_3_q));  // open: Qn, preset, en, reset
  or or_8 (IR1_t, IR1, IRA);
  // Probe on 13'h299
  Comparator #(.width(32), .mode("twosComplement")) comparator_5 (
    .a({mips_regifile_1_r1, Shamt}), .b({32{1'b0}}), .gt(comparator_5_gt));  // open: eq, lt
  Multiplexer #(.select(1), .width(32), .disabled("Z"), .enable("false")) multiplexer_4 (
    .in0(multiplexer_2_out), .in1(adder_2_out), .out(PCnext), .sel(and_7_out));
  Register #(.width(32), .trigger("rising"), .Select("low")) u_PC (
    .D(PCin), .en(multiplexer_3_out), .Q(PC_q), .clk(CLK), .clr(1'b0));
  Counter #(.width(16), .max('hffff), .ongoal("wrap"), .trigger("rising"), .behavior("old")) counter_1 (
    .load(1'b0), .count(multiplexer_3_out), .Q(\总周期数 ), .clk(CLK), .clr(1'b0));  // open: D, carry, preset
  or or_9 (IR2_t, IR2, IRB);
  Comparator #(.width(13), .mode("twosComplement")) comparator_6 (
    .a(CNT_num), .b(13'h299), .eq(comparator_6_eq), .lt(comparator_6_lt));  // open: gt
  Clock #(.highDuration(1), .lowDuration(1)) clock_2 (.out(clock_2_out));
  and and_7 (and_7_out, comparator_5_gt, BGTZ);
  Adder #(.width(32)) adder_1 (.a(PC_q), .b(32'h4), .out(PC_4));  // open: cin, cout
  and and_8 (and_8_out, Syscall, NotEqual);
  Priority_Encoder #(.select(2), .disabled("Z")) priority_encoder_1 (
    .in0(1'b1), .in1(IR1_q), .in2(IR1_2_q), .in3(IR1_3_q), .out(priority_encoder_1_out),
    .gs(priority_encoder_1_gs));  // open: en_out, en_in
  nand nand_1 (nand_1_out, d_ff_4_q, comparator_6_eq);
  Counter #(.width(13), .max('h1fff), .ongoal("stay"), .trigger("rising"), .behavior("old")) counter_2 (
    .count(comparator_6_lt), .Q(CNT_num), .clk(clock_2_out));  // open: load, D, carry, clr, preset
  assign PC = PC_q & 32'hffff;  // AND_Gate and_9, 32 bits wide
  Multiplexer #(.select(2), .width(1), .disabled("Z"), .enable("false")) multiplexer_5 (
    .in0(1'b0), .in1(priority_encoder_1_gs), .in2(priority_encoder_1_gs), .in3(priority_encoder_1_gs),
    .out(multiplexer_5_out), .sel(priority_encoder_1_out));
  or or_10 (IR3_t, IR3, IRC);
  assign CLK = nand_1_out ? clock_2_out : 1'bz;  // Controlled_Buffer controlled_buffer_1
  Pull_Resistor #(.pull(1)) pull_resistor_4 (.node(CLK));
  // Mips_Probe mips_probe_1: pin names not known; wires that end beside it: IR
  ROM #(.addrWidth(10), .dataWidth(32), .Select("high")) rom_1 (.addr(PC_q[11:2]), .data(IR));
  Multiplexer #(.select(2), .width(32), .disabled("Z"), .enable("false")) multiplexer_6 (
    .in0(PCnext), .in1(32'h30ac), .in2(32'h3150), .in3(32'h31f4), .out(multiplexer_6_out),
    .sel(priority_encoder_1_out));
  Multiplexer #(.select(1), .width(5), .disabled("Z"), .enable("false")) multiplexer_7 (
    .in0(IR[25:21]), .in1(5'b00010), .out(multiplexer_7_out), .sel(Syscall));
  Multiplexer #(.select(1), .width(32), .disabled("Z"), .enable("false")) multiplexer_8 (
    .in0(PCnext), .in1(multiplexer_6_out), .out(multiplexer_8_out), .sel(and_10_out));
  and and_10 (and_10_out, multiplexer_5_out, ~register_2_q);  // AND_Gate
  Comparator #(.width(6), .mode("twosComplement")) comparator_7 (
    .a(IR[31:26]), .b(6'b010000), .eq(comparator_7_eq));  // open: gt, lt
  Comparator #(.width(6), .mode("twosComplement")) comparator_8 (
    .a(IR[5:0]), .b(6'b011000), .eq(comparator_8_eq));  // open: gt, lt
  \单周期硬布线控制器  \u_单周期硬布线控制器_1  (
    .Func(IR[5:0]), .OP(IR[31:26]), .ALU_OP(AluOP), .MemToReg(MemToReg), .MemWrite(MemWrite),
    .ALU_SRC(AluSrcB), .RegWrite(RegWrite), .SysCALL(Syscall), .SignedExt(SignedExt), .RegDst(RegDst),
    .JR(\单周期硬布线控制器_1_jr [0]), .JMP(\单周期硬布线控制器_1_jr [1]), .Beq(Beq), .JAL(JAL), .Bne(Bne), .LB(LB), .BGTZ(BGTZ));
  Multiplexer #(.select(1), .width(5), .disabled("Z"), .enable("false")) multiplexer_9 (
    .in0(IR[20:16]), .in1(IR[15:11]), .out(multiplexer_9_out), .sel(RegDst));
  assign bit_extender_1_out = {{16{1'b0}}, IR[15:0]};  // Bit_Extender bit_extender_1
  assign bit_extender_2_out = {{16{IR[15]}}, IR[15:0]};  // Bit_Extender bit_extender_2
  Shifter #(.width(28), .shift("ll")) shifter_1 (.in(IR[27:0]), .\dist (5'b00010), .out(shifter_1_out));
  Register #(.width(32), .trigger("rising"), .Select("low")) register_1 (
    .D(PCnext), .en(and_10_out), .Q(register_1_q), .clk(CLK));  // open: clr
  Register #(.width(1), .trigger("rising"), .Select("low")) register_2 (
    .D(1'b1), .en(and_10_out), .Q(register_2_q), .clk(CLK), .clr(ERET));
  and and_11 (ERET, comparator_7_eq, comparator_8_eq);
  Multiplexer #(.select(1), .width(5), .disabled("Z"), .enable("false")) multiplexer_10 (
    .in0(multiplexer_9_out), .in1({5{1'b1}}), .out(multiplexer_10_out), .sel(JAL));
  Multiplexer #(.select(1), .width(32), .disabled("Z"), .enable("false")) multiplexer_11 (
    .in0(bit_extender_1_out), .in1(bit_extender_2_out), .out(multiplexer_11_out), .sel(SignedExt));
  Multiplexer #(.select(1), .width(32), .disabled("Z"), .enable("false")) multiplexer_12 (
    .in0(multiplexer_8_out), .in1(register_1_q), .out(PCin), .sel(ERET));
  Multiplexer #(.select(1), .width(2), .disabled("Z"), .enable("false")) multiplexer_13 (
    .in0(priority_encoder_1_out), .in1(2'b00), .out(multiplexer_13_out), .sel(ERET));
  or or_11 (or_11_out, and_10_out, ERET);
  Multiplexer #(.select(1), .width(5), .disabled("Z"), .enable("false")) multiplexer_14 (
    .in0(IR[20:16]), .in1(5'b00100), .out(multiplexer_14_out), .sel(Syscall));
  Shifter #(.width(32), .shift("ll")) shifter_2 (.in(multiplexer_11_out), .\dist (5'b00010), .out(shifter_2_out));
  Adder #(.width(32)) adder_2 (.a(shifter_2_out), .b(PC_4), .out(adder_2_out));  // open: cin, cout
  Register #(.width(2), .trigger("rising"), .Select("low")) register_3 (
    .D(multiplexer_13_out), .en(or_11_out), .Q(IRnow), .clk(CLK));  // open: clr
  MIPS_Regifile mips_regifile_1 (
    .Din(RDin), .Clk(CLK), .R1({mips_regifile_1_r1, Shamt}), .R2(MDin), .WE(RegWrite),
    .W_num(multiplexer_10_out), .R1_num(multiplexer_7_out), .R2_num(multiplexer_14_out));
  or or_12 (or_12_out, and_13_out, and_12_out);
  and and_12 (and_12_out, Beq, mips_alu_1_equal);
  Multiplexer #(.select(1), .width(32), .disabled("Z"), .enable("false")) multiplexer_15 (
    .in0(MDin), .in1(multiplexer_11_out), .out(multiplexer_15_out), .sel(AluSrcB));
  Comparator #(.width(6), .mode("twosComplement")) comparator_9 (
    .a(IR[31:26]), .b({6{1'b0}}), .eq(comparator_9_eq));  // open: gt, lt
  Comparator #(.width(6), .mode("twosComplement")) comparator_10 (
    .a(IR[5:0]), .b(6'b000100), .eq(comparator_10_eq));  // open: gt, lt
  not not_1 (NotEqual, mips_alu_1_equal);
  and and_13 (and_13_out, Bne, not_2_out);
  not not_2 (not_2_out, mips_alu_1_equal);
  Multiplexer #(.select(1), .width(32), .disabled("Z"), .enable("false")) multiplexer_16 (
    .in0(multiplexer_15_out), .in1(32'h22), .out(multiplexer_16_out), .sel(Syscall));
  Multiplexer #(.select(1), .width(5), .disabled("Z"), .enable("false")) multiplexer_17 (
    .in0(IR[10:6]), .in1(Shamt), .out(multiplexer_17_out), .sel(and_14_out));
  and and_14 (and_14_out, comparator_9_eq, comparator_10_eq);
  and and_15 (and_15_out, mips_alu_1_equal, Syscall);
  MIPS_ALU mips_alu_1 (
    .X({mips_regifile_1_r1, Shamt}), .Y(multiplexer_16_out), .AluOP(AluOP), .Equal(mips_alu_1_equal),
    .Result({mips_alu_1_result_3, mips_alu_1_result_2, mips_alu_1_result}), .shamt(multiplexer_17_out));  // open: Result_2
  Multiplexer #(.select(1), .width(32), .disabled("Z"), .enable("false")) multiplexer_18 (
    .in0(multiplexer_19_out), .in1(PC_4), .out(RDin), .sel(JAL));
  Register #(.width(32), .trigger("rising"), .Select("low")) register_4 (
    .D(MDin), .en(and_15_out), .Q(LedData), .clk(CLK), .clr(1'b0));
  Multiplexer #(.select(1), .width(32), .disabled("Z"), .enable("false")) multiplexer_19 (
    .in0(multiplexer_20_out), .in1(bit_extender_3_out), .out(multiplexer_19_out), .sel(LB));
  RAM #(.addrWidth(10), .dataWidth(32), .bus("separate"), .Select("high")) ram_1 (
    .addr(mips_alu_1_result_2), .din(MDin), .data(ram_1_data), .str(MemWrite), .clk(CLK), .clr(1'b0));  // open: sel, ld
  Multiplexer #(.select(1), .width(32), .disabled("Z"), .enable("false")) multiplexer_20 (
    .in0({mips_alu_1_result_3, mips_alu_1_result_2, mips_alu_1_result}), .in1(ram_1_data),
    .out(multiplexer_20_out), .sel(MemToReg));
  Multiplexer #(.select(2), .width(8), .disabled("Z"), .enable("false")) multiplexer_21 (
    .in0(multiplexer_20_out[7:0]), .in1(multiplexer_20_out[15:8]), .in2(multiplexer_20_out[23:16]),
    .in3(multiplexer_20_out[31:24]), .out(multiplexer_21_out), .sel(mips_alu_1_result));
  assign bit_extender_3_out = {{24{multiplexer_21_out[7]}}, multiplexer_21_out};  // Bit_Extender bit_extender_3

  // Notes on the sheet:
  //   中断源
  //   中断等待指示
  //   总复位信号应将除ROM以外所有存储组件全部清零
  //   单级中断测试信号模拟器
  //   数码管输出
  //   数码管输出应该用寄存器锁存，否则显示数据只能一闪而过
  //   控制位
  //   暂停节拍，不能为0
  //   Reset 
  //   Reset 
  //   Reset 
  //   用这个时钟源需要去掉电路中的其他时钟源
  //   戳工具置1进入计数暂停模式，ctrl+k时钟自动运行到对应节拍暂停
  //   ctrl+k关闭时钟连续运行，将控制位置零，进入单步调试模式调试
  //   可计数暂停的时钟源
  //   指令字
  //   contents of rom_1 (hex, n*v repeats v):
  //   201d07d0 20100001 109fc0 139fc3 8021 2012000c 24160008 26100001 3210000f 20080008 20090001 139900
  //   2709825 132020 20020022 c 1094022 1500fff9 22100001 2018000f 2188024 108700 20080008 20090001 139902
  //   2709825 132021 20020022 c 1094022 1500fff9 108702 2c9b022 12c00001 8000c07 4020 1084027 84400
  //   3508ffff 82021 20020022 c 8000c01 afa20000 23bd0004 afa40000 23bd0004 afb00000 23bd0004 afb30000
  //   23bd0004 afb40000 23bd0004 afb50000 23bd0004 afb60000 23bd0004 20160001 20140003 20150001 168020
  //   108100 2149825 132020 20020022 c 1600fffa 295a022 1680fff7 23bdfffc 8fb60000 23bdfffc 8fb50000
  //   23bdfffc 8fb40000 23bdfffc 8fb30000 23bdfffc 8fb00000 23bdfffc 8fa40000 23bdfffc 8fa20000 42000018
  //   afa20000 23bd0004 afa40000 23bd0004 afb00000 23bd0004 afb30000 23bd0004 afb40000 23bd0004 afb50000
  //   23bd0004 afb60000 23bd0004 20160002 20140003 20150001 168020 108100 2149825 132020 20020022 c
  //   1600fffa 295a022 1680fff7 23bdfffc 8fb60000 23bdfffc 8fb50000 23bdfffc 8fb40000 23bdfffc 8fb30000
  //   23bdfffc 8fb00000 23bdfffc 8fa40000 23bdfffc 8fa20000 42000018 afa20000 23bd0004 afa40000 23bd0004
  //   afb00000 23bd0004 afb30000 23bd0004 afb40000 23bd0004 afb50000 23bd0004 afb60000 23bd0004 20160003
  //   20140003 20150001 168020 108100 2149825 132020 20020022 c 1600fffa 295a022 1680fff7 23bdfffc
  //   8fb60000 23bdfffc 8fb50000 23bdfffc 8fb40000 23bdfffc 8fb30000 23bdfffc 8fb00000 23bdfffc 8fa40000
  //   23bdfffc 8fa20000 42000018
  //   OP
  //   Func
  //   rs
  //   rt
  //   rd
  //   JMP
  //   JR
  //   LB
  //   BGTZ
  //   OP
  //   Func
  //   Syscall
  //   为方便自动评测，需要输出PC，IR，寄存器堆写如数据RDin
  //   Beq
  //   Bne
  //   MemToReg
  //   MemWrite
  //   AluOP
  //   AluSrcB
  //   RegWrite
  //   JAL
  //   RegDst
  //   RAM写使能MemWrite、RAM写入数据MDin等信号
endmodule

module \单周期MIPS_多级中断  (
  input  IR1,
  input  IR2,
  input  IR3,
  output RegWrite,
  output MemWrite,
  output [31:0] PC,
  output [31:0] IR,
  output [31:0] RDin,
  output [31:0] MDin,
  output [31:0] LedData
);

  wire AluSrcB, and_4_out, and_5_out, and_6_out, and_7_out, and_8_out, and_9_out, and_10_out, and_11_out,
       and_13_out, and_14_out, and_15_out, and_16_out, and_17_out, and_18_out, and_19_out, and_21_out,
       and_22_out, Beq, BGTZ, Bne, CLK, clock_2_out, comparator_1_eq, comparator_2_eq, comparator_3_eq,
       comparator_4_eq, comparator_5_eq, comparator_6_eq, comparator_7_eq, comparator_8_eq, comparator_9_eq,
       comparator_10_gt, comparator_11_eq, comparator_11_lt, comparator_12_eq, comparator_13_eq,
       comparator_14_eq, comparator_15_eq, comparator_16_gt, comparator_17_eq, comparator_18_eq, d_ff_1_q,
       d_ff_2_q, d_ff_3_q, d_ff_4_q, d_ff_5_q, d_ff_5_qn, decoder_1_out1, decoder_1_out2, decoder_1_out3,
       ERET, Go, IEin, INT, IR1_2_q, IR1_3_q, IR1_q, IR1_t, IR2_t, IR3_t, IRA, IRB, IRC, JAL, LB, MemToReg,
       MFC0, mips_alu_1_equal, MTC0, multiplexer_3_out, multiplexer_11_out, nand_1_out, not_2_out, NotEqual,
       or_4_out, or_5_out, or_6_out, or_7_out, or_8_out, or_13_out, or_14_out, or_15_out,
       priority_encoder_1_gs, priority_encoder_2_out, priority_encoder_3_out, pull_resistor_1_node,
       pull_resistor_2_node, pull_resistor_3_node, pull_resistor_5_node, RegDst, SignedExt, Syscall, W1, W2,
       W3, \单周期硬布线控制器_1_regwrite ;
  wire [1:0] IRnow, priority_encoder_1_out, \单周期硬布线控制器_1_jr ;
  wire [1:1] IEdell;
  wire [3:0] AluOP;
  wire [4:0] multiplexer_5_out, multiplexer_6_out, multiplexer_8_out, multiplexer_9_out, multiplexer_14_out,
       Shamt;
  wire [7:0] multiplexer_20_out, multiplexer_20_out_3, multiplexer_21_out;
  wire [12:0] CNT_num;
  wire [15:0] \总周期数 ;
  wire [23:8] multiplexer_20_out_2;
  wire [27:0] shifter_1_out;
  wire [31:0] adder_2_out, bit_extender_1_out, bit_extender_2_out, bit_extender_3_out, demultiplexer_1_out0,
       mips_alu_1_result, multiplexer_1_out, multiplexer_2_out, multiplexer_7_out, multiplexer_10_out,
       multiplexer_12_out, multiplexer_13_out, multiplexer_16_out, multiplexer_17_out, multiplexer_18_out,
       multiplexer_19_out, multiplexer_23_out, PC_4, PC_q, PCin, PCnext, ram_1_data, register_2_q,
       shifter_2_out, SiteData;
  wire [31:1] demultiplexer_1_out1;
  wire [31:5] mips_regifile_1_r1;

  Clock #(.highDuration(1), .lowDuration(1)) clock_1 ();  // open: out
  Button _1 (.out(IRA));
  Button _2 (.out(IRB));
  Button _3 (.out(IRC));
  Button \u_继续运行  (.out(Go));
  LED #(.active("true")) led_1 (.in(W1));
  LED #(.active("true")) led_2 (.in(W2));
  LED #(.active("true")) led_3 (.in(W3));
  Comparator #(.width(5), .mode("twosComplement")) comparator_1 (
    .a(IR[25:21]), .b({5{1'b0}}), .eq(comparator_1_eq));  // open: gt, lt
  Comparator #(.width(5), .mode("twosComplement")) comparator_2 (
    .a(IR[25:21]), .b(5'b00100), .eq(comparator_2_eq));  // open: gt, lt
  Hex_Digit_Display hex_digit_display_1 (.value(LedData[31:28]));  // open: dp
  Comparator #(.width(16), .mode("twosComplement")) comparator_3 (
    .a(\总周期数 ), .b(16'h7), .eq(comparator_3_eq));  // open: gt, lt
  Comparator #(.width(16), .mode("twosComplement")) comparator_4 (
    .a(\总周期数 ), .b(16'h241), .eq(comparator_4_eq));  // open: gt, lt
  Comparator #(.width(6), .mode("twosComplement")) comparator_5 (
    .a(IR[31:26]), .b(6'b010000), .eq(comparator_5_eq));  // open: gt, lt
  Comparator #(.width(6), .mode("twosComplement")) comparator_6 (
    .a(IR[5:0]), .b(6'b011000), .eq(comparator_6_eq));  // open: gt, lt
  and and_1 (MFC0, comparator_1_eq, comparator_5_eq);
  and and_2 (MTC0, comparator_2_eq, comparator_5_eq);
  or or_1 (W1, IR1_q, d_ff_1_q);
  or or_2 (W2, IR1_2_q, d_ff_2_q);
  or or_3 (W3, IR1_3_q, d_ff_3_q);
  Hex_Digit_Display hex_digit_display_2 (.value(LedData[23:20]));  // open: dp
  Hex_Digit_Display hex_digit_display_3 (.value(LedData[27:24]));  // open: dp
  Comparator #(.width(16), .mode("twosComplement")) comparator_7 (
    .a(16'h258), .b(\总周期数 ), .eq(comparator_7_eq));  // open: gt, lt
  or or_4 (or_4_out, comparator_7_eq, comparator_8_eq);
  Comparator #(.width(16), .mode("twosComplement")) comparator_8 (
    .a(\总周期数 ), .b(16'h1), .eq(comparator_8_eq));  // open: gt, lt
  Comparator #(.width(16), .mode("twosComplement")) comparator_9 (
    .a(\总周期数 ), .b(16'h4), .eq(comparator_9_eq));  // open: gt, lt
  or or_5 (or_5_out, comparator_3_eq, comparator_4_eq);
  and and_3 (ERET, comparator_5_eq, comparator_6_eq);
  D_Flip_Flop #(.trigger("rising"), .Pre_Clr_Positions("LEGACY"), .NegatePresetClear("false"), .enable("true"), .NewFFLayout("false")) d_ff_1 (
    .clk(IR1_t), .D(1'b1), .Q(d_ff_1_q), .reset(IR1_q));  // open: Qn, preset, en
  D_Flip_Flop #(.trigger("rising"), .Pre_Clr_Positions("LEGACY"), .NegatePresetClear("false"), .enable("true"), .NewFFLayout("false")) d_ff_2 (
    .clk(IR2_t), .D(1'b1), .Q(d_ff_2_q), .reset(IR1_2_q));  // open: Qn, preset, en
  D_Flip_Flop #(.trigger("rising"), .Pre_Clr_Positions("LEGACY"), .NegatePresetClear("false"), .enable("true"), .NewFFLayout("false")) d_ff_3 (
    .clk(IR3_t), .D(1'b1), .Q(d_ff_3_q), .reset(IR1_3_q));  // open: Qn, preset, en
  Decoder #(.select(2), .tristate("false"), .disabled("Z"), .enable("false")) decoder_1 (
    .out1(decoder_1_out1), .out2(decoder_1_out2), .out3(decoder_1_out3), .sel(IRnow));  // open: out0
  Hex_Digit_Display hex_digit_display_4 (.value(LedData[19:16]));  // open: dp
  Hex_Digit_Display hex_digit_display_5 (.value(LedData[15:12]));  // open: dp
  Pull_Resistor #(.pull(0)) pull_resistor_1 (.node(pull_resistor_1_node));
  assign pull_resistor_1_node = or_4_out ? ~CLK : 1'bz;  // Controlled_Inverter controlled_inverter_1
  Pull_Resistor #(.pull(0)) pull_resistor_2 (.node(pull_resistor_2_node));
  assign pull_resistor_2_node = comparator_9_eq ? ~CLK : 1'bz;  // Controlled_Inverter controlled_inverter_2
  Pull_Resistor #(.pull(0)) pull_resistor_3 (.node(pull_resistor_3_node));
  assign pull_resistor_3_node = or_5_out ? ~CLK : 1'bz;  // Controlled_Inverter controlled_inverter_3
  or or_6 (or_6_out, d_ff_1_q, IR1_q);
  or or_7 (or_7_out, d_ff_2_q, IR1_2_q);
  or or_8 (or_8_out, d_ff_3_q, IR1_3_q);
  Hex_Digit_Display hex_digit_display_6 (.value(LedData[11:8]));  // open: dp
  Hex_Digit_Display hex_digit_display_7 (.value(LedData[7:4]));  // open: dp
  // Probe on \总周期数 
  Multiplexer #(.select(1), .width(32), .disabled("Z"), .enable("false")) multiplexer_1 (
    .in0(PC_4), .in1(adder_2_out), .out(multiplexer_1_out), .sel(or_13_out));
  and and_4 (and_4_out, decoder_1_out1, ERET);
  and and_5 (and_5_out, decoder_1_out2, ERET);
  and and_6 (and_6_out, decoder_1_out3, ERET);
  Hex_Digit_Display hex_digit_display_8 (.value(LedData[3:0]));  // open: dp
  D_Flip_Flop #(.trigger("high"), .Pre_Clr_Positions("LEGACY"), .NegatePresetClear("false"), .enable("true"), .NewFFLayout("false")) d_ff_4 (.Q(d_ff_4_q));  // open: clk, D, Qn, preset, en, reset
  // Probe on 13'h16
  Multiplexer #(.select(2), .width(32), .disabled("Z"), .enable("false")) multiplexer_2 (
    .in0(multiplexer_1_out), .in1({mips_regifile_1_r1, Shamt}), .in2({PC_4[31:28], shifter_1_out}),
    .in3({mips_regifile_1_r1, Shamt}), .out(multiplexer_2_out), .sel(\单周期硬布线控制器_1_jr ));
  Multiplexer #(.select(1), .width(1), .disabled("Z"), .enable("false")) multiplexer_3 (
    .in0(1'b1), .in1(Go), .out(multiplexer_3_out), .sel(and_10_out));
  and and_7 (and_7_out, or_6_out, ~and_4_out);  // AND_Gate
  and and_8 (and_8_out, or_7_out, ~and_5_out);  // AND_Gate
  and and_9 (and_9_out, or_8_out, ~and_6_out);  // AND_Gate
  Clock #(.highDuration(1), .lowDuration(1)) clock_2 (.out(clock_2_out));
  Comparator #(.width(32), .mode("twosComplement")) comparator_10 (
    .a({mips_regifile_1_r1, Shamt}), .b({32{1'b0}}), .gt(comparator_10_gt));  // open: eq, lt
  Multiplexer #(.select(1), .width(32), .disabled("Z"), .enable("false")) multiplexer_4 (
    .in0(multiplexer_2_out), .in1(adder_2_out), .out(PCnext), .sel(and_11_out));
  Register #(.width(32), .trigger("rising"), .Select("low")) u_PC (
    .D(PCin), .en(multiplexer_3_out), .Q(PC_q), .clk(CLK), .clr(1'b0));
  Counter #(.width(16), .max('hffff), .ongoal("wrap"), .trigger("rising"), .behavior("old")) counter_1 (
    .load(1'b0), .count(multiplexer_3_out), .Q(\总周期数 ), .clk(CLK), .clr(1'b0));  // open: D, carry, preset
  and and_10 (and_10_out, Syscall, NotEqual);
  D_Flip_Flop #(.trigger("rising"), .Pre_Clr_Positions("LEGACY"), .NegatePresetClear("false"), .enable("true"), .NewFFLayout("false")) u_IR1 (
    .clk(CLK), .D(and_7_out), .Q(IR1_q));  // open: Qn, preset, en, reset
  D_Flip_Flop #(.trigger("rising"), .Pre_Clr_Positions("LEGACY"), .NegatePresetClear("false"), .enable("true"), .NewFFLayout("false")) IR1_2 (
    .clk(CLK), .D(and_8_out), .Q(IR1_2_q));  // open: Qn, preset, en, reset
  D_Flip_Flop #(.trigger("rising"), .Pre_Clr_Positions("LEGACY"), .NegatePresetClear("false"), .enable("true"), .NewFFLayout("false")) IR1_3 (
    .clk(CLK), .D(and_9_out), .Q(IR1_3_q));  // open: Qn, preset, en, reset
  or or_9 (IR1_t, IR1, IRA);
  Comparator #(.width(13), .mode("twosComplement")) comparator_11 (
    .a(CNT_num), .b(13'h16), .eq(comparator_11_eq), .lt(comparator_11_lt));  // open: gt
  and and_11 (and_11_out, comparator_10_gt, BGTZ);
  assign PC = PC_q & 32'hffff;  // AND_Gate and_12, 32 bits wide
  Adder #(.width(32)) adder_1 (.a(PC_q), .b(32'h4), .out(PC_4));  // open: cin, cout
  or or_10 (IR2_t, IR2, IRB);
  nand nand_1 (nand_1_out, d_ff_4_q, comparator_11_eq);
  Counter #(.width(13), .max('h1fff), .ongoal("stay"), .trigger("rising"), .behavior("old")) counter_2 (
    .count(comparator_11_lt), .Q(CNT_num), .clk(clock_2_out));  // open: load, D, carry, clr, preset
  ROM #(.addrWidth(10), .dataWidth(32), .Select("high")) rom_1 (.addr(PC_q[11:2]), .data(IR));
  assign CLK = nand_1_out ? clock_2_out : 1'bz;  // Controlled_Buffer controlled_buffer_1
  Pull_Resistor #(.pull(1)) pull_resistor_4 (.node(CLK));
  // Mips_Probe mips_probe_1: pin names not known; wires that end beside it: IR
  Priority_Encoder #(.select(2), .disabled("Z")) priority_encoder_1 (
    .in0(1'b0), .in1(IR1_q), .in2(IR1_2_q), .in3(IR1_3_q), .out(priority_encoder_1_out),
    .gs(priority_encoder_1_gs));  // open: en_out, en_in
  or or_11 (IR3_t, IR3, IRC);
  Multiplexer #(.select(1), .width(5), .disabled("Z"), .enable("false")) multiplexer_5 (
    .in0(IR[25:21]), .in1(5'b00010), .out(multiplexer_5_out), .sel(Syscall));
  assign bit_extender_1_out = {{16{1'b0}}, IR[15:0]};  // Bit_Extender bit_extender_1
  assign bit_extender_2_out = {{16{IR[15]}}, IR[15:0]};  // Bit_Extender bit_extender_2
  Shifter #(.width(28), .shift("ll")) shifter_1 (.in(IR[27:0]), .\dist (5'b00010), .out(shifter_1_out));
  stack stack_1 (.INPUT(priority_encoder_1_out), .clk(CLK), .\int (INT), .eret(ERET), .out_5(IRnow));
  Comparator #(.width(5), .mode("twosComplement")) comparator_12 (
    .a(IR[15:11]), .b(5'b01110), .eq(comparator_12_eq));  // open: gt, lt
  Comparator #(.width(5), .mode("twosComplement")) comparator_13 (
    .a(IR[15:11]), .b(5'b01100), .eq(comparator_13_eq));  // open: gt, lt
  \单周期硬布线控制器  \u_单周期硬布线控制器_1  (
    .Func(IR[5:0]), .OP(IR[31:26]), .ALU_OP(AluOP), .MemToReg(MemToReg), .MemWrite(MemWrite),
    .ALU_SRC(AluSrcB), .RegWrite(\单周期硬布线控制器_1_regwrite ), .SysCALL(Syscall), .SignedExt(SignedExt),
    .RegDst(RegDst), .JR(\单周期硬布线控制器_1_jr [0]), .JMP(\单周期硬布线控制器_1_jr [1]), .Beq(Beq), .JAL(JAL), .Bne(Bne),
    .LB(LB), .BGTZ(BGTZ));
  Multiplexer #(.select(1), .width(5), .disabled("Z"), .enable("false")) multiplexer_6 (
    .in0(IR[20:16]), .in1(IR[15:11]), .out(multiplexer_6_out), .sel(RegDst));
  Multiplexer #(.select(1), .width(32), .disabled("Z"), .enable("false")) multiplexer_7 (
    .in0(bit_extender_1_out), .in1(bit_extender_2_out), .out(multiplexer_7_out), .sel(SignedExt));
  and and_13 (and_13_out, comparator_12_eq, MTC0);
  and and_14 (and_14_out, comparator_13_eq, MTC0);
  Multiplexer #(.select(1), .width(5), .disabled("Z"), .enable("false")) multiplexer_8 (
    .in0(IR[20:16]), .in1(5'b00100), .out(multiplexer_8_out), .sel(Syscall));
  Multiplexer #(.select(1), .width(5), .disabled("Z"), .enable("false")) multiplexer_9 (
    .in0(multiplexer_6_out), .in1({5{1'b1}}), .out(multiplexer_9_out), .sel(JAL));
  Shifter #(.width(32), .shift("ll")) shifter_2 (.in(multiplexer_7_out), .\dist (5'b00010), .out(shifter_2_out));
  Priority_Encoder #(.select(1), .disabled("Z")) priority_encoder_2 (
    .in0(and_13_out), .in1(and_14_out), .out(priority_encoder_2_out));  // open: gs, en_out, en_in
  or or_12 (RegWrite, MFC0, \单周期硬布线控制器_1_regwrite );
  Adder #(.width(32)) adder_2 (.a(shifter_2_out), .b(PC_4), .out(adder_2_out));  // open: cin, cout
  Pull_Resistor #(.pull(0)) pull_resistor_5 (.node(pull_resistor_5_node));
  Decoder #(.select(1), .tristate("false"), .disabled("Z"), .enable("false")) decoder_2 (
    .out0(pull_resistor_5_node), .out1(IEdell[1]), .sel(priority_encoder_2_out));
  Demultiplexer #(.select(1), .width(32), .tristate("false"), .disabled("Z"), .enable("false")) demultiplexer_1 (
    .out0(demultiplexer_1_out0), .out1({demultiplexer_1_out1, IEin}), .in(MDin), .sel(priority_encoder_2_out));
  or or_13 (or_13_out, and_16_out, and_15_out);
  MIPS_Regifile mips_regifile_1 (
    .Din(RDin), .Clk(CLK), .R1({mips_regifile_1_r1, Shamt}), .R2(MDin), .WE(RegWrite),
    .W_num(multiplexer_9_out), .R1_num(multiplexer_5_out), .R2_num(multiplexer_8_out));
  Multiplexer #(.select(2), .width(32), .disabled("Z"), .enable("false")) multiplexer_10 (
    .in1(32'h30ac), .in2(32'h3174), .in3(32'h323c), .out(multiplexer_10_out), .sel(priority_encoder_1_out));  // open: in0
  Multiplexer #(.select(2), .width(1), .disabled("Z"), .enable("false")) multiplexer_11 (
    .in0(1'b1), .in1(1'b0), .in2(IEin), .out(multiplexer_11_out), .sel({IEdell[1], ERET}));  // open: in3
  Pull_Resistor #(.pull(0)) pull_resistor_6 (.node(IEdell[1]));
  Pull_Resistor #(.pull(0)) pull_resistor_7 (.node(IEin));
  and and_15 (and_15_out, Beq, mips_alu_1_equal);
  Multiplexer #(.select(1), .width(32), .disabled("Z"), .enable("false")) multiplexer_12 (
    .in0(MDin), .in1(multiplexer_7_out), .out(multiplexer_12_out), .sel(AluSrcB));
  Comparator #(.width(6), .mode("twosComplement")) comparator_14 (
    .a(IR[31:26]), .b({6{1'b0}}), .eq(comparator_14_eq));  // open: gt, lt
  Comparator #(.width(6), .mode("twosComplement")) comparator_15 (
    .a(IR[5:0]), .b(6'b000100), .eq(comparator_15_eq));  // open: gt, lt
  Comparator #(.width(2), .mode("unsigned")) comparator_16 (
    .a(priority_encoder_1_out), .b(IRnow), .gt(comparator_16_gt));  // open: eq, lt
  D_Flip_Flop #(.trigger("rising"), .Pre_Clr_Positions("LEGACY"), .NegatePresetClear("false"), .enable("true"), .NewFFLayout("false")) d_ff_5 (
    .clk(CLK), .D(multiplexer_11_out), .Q(d_ff_5_q), .Qn(d_ff_5_qn), .en(or_14_out));  // open: preset, reset
  or or_14 (or_14_out, IEdell[1], INT, ERET);
  not not_1 (NotEqual, mips_alu_1_equal);
  and and_16 (and_16_out, Bne, not_2_out);
  not not_2 (not_2_out, mips_alu_1_equal);
  Multiplexer #(.select(1), .width(32), .disabled("Z"), .enable("false")) multiplexer_13 (
    .in0(multiplexer_12_out), .in1(32'h22), .out(multiplexer_13_out), .sel(Syscall));
  Multiplexer #(.select(1), .width(5), .disabled("Z"), .enable("false")) multiplexer_14 (
    .in0(IR[10:6]), .in1(Shamt), .out(multiplexer_14_out), .sel(and_17_out));
  and and_17 (and_17_out, comparator_14_eq, comparator_15_eq);
  and and_18 (and_18_out, priority_encoder_1_gs, d_ff_5_qn);
  and and_19 (and_19_out, mips_alu_1_equal, Syscall);
  MIPS_ALU mips_alu_1 (
    .X({mips_regifile_1_r1, Shamt}), .Y(multiplexer_13_out), .AluOP(AluOP), .Equal(mips_alu_1_equal),
    .Result(mips_alu_1_result), .shamt(multiplexer_14_out));  // open: Result_2
  Multiplexer #(.select(1), .width(32), .disabled("Z"), .enable("false")) multiplexer_15 (
    .in0(multiplexer_17_out), .in1(SiteData), .out(RDin), .sel(MFC0));
  and and_20 (INT, comparator_16_gt, and_18_out);
  Multiplexer #(.select(1), .width(32), .disabled("Z"), .enable("false")) multiplexer_16 (
    .in0(PCnext), .in1(demultiplexer_1_out0), .out(multiplexer_16_out), .sel(pull_resistor_5_node));
  Multiplexer #(.select(1), .width(32), .disabled("Z"), .enable("false")) multiplexer_17 (
    .in0(multiplexer_19_out), .in1(PC_4), .out(multiplexer_17_out), .sel(JAL));
  Multiplexer #(.select(1), .width(32), .disabled("Z"), .enable("false")) multiplexer_18 (
    .in0(PCnext), .in1(multiplexer_10_out), .out(multiplexer_18_out), .sel(INT));
  or or_15 (or_15_out, INT, pull_resistor_5_node);
  Comparator #(.width(5), .mode("twosComplement")) comparator_17 (
    .a(IR[15:11]), .b(5'b01110), .eq(comparator_17_eq));  // open: gt, lt
  Comparator #(.width(5), .mode("twosComplement")) comparator_18 (
    .a(IR[15:11]), .b(5'b01100), .eq(comparator_18_eq));  // open: gt, lt
  Register #(.width(32), .trigger("rising"), .Select("low")) register_1 (
    .D(MDin), .en(and_19_out), .Q(LedData), .clk(CLK), .clr(1'b0));
  Multiplexer #(.select(1), .width(32), .disabled("Z"), .enable("false")) multiplexer_19 (
    .in0({multiplexer_20_out_3, multiplexer_20_out_2, multiplexer_20_out}), .in1(bit_extender_3_out),
    .out(multiplexer_19_out), .sel(LB));
  Register #(.width(32), .trigger("rising"), .Select("low")) register_2 (
    .D(multiplexer_16_out), .en(or_15_out), .Q(register_2_q), .clk(CLK));  // open: clr
  Multiplexer #(.select(1), .width(32), .disabled("Z"), .enable("false")) multiplexer_20 (
    .in0(mips_alu_1_result), .in1(ram_1_data),
    .out({multiplexer_20_out_3, multiplexer_20_out_2, multiplexer_20_out}), .sel(MemToReg));
  RAM #(.addrWidth(10), .dataWidth(32), .bus("separate"), .Select("high")) ram_1 (
    .addr(mips_alu_1_result[11:2]), .din(MDin), .data(ram_1_data), .str(MemWrite), .clk(CLK), .clr(1'b0));  // open: sel, ld
  and and_21 (and_21_out, comparator_17_eq, MFC0);
  and and_22 (and_22_out, comparator_18_eq, MFC0);
  Multiplexer #(.select(2), .width(8), .disabled("Z"), .enable("false")) multiplexer_21 (
    .in0(multiplexer_20_out), .in1(multiplexer_20_out_2[15:8]), .in2(multiplexer_20_out_2[23:16]),
    .in3(multiplexer_20_out_3), .out(multiplexer_21_out), .sel(mips_alu_1_result[1:0]));
  assign bit_extender_3_out = {{24{multiplexer_21_out[7]}}, multiplexer_21_out};  // Bit_Extender bit_extender_3
  Multiplexer #(.select(1), .width(32), .disabled("Z"), .enable("false")) multiplexer_22 (
    .in0(multiplexer_18_out), .in1(register_2_q), .out(PCin), .sel(ERET));
  Multiplexer #(.select(1), .width(32), .disabled("Z"), .enable("false")) multiplexer_23 (
    .in0({32{1'b0}}), .in1(32'h1), .out(multiplexer_23_out), .sel(d_ff_5_q));
  Priority_Encoder #(.select(1), .disabled("Z")) priority_encoder_3 (
    .in0(and_21_out), .in1(and_22_out), .out(priority_encoder_3_out));  // open: gs, en_out, en_in
  Multiplexer #(.select(1), .width(32), .disabled("Z"), .enable("false")) multiplexer_24 (
    .in0(register_2_q), .in1(multiplexer_23_out), .out(SiteData), .sel(priority_encoder_3_out));

  // Other names for the same wires on the sheet: IEdell[0] = ERET; Func[5:0] = IR[5:0]; RD[4:0] = IR[15:11];
  //   MF[4:0] = IR[25:21]; OP[5:0] = IR[31:26]; R2[31:0] = MDin

  // Notes on the sheet:
  //   中断源
  //   中断等待指示
  //   总复位信号应将除ROM以外所有存储组件全部清零
  //   多级中断测试信号模拟器
  //   数码管输出
  //   数码管输出应该用寄存器锁存，否则显示数据只能一闪而过
  //   控制位
  //   暂停节拍，不能为0
  //   Reset 
  //   Reset 
  //   Reset 
  //   戳工具置1进入计数暂停模式，ctrl+k时钟自动运行到对应节拍暂停
  //   ctrl+k关闭时钟连续运行，将控制位置零，进入单步调试模式调试
  //   用这个时钟源需要去掉电路中的其他时钟源
  //   指令存储器
  //   contents of rom_1 (hex, n*v repeats v):
  //   201d07d0 20100001 109fc0 139fc3 8021 2012000c 24160008 26100001 3210000f 20080008 20090001 139900
  //   2709825 132020 20020022 c 1094022 1500fff9 22100001 2018000f 2188024 108700 20080008 20090001 139902
  //   2709825 132021 20020022 c 1094022 1500fff9 108702 2c9b022 12c00001 8000c07 4020 1084027 84400
  //   3508ffff 82021 20020022 c 8000c01 afa20000 23bd0004 afa40000 23bd0004 afb00000 23bd0004 afb30000
  //   23bd0004 afb40000 23bd0004 afb50000 23bd0004 afb60000 23bd0004 40167000 afb60000 23bd0004 40806000
  //   20160001 20140003 20150001 168020 108100 2149825 132020 20020022 c 1600fffa 295a022 1680fff7
  //   20160001 40966000 23bdfffc 8fb60000 40967000 23bdfffc 8fb60000 23bdfffc 8fb50000 23bdfffc 8fb40000
  //   23bdfffc 8fb30000 23bdfffc 8fb00000 23bdfffc 8fa40000 23bdfffc 8fa20000 42000018 afa20000 23bd0004
  //   afa40000 23bd0004 afb00000 23bd0004 afb30000 23bd0004 afb40000 23bd0004 afb50000 23bd0004 afb60000
  //   23bd0004 40167000 afb60000 23bd0004 40806000 20160002 20140003 20150001 168020 108100 2149825 132020
  //   20020022 c 1600fffa 295a022 1680fff7 20160001 40966000 23bdfffc 8fb60000 40967000 23bdfffc 8fb60000
  //   23bdfffc 8fb50000 23bdfffc 8fb40000 23bdfffc 8fb30000 23bdfffc 8fb00000 23bdfffc 8fa40000 23bdfffc
  //   8fa20000 42000018 afa20000 23bd0004 afa40000 23bd0004 afb00000 23bd0004 afb30000 23bd0004 afb40000
  //   23bd0004 afb50000 23bd0004 afb60000 23bd0004 40167000 afb60000 23bd0004 40806000 20160003 20140003
  //   20150001 168020 108100 2149825 132020 20020022 c 1600fffa 295a022 1680fff7 20160001 40966000
  //   23bdfffc 8fb60000 40967000 23bdfffc 8fb60000 23bdfffc 8fb50000 23bdfffc 8fb40000 23bdfffc 8fb30000
  //   23bdfffc 8fb00000 23bdfffc 8fa40000 23bdfffc 8fa20000 42000018
  //   可计数暂停的时钟源
  //   OP
  //   Func
  //   rs
  //   指令字
  //   rt
  //   rd
  //   JMP
  //   JR
  //   LB
  //   BGTZ
  //   OP
  //   Func
  //   Beq
  //   Bne
  //   AluOP
  //   AluSrcB
  //   RegWrite
  //   JAL
  //   RegDst
  //   Syscall
  //   MemToReg
  //   MemWrite
  //   为方便自动评测，需要输出PC，IR，寄存器堆写如数据RDin
  //   RAM写使能MemWrite、RAM写入数据MDin等信号
endmodule

module \封装正确性测试  (
);

  wire IR1, IR2, IR3, MemW, RegW;
  wire [31:0] EX_PC, ID_PC, IF_PC, IR, LED, MDin, MDinr, MEM_PC, PC, RDin, RDinr, WB_PC;

  \单周期MIPS  \u_单周期mips_1  (
    .IR1(IR1), .IR2(IR2), .IR3(IR3), .RegWrite(RegW), .MemWrite(MemW), .PC(PC), .IR(IR), .RDin(RDin),
    .MDin(MDin), .LedData(LED));
  \气泡流水线  \u_气泡流水线_1  (
    .RegWrite(RegW), .MemWrite(MemW), .IF_PC(IF_PC), .ID_PC(ID_PC), .EX_PC(EX_PC), .M_PC(MEM_PC),
    .WB_PC(WB_PC), .RDin(RDinr), .MDin(MDinr), .LedData(LED));
  \单周期MIPS_单级中断  \u_单周期mips_单级中断_1  (
    .IR1(IR1), .IR2(IR2), .IR3(IR3), .RegWrite(RegW), .MemWrite(MemW), .PC(PC), .IR(IR), .RDin(RDin),
    .MDin(MDin), .LedData(LED));
  \理想流水线  \u_理想流水线_1  (
    .RegWrite(RegW), .MemWrite(MemW), .IF_PC(IF_PC), .ID_PC(ID_PC), .EX_PC(EX_PC), .M_PC(MEM_PC),
    .WB_PC(WB_PC), .RDin(RDinr), .MDin(MDinr), .LedData(LED));
  \重定向流水线  \u_重定向流水线_1  (
    .RegWrite(RegW), .MemWrite(MemW), .IF_PC(IF_PC), .ID_PC(ID_PC), .EX_PC(EX_PC), .M_PC(MEM_PC),
    .WB_PC(WB_PC), .RDin(RDinr), .MDin(MDinr), .LedData(LED));
  \单周期MIPS_多级中断  \u_单周期mips_多级中断_1  (
    .IR1(IR1), .IR2(IR2), .IR3(IR3), .RegWrite(RegW), .MemWrite(MemW), .PC(PC), .IR(IR), .RDin(RDin),
    .MDin(MDin), .LedData(LED));

  // Notes on the sheet:
  //   单周期封装测试
  //   气泡流水封装测试
  //   单周期+单级中断封装测试
  //   请检查上面封装有无位宽不匹配，引脚标签是否和连接的标签相对应，否则无法在educoder平台上正确测试
  //   理想流水封装测试
  //   重定向流水封装测试
  //   单周期+多级中断封装测试
endmodule

module \LB_BGTZ控制信号生成  (
  input  OP1,
  input  OP0,
  input  OP2,
  input  OP3,
  input  OP4,
  input  OP5,
  input  F0,
  input  F1,
  input  F2,
  input  F3,
  input  F4,
  input  F5,
  output LB,
  output BGTZ
);

  wire not_1_out, not_2_out, not_3_out, not_4_out, not_5_out, not_6_out, not_7_out, not_8_out;

  not not_1 (not_1_out, OP0);
  not not_2 (not_2_out, OP1);
  not not_3 (not_3_out, OP2);
  not not_4 (not_4_out, OP3);
  not not_5 (not_5_out, OP4);
  not not_6 (not_6_out, OP3);
  not not_7 (not_7_out, OP4);
  not not_8 (not_8_out, OP5);
  and and_1 (LB, not_1_out, not_2_out, not_3_out, not_4_out, not_5_out, OP5);
  and and_2 (BGTZ, OP0, OP1, OP2, not_6_out, not_7_out, not_8_out);
endmodule

// IF/ID
module IF_ID (
  input  \气泡_高电平时有效 ,
  input  clk,
  input  clear,
  input  enable,
  input  [31:0] IR_in,
  input  [31:0] PC_in,
  input  [31:0] OldPC_in,
  output [31:0] IR_out,
  output [31:0] PC_out,
  output [31:0] OldPC_out
);

  wire [31:0] multiplexer_1_out, multiplexer_2_out, multiplexer_3_out;

  Multiplexer #(.select(1), .width(32), .disabled("Z"), .enable("false")) multiplexer_1 (
    .in0(IR_in), .in1({32{1'b0}}), .out(multiplexer_1_out), .sel(\气泡_高电平时有效 ));
  Multiplexer #(.select(1), .width(32), .disabled("Z"), .enable("false")) multiplexer_2 (
    .in0(PC_in), .in1({32{1'b0}}), .out(multiplexer_2_out), .sel(\气泡_高电平时有效 ));
  Multiplexer #(.select(1), .width(32), .disabled("Z"), .enable("false")) multiplexer_3 (
    .in0(OldPC_in), .in1({32{1'b0}}), .out(multiplexer_3_out), .sel(\气泡_高电平时有效 ));
  Register #(.width(32), .trigger("rising"), .Select("low")) IR (
    .D(multiplexer_1_out), .en(enable), .Q(IR_out), .clk(clk), .clr(clear));
  Register #(.width(32), .trigger("rising"), .Select("low")) PC (
    .D(multiplexer_2_out), .en(enable), .Q(PC_out), .clk(clk), .clr(clear));
  Register #(.width(32), .trigger("rising"), .Select("low")) OldPC (
    .D(multiplexer_3_out), .en(enable), .Q(OldPC_out), .clk(clk), .clr(clear));
endmodule

// ID/EX
module ID_EX (
  input  \气泡_高电平时有效 ,
  input  clk,
  input  clear,
  input  enable,
  input  Beq_in,
  input  Bne_in,
  input  MemToReg_in,
  input  MemWrite_in,
  input  [3:0] AluOP_in,
  input  AluSrc_in,
  input  RegWrite_in,
  input  JAL_in,
  input  RegDst_in,
  input  Syscall_in,
  input  JMP_in,
  input  JR_in,
  input  SignedExt_in,
  input  LB_in,
  input  BGTZ_in,
  input  [31:0] IR_in,
  input  [31:0] PC_in,
  input  [31:0] R1_in,
  input  [31:0] R2_in,
  input  [31:0] Imm_in,
  input  [31:0] OldPC_in,
  output Beq_out,
  output Bne_out,
  output MemToReg_out,
  output MemWrite_out,
  output [3:0] AluOP_out,
  output AluSrc_out,
  output RegWrite_out,
  output JAL_out,
  output RegDst_out,
  output Syscall_out,
  output JMP_out,
  output JR_out,
  output SignedExt_out,
  output LB_out,
  output BGTZ_out,
  output [31:0] IR_out,
  output [31:0] PC_out,
  output [31:0] R1_out,
  output [31:0] R2_out,
  output [31:0] Imm_out,
  output [31:0] OldPC_out
);

  wire multiplexer_1_out, multiplexer_2_out, multiplexer_3_out, multiplexer_4_out, multiplexer_5_out,
       multiplexer_6_out, multiplexer_7_out, multiplexer_8_out, multiplexer_9_out, multiplexer_10_out,
       multiplexer_11_out, multiplexer_12_out, multiplexer_13_out, multiplexer_14_out;
  wire [3:0] multiplexer_21_out;
  wire [31:0] multiplexer_15_out, multiplexer_16_out, multiplexer_17_out, multiplexer_18_out,
       multiplexer_19_out, multiplexer_20_out;

  Multiplexer #(.select(1), .width(1), .disabled("Z"), .enable("false")) multiplexer_1 (
    .in0(Beq_in), .in1(1'b0), .out(multiplexer_1_out), .sel(\气泡_高电平时有效 ));
  Multiplexer #(.select(1), .width(1), .disabled("Z"), .enable("false")) multiplexer_2 (
    .in0(Bne_in), .in1(1'b0), .out(multiplexer_2_out), .sel(\气泡_高电平时有效 ));
  Multiplexer #(.select(1), .width(1), .disabled("Z"), .enable("false")) multiplexer_3 (
    .in0(MemToReg_in), .in1(1'b0), .out(multiplexer_3_out), .sel(\气泡_高电平时有效 ));
  Multiplexer #(.select(1), .width(1), .disabled("Z"), .enable("false")) multiplexer_4 (
    .in0(MemWrite_in), .in1(1'b0), .out(multiplexer_4_out), .sel(\气泡_高电平时有效 ));
  Multiplexer #(.select(1), .width(1), .disabled("Z"), .enable("false")) multiplexer_5 (
    .in0(AluSrc_in), .in1(1'b0), .out(multiplexer_5_out), .sel(\气泡_高电平时有效 ));
  Multiplexer #(.select(1), .width(1), .disabled("Z"), .enable("false")) multiplexer_6 (
    .in0(RegWrite_in), .in1(1'b0), .out(multiplexer_6_out), .sel(\气泡_高电平时有效 ));
  Multiplexer #(.select(1), .width(1), .disabled("Z"), .enable("false")) multiplexer_7 (
    .in0(JAL_in), .in1(1'b0), .out(multiplexer_7_out), .sel(\气泡_高电平时有效 ));
  Multiplexer #(.select(1), .width(1), .disabled("Z"), .enable("false")) multiplexer_8 (
    .in0(RegDst_in), .in1(1'b0), .out(multiplexer_8_out), .sel(\气泡_高电平时有效 ));
  Multiplexer #(.select(1), .width(1), .disabled("Z"), .enable("false")) multiplexer_9 (
    .in0(Syscall_in), .in1(1'b0), .out(multiplexer_9_out), .sel(\气泡_高电平时有效 ));
  Multiplexer #(.select(1), .width(1), .disabled("Z"), .enable("false")) multiplexer_10 (
    .in0(JMP_in), .in1(1'b0), .out(multiplexer_10_out), .sel(\气泡_高电平时有效 ));
  Multiplexer #(.select(1), .width(1), .disabled("Z"), .enable("false")) multiplexer_11 (
    .in0(JR_in), .in1(1'b0), .out(multiplexer_11_out), .sel(\气泡_高电平时有效 ));
  Multiplexer #(.select(1), .width(1), .disabled("Z"), .enable("false")) multiplexer_12 (
    .in0(SignedExt_in), .in1(1'b0), .out(multiplexer_12_out), .sel(\气泡_高电平时有效 ));
  Multiplexer #(.select(1), .width(1), .disabled("Z"), .enable("false")) multiplexer_13 (
    .in0(LB_in), .in1(1'b0), .out(multiplexer_13_out), .sel(\气泡_高电平时有效 ));
  Multiplexer #(.select(1), .width(1), .disabled("Z"), .enable("false")) multiplexer_14 (
    .in0(BGTZ_in), .in1(1'b0), .out(multiplexer_14_out), .sel(\气泡_高电平时有效 ));
  Multiplexer #(.select(1), .width(32), .disabled("Z"), .enable("false")) multiplexer_15 (
    .in0(IR_in), .in1({32{1'b0}}), .out(multiplexer_15_out), .sel(\气泡_高电平时有效 ));
  Multiplexer #(.select(1), .width(32), .disabled("Z"), .enable("false")) multiplexer_16 (
    .in0(PC_in), .in1({32{1'b0}}), .out(multiplexer_16_out), .sel(\气泡_高电平时有效 ));
  Multiplexer #(.select(1), .width(32), .disabled("Z"), .enable("false")) multiplexer_17 (
    .in0(R1_in), .in1({32{1'b0}}), .out(multiplexer_17_out), .sel(\气泡_高电平时有效 ));
  Multiplexer #(.select(1), .width(32), .disabled("Z"), .enable("false")) multiplexer_18 (
    .in0(R2_in), .in1({32{1'b0}}), .out(multiplexer_18_out), .sel(\气泡_高电平时有效 ));
  Multiplexer #(.select(1), .width(32), .disabled("Z"), .enable("false")) multiplexer_19 (
    .in0(Imm_in), .in1({32{1'b0}}), .out(multiplexer_19_out), .sel(\气泡_高电平时有效 ));
  Multiplexer #(.select(1), .width(32), .disabled("Z"), .enable("false")) multiplexer_20 (
    .in0(OldPC_in), .in1({32{1'b0}}), .out(multiplexer_20_out), .sel(\气泡_高电平时有效 ));
  Multiplexer #(.select(1), .width(4), .disabled("Z"), .enable("false")) multiplexer_21 (
    .in0(AluOP_in), .in1(4'b0000), .out(multiplexer_21_out), .sel(\气泡_高电平时有效 ));
  Register #(.width(1), .trigger("rising"), .Select("low")) Beq (
    .D(multiplexer_1_out), .en(enable), .Q(Beq_out), .clk(clk), .clr(clear));
  Register #(.width(1), .trigger("rising"), .Select("low")) Bne (
    .D(multiplexer_2_out), .en(enable), .Q(Bne_out), .clk(clk), .clr(clear));
  Register #(.width(1), .trigger("rising"), .Select("low")) MemToReg (
    .D(multiplexer_3_out), .en(enable), .Q(MemToReg_out), .clk(clk), .clr(clear));
  Register #(.width(1), .trigger("rising"), .Select("low")) MemWrite (
    .D(multiplexer_4_out), .en(enable), .Q(MemWrite_out), .clk(clk), .clr(clear));
  Register #(.width(4), .trigger("rising"), .Select("low")) AluOP (
    .D(multiplexer_21_out), .en(enable), .Q(AluOP_out), .clk(clk), .clr(clear));
  Register #(.width(1), .trigger("rising"), .Select("low")) AluSrc (
    .D(multiplexer_5_out), .en(enable), .Q(AluSrc_out), .clk(clk), .clr(clear));
  Register #(.width(1), .trigger("rising"), .Select("low")) RegWrite (
    .D(multiplexer_6_out), .en(enable), .Q(RegWrite_out), .clk(clk), .clr(clear));
  Register #(.width(1), .trigger("rising"), .Select("low")) JAL (
    .D(multiplexer_7_out), .en(enable), .Q(JAL_out), .clk(clk), .clr(clear));
  Register #(.width(1), .trigger("rising"), .Select("low")) RegDst (
    .D(multiplexer_8_out), .en(enable), .Q(RegDst_out), .clk(clk), .clr(clear));
  Register #(.width(1), .trigger("rising"), .Select("low")) Syscall (
    .D(multiplexer_9_out), .en(enable), .Q(Syscall_out), .clk(clk), .clr(clear));
  Register #(.width(1), .trigger("rising"), .Select("low")) JMP (
    .D(multiplexer_10_out), .en(enable), .Q(JMP_out), .clk(clk), .clr(clear));
  Register #(.width(1), .trigger("rising"), .Select("low")) JR (
    .D(multiplexer_11_out), .en(enable), .Q(JR_out), .clk(clk), .clr(clear));
  Register #(.width(1), .trigger("rising"), .Select("low")) SignedExt (
    .D(multiplexer_12_out), .en(enable), .Q(SignedExt_out), .clk(clk), .clr(clear));
  Register #(.width(1), .trigger("rising"), .Select("low")) LB (
    .D(multiplexer_13_out), .en(enable), .Q(LB_out), .clk(clk), .clr(clear));
  Register #(.width(1), .trigger("rising"), .Select("low")) BGEZ (
    .D(multiplexer_14_out), .en(enable), .Q(BGTZ_out), .clk(clk), .clr(clear));
  Register #(.width(32), .trigger("rising"), .Select("low")) IR (
    .D(multiplexer_15_out), .en(enable), .Q(IR_out), .clk(clk), .clr(clear));
  Register #(.width(32), .trigger("rising"), .Select("low")) PC (
    .D(multiplexer_16_out), .en(enable), .Q(PC_out), .clk(clk), .clr(clear));
  Register #(.width(32), .trigger("rising"), .Select("low")) R1 (
    .D(multiplexer_17_out), .en(enable), .Q(R1_out), .clk(clk), .clr(clear));
  Register #(.width(32), .trigger("rising"), .Select("low")) R2 (
    .D(multiplexer_18_out), .en(enable), .Q(R2_out), .clk(clk), .clr(clear));
  Register #(.width(32), .trigger("rising"), .Select("low")) Imm (
    .D(multiplexer_19_out), .en(enable), .Q(Imm_out), .clk(clk), .clr(clear));
  Register #(.width(32), .trigger("rising"), .Select("low")) OldPC (
    .D(multiplexer_20_out), .en(enable), .Q(OldPC_out), .clk(clk), .clr(clear));
endmodule

// EX/MEM
module EX_MEM (
  input  \气泡_高电平时有效 ,
  input  clk,
  input  clear,
  input  enable,
  input  MemToReg_in,
  input  MemWrite_in,
  input  RegWrite_in,
  input  JAL_in,
  input  LB_in,
  input  RegDst_in,
  input  Syscall_in,
  input  equal_in,
  input  pause_in,
  input  [31:0] IR_in,
  input  [31:0] PC_in,
  input  [31:0] ALUResult_in,
  input  [31:0] R2_in,
  input  [31:0] OldPC_in,
  output MemToReg_out,
  output MemWrite_out,
  output RegWrite_out,
  output JAL_out,
  output LB_out,
  output RegDst_out,
  output Syscall_out,
  output equal_out,
  output pause_out,
  output [31:0] IR_out,
  output [31:0] PC_out,
  output [31:0] ALUResult_out,
  output [31:0] R2_out,
  output [31:0] OldPC_out
);

  wire multiplexer_1_out, multiplexer_2_out, multiplexer_3_out, multiplexer_4_out, multiplexer_5_out,
       multiplexer_6_out, multiplexer_7_out, multiplexer_8_out, multiplexer_9_out;
  wire [31:0] multiplexer_10_out, multiplexer_11_out, multiplexer_12_out, multiplexer_13_out,
       multiplexer_14_out;

  Multiplexer #(.select(1), .width(1), .disabled("Z"), .enable("false")) multiplexer_1 (
    .in0(MemToReg_in), .in1(1'b0), .out(multiplexer_1_out), .sel(\气泡_高电平时有效 ));
  Multiplexer #(.select(1), .width(1), .disabled("Z"), .enable("false")) multiplexer_2 (
    .in0(MemWrite_in), .in1(1'b0), .out(multiplexer_2_out), .sel(\气泡_高电平时有效 ));
  Multiplexer #(.select(1), .width(1), .disabled("Z"), .enable("false")) multiplexer_3 (
    .in0(RegWrite_in), .in1(1'b0), .out(multiplexer_3_out), .sel(\气泡_高电平时有效 ));
  Multiplexer #(.select(1), .width(1), .disabled("Z"), .enable("false")) multiplexer_4 (
    .in0(JAL_in), .in1(1'b0), .out(multiplexer_4_out), .sel(\气泡_高电平时有效 ));
  Multiplexer #(.select(1), .width(1), .disabled("Z"), .enable("false")) multiplexer_5 (
    .in0(LB_in), .in1(1'b0), .out(multiplexer_5_out), .sel(\气泡_高电平时有效 ));
  Multiplexer #(.select(1), .width(1), .disabled("Z"), .enable("false")) multiplexer_6 (
    .in0(RegDst_in), .in1(1'b0), .out(multiplexer_6_out), .sel(\气泡_高电平时有效 ));
  Multiplexer #(.select(1), .width(1), .disabled("Z"), .enable("false")) multiplexer_7 (
    .in0(Syscall_in), .in1(1'b0), .out(multiplexer_7_out), .sel(\气泡_高电平时有效 ));
  Multiplexer #(.select(1), .width(1), .disabled("Z"), .enable("false")) multiplexer_8 (
    .in0(equal_in), .in1(1'b0), .out(multiplexer_8_out), .sel(\气泡_高电平时有效 ));
  Multiplexer #(.select(1), .width(1), .disabled("Z"), .enable("false")) multiplexer_9 (
    .in0(pause_in), .in1(1'b0), .out(multiplexer_9_out), .sel(\气泡_高电平时有效 ));
  Multiplexer #(.select(1), .width(32), .disabled("Z"), .enable("false")) multiplexer_10 (
    .in0(IR_in), .in1({32{1'b0}}), .out(multiplexer_10_out), .sel(\气泡_高电平时有效 ));
  Multiplexer #(.select(1), .width(32), .disabled("Z"), .enable("false")) multiplexer_11 (
    .in0(PC_in), .in1({32{1'b0}}), .out(multiplexer_11_out), .sel(\气泡_高电平时有效 ));
  Multiplexer #(.select(1), .width(32), .disabled("Z"), .enable("false")) multiplexer_12 (
    .in0(ALUResult_in), .in1({32{1'b0}}), .out(multiplexer_12_out), .sel(\气泡_高电平时有效 ));
  Multiplexer #(.select(1), .width(32), .disabled("Z"), .enable("false")) multiplexer_13 (
    .in0(R2_in), .in1({32{1'b0}}), .out(multiplexer_13_out), .sel(\气泡_高电平时有效 ));
  Multiplexer #(.select(1), .width(32), .disabled("Z"), .enable("false")) multiplexer_14 (
    .in0(OldPC_in), .in1({32{1'b0}}), .out(multiplexer_14_out), .sel(\气泡_高电平时有效 ));
  Register #(.width(1), .trigger("rising"), .Select("low")) MemToReg (
    .D(multiplexer_1_out), .en(enable), .Q(MemToReg_out), .clk(clk), .clr(clear));
  Register #(.width(1), .trigger("rising"), .Select("low")) MemWrite (
    .D(multiplexer_2_out), .en(enable), .Q(MemWrite_out), .clk(clk), .clr(clear));
  Register #(.width(1), .trigger("rising"), .Select("low")) RegWrite (
    .D(multiplexer_3_out), .en(enable), .Q(RegWrite_out), .clk(clk), .clr(clear));
  Register #(.width(1), .trigger("rising"), .Select("low")) JAL (
    .D(multiplexer_4_out), .en(enable), .Q(JAL_out), .clk(clk), .clr(clear));
  Register #(.width(1), .trigger("rising"), .Select("low")) LB (
    .D(multiplexer_5_out), .en(enable), .Q(LB_out), .clk(clk), .clr(clear));
  Register #(.width(1), .trigger("rising"), .Select("low")) RegDst (
    .D(multiplexer_6_out), .en(enable), .Q(RegDst_out), .clk(clk), .clr(clear));
  Register #(.width(1), .trigger("rising"), .Select("low")) Syscall (
    .D(multiplexer_7_out), .en(enable), .Q(Syscall_out), .clk(clk), .clr(clear));
  Register #(.width(1), .trigger("rising"), .Select("low")) equal (
    .D(multiplexer_8_out), .en(enable), .Q(equal_out), .clk(clk), .clr(clear));
  Register #(.width(1), .trigger("rising"), .Select("low")) pause (
    .D(multiplexer_9_out), .en(enable), .Q(pause_out), .clk(clk), .clr(clear));
  Register #(.width(32), .trigger("rising"), .Select("low")) IR (
    .D(multiplexer_10_out), .en(enable), .Q(IR_out), .clk(clk), .clr(clear));
  Register #(.width(32), .trigger("rising"), .Select("low")) PC (
    .D(multiplexer_11_out), .en(enable), .Q(PC_out), .clk(clk), .clr(clear));
  Register #(.width(32), .trigger("rising"), .Select("low")) ALUResult (
    .D(multiplexer_12_out), .en(enable), .Q(ALUResult_out), .clk(clk), .clr(clear));
  Register #(.width(32), .trigger("rising"), .Select("low")) R2 (
    .D(multiplexer_13_out), .en(enable), .Q(R2_out), .clk(clk), .clr(clear));
  Register #(.width(32), .trigger("rising"), .Select("low")) OldPC (
    .D(multiplexer_14_out), .en(enable), .Q(OldPC_out), .clk(clk), .clr(clear));
endmodule

// MEM/WB
module MEM_WB (
  input  \气泡_高电平时有效 ,
  input  clk,
  input  clear,
  input  enable,
  input  MemToReg_in,
  input  MemWrite_in,
  input  RegWrite_in,
  input  JAL_in,
  input  LB_in,
  input  RegDst_in,
  input  Syscall_in,
  input  equal_in,
  input  pause_in,
  input  [31:0] IR_in,
  input  [31:0] PC_in,
  input  [31:0] ALUResult_in,
  input  [31:0] Memorydata_in,
  input  [31:0] OldPC_in,
  output MemToReg_out,
  output MemWrite_out,
  output RegWrite_out,
  output JAL_out,
  output LB_out,
  output RegDst_out,
  output Syscall_out,
  output equal_out,
  output pause_out,
  output [31:0] IR_out,
  output [31:0] PC_out,
  output [31:0] ALUResult_out,
  output [31:0] Memorydata_out,
  output [31:0] OldPC_out
);

  wire multiplexer_1_out, multiplexer_2_out, multiplexer_3_out, multiplexer_4_out, multiplexer_5_out,
       multiplexer_6_out, multiplexer_7_out, multiplexer_8_out, multiplexer_9_out;
  wire [31:0] multiplexer_10_out, multiplexer_11_out, multiplexer_12_out, multiplexer_13_out,
       multiplexer_14_out;

  Multiplexer #(.select(1), .width(1), .disabled("Z"), .enable("false")) multiplexer_1 (
    .in0(MemToReg_in), .in1(1'b0), .out(multiplexer_1_out), .sel(\气泡_高电平时有效 ));
  Multiplexer #(.select(1), .width(1), .disabled("Z"), .enable("false")) multiplexer_2 (
    .in0(MemWrite_in), .in1(1'b0), .out(multiplexer_2_out), .sel(\气泡_高电平时有效 ));
  Multiplexer #(.select(1), .width(1), .disabled("Z"), .enable("false")) multiplexer_3 (
    .in0(RegWrite_in), .in1(1'b0), .out(multiplexer_3_out), .sel(\气泡_高电平时有效 ));
  Multiplexer #(.select(1), .width(1), .disabled("Z"), .enable("false")) multiplexer_4 (
    .in0(JAL_in), .in1(1'b0), .out(multiplexer_4_out), .sel(\气泡_高电平时有效 ));
  Multiplexer #(.select(1), .width(1), .disabled("Z"), .enable("false")) multiplexer_5 (
    .in0(LB_in), .in1(1'b0), .out(multiplexer_5_out), .sel(\气泡_高电平时有效 ));
  Multiplexer #(.select(1), .width(1), .disabled("Z"), .enable("false")) multiplexer_6 (
    .in0(RegDst_in), .in1(1'b0), .out(multiplexer_6_out), .sel(\气泡_高电平时有效 ));
  Multiplexer #(.select(1), .width(1), .disabled("Z"), .enable("false")) multiplexer_7 (
    .in0(Syscall_in), .in1(1'b0), .out(multiplexer_7_out), .sel(\气泡_高电平时有效 ));
  Multiplexer #(.select(1), .width(1), .disabled("Z"), .enable("false")) multiplexer_8 (
    .in0(equal_in), .in1(1'b0), .out(multiplexer_8_out), .sel(\气泡_高电平时有效 ));
  Multiplexer #(.select(1), .width(1), .disabled("Z"), .enable("false")) multiplexer_9 (
    .in0(pause_in), .in1(1'b0), .out(multiplexer_9_out), .sel(\气泡_高电平时有效 ));
  Multiplexer #(.select(1), .width(32), .disabled("Z"), .enable("false")) multiplexer_10 (
    .in0(IR_in), .in1({32{1'b0}}), .out(multiplexer_10_out), .sel(\气泡_高电平时有效 ));
  Multiplexer #(.select(1), .width(32), .disabled("Z"), .enable("false")) multiplexer_11 (
    .in0(PC_in), .in1({32{1'b0}}), .out(multiplexer_11_out), .sel(\气泡_高电平时有效 ));
  Multiplexer #(.select(1), .width(32), .disabled("Z"), .enable("false")) multiplexer_12 (
    .in0(ALUResult_in), .in1({32{1'b0}}), .out(multiplexer_12_out), .sel(\气泡_高电平时有效 ));
  Multiplexer #(.select(1), .width(32), .disabled("Z"), .enable("false")) multiplexer_13 (
    .in0(Memorydata_in), .in1({32{1'b0}}), .out(multiplexer_13_out), .sel(\气泡_高电平时有效 ));
  Multiplexer #(.select(1), .width(32), .disabled("Z"), .enable("false")) multiplexer_14 (
    .in0(OldPC_in), .in1({32{1'b0}}), .out(multiplexer_14_out), .sel(\气泡_高电平时有效 ));
  Register #(.width(1), .trigger("rising"), .Select("low")) MemToReg (
    .D(multiplexer_1_out), .en(enable), .Q(MemToReg_out), .clk(clk), .clr(clear));
  Register #(.width(1), .trigger("rising"), .Select("low")) MemWrite (
    .D(multiplexer_2_out), .en(enable), .Q(MemWrite_out), .clk(clk), .clr(clear));
  Register #(.width(1), .trigger("rising"), .Select("low")) RegWrite (
    .D(multiplexer_3_out), .en(enable), .Q(RegWrite_out), .clk(clk), .clr(clear));
  Register #(.width(1), .trigger("rising"), .Select("low")) JAL (
    .D(multiplexer_4_out), .en(enable), .Q(JAL_out), .clk(clk), .clr(clear));
  Register #(.width(1), .trigger("rising"), .Select("low")) LB (
    .D(multiplexer_5_out), .en(enable), .Q(LB_out), .clk(clk), .clr(clear));
  Register #(.width(1), .trigger("rising"), .Select("low")) RegDst (
    .D(multiplexer_6_out), .en(enable), .Q(RegDst_out), .clk(clk), .clr(clear));
  Register #(.width(1), .trigger("rising"), .Select("low")) Syscall (
    .D(multiplexer_7_out), .en(enable), .Q(Syscall_out), .clk(clk), .clr(clear));
  Register #(.width(1), .trigger("rising"), .Select("low")) equal (
    .D(multiplexer_8_out), .en(enable), .Q(equal_out), .clk(clk), .clr(clear));
  Register #(.width(1), .trigger("rising"), .Select("low")) pause (
    .D(multiplexer_9_out), .en(enable), .Q(pause_out), .clk(clk), .clr(clear));
  Register #(.width(32), .trigger("rising"), .Select("low")) IR (
    .D(multiplexer_10_out), .en(enable), .Q(IR_out), .clk(clk), .clr(clear));
  Register #(.width(32), .trigger("rising"), .Select("low")) PC (
    .D(multiplexer_11_out), .en(enable), .Q(PC_out), .clk(clk), .clr(clear));
  Register #(.width(32), .trigger("rising"), .Select("low")) ALUResult (
    .D(multiplexer_12_out), .en(enable), .Q(ALUResult_out), .clk(clk), .clr(clear));
  Register #(.width(32), .trigger("rising"), .Select("low")) Memorydata (
    .D(multiplexer_13_out), .en(enable), .Q(Memorydata_out), .clk(clk), .clr(clear));
  Register #(.width(32), .trigger("rising"), .Select("low")) OldPC (
    .D(multiplexer_14_out), .en(enable), .Q(OldPC_out), .clk(clk), .clr(clear));
endmodule
// 源寄存器使用情况
module \源寄存器使用情况  (
  input  OP0,
  input  OP1,
  input  OP2,
  input  OP3,
  input  OP4,
  input  OP5,
  input  F0,
  input  F1,
  input  F2,
  input  F3,
  input  F4,
  input  F5,
  output R1_Used,
  output R2_Used
);

  wire and_1_out, and_2_out, and_3_out, and_4_out, and_5_out, and_6_out, and_7_out, and_8_out, and_9_out,
       and_10_out, and_11_out, and_12_out, and_13_out, and_14_out, and_15_out, and_16_out, and_17_out,
       and_18_out, and_19_out, and_20_out, and_21_out, and_22_out, and_23_out, and_24_out, and_25_out,
       and_26_out, and_27_out, and_28_out, and_29_out, and_30_out, and_31_out, and_32_out, and_33_out,
       and_34_out, and_35_out, and_36_out, and_37_out, and_38_out, and_39_out, and_40_out, and_41_out,
       and_42_out, and_43_out, and_44_out, not_1_out, not_2_out, not_3_out, not_4_out, not_5_out, not_6_out,
       not_7_out, not_8_out, not_9_out, not_10_out, not_11_out, not_12_out, not_13_out, not_14_out,
       not_15_out, not_16_out, not_17_out, not_18_out, not_19_out, not_20_out, not_21_out, not_22_out,
       not_23_out, not_24_out, not_25_out, not_26_out, not_27_out, not_28_out, not_29_out, not_30_out,
       not_31_out, not_32_out, not_33_out, not_34_out, not_35_out, not_36_out, not_37_out, not_38_out,
       not_39_out, not_40_out, not_41_out, not_42_out, not_43_out, not_44_out, not_45_out, not_46_out,
       not_47_out, not_48_out, not_49_out, not_50_out, not_51_out, not_52_out, not_53_out, not_54_out,
       not_55_out, not_56_out, not_57_out, not_58_out, not_59_out, not_60_out, not_61_out, not_62_out,
       not_63_out, not_64_out, not_65_out, not_66_out, not_67_out, not_68_out, not_69_out, not_70_out,
       not_71_out, not_72_out, not_73_out, not_74_out, not_75_out, not_76_out, not_77_out, not_78_out,
       not_79_out, not_80_out, not_81_out, not_82_out, not_83_out, not_84_out, not_85_out, not_86_out,
       not_87_out, not_88_out, not_89_out, not_90_out, not_91_out, not_92_out, not_93_out, not_94_out,
       not_95_out, not_96_out, not_97_out, not_98_out, not_99_out, not_100_out, not_101_out, not_102_out,
       not_103_out, not_104_out, not_105_out, not_106_out, not_107_out, not_108_out, not_109_out,
       not_110_out, not_111_out, not_112_out, not_113_out, not_114_out, not_115_out, not_116_out,
       not_117_out, not_118_out, not_119_out, not_120_out, not_121_out, not_122_out, not_123_out,
       not_124_out, not_125_out, not_126_out, not_127_out, not_128_out, not_129_out, not_130_out,
       not_131_out, not_132_out, not_133_out, not_134_out, not_135_out, not_136_out, not_137_out,
       not_138_out, not_139_out, not_140_out, not_141_out, not_142_out, not_143_out, not_144_out,
       not_145_out, not_146_out, not_147_out, not_148_out, not_149_out, not_150_out, not_151_out,
       not_152_out, not_153_out, not_154_out, not_155_out, not_156_out, not_157_out, not_158_out,
       not_159_out, not_160_out, not_161_out, not_162_out, not_163_out, not_164_out, not_165_out,
       not_166_out, not_167_out, not_168_out, not_169_out, not_170_out, not_171_out, not_172_out,
       not_173_out, not_174_out, not_175_out, not_176_out, not_177_out, not_178_out, not_179_out,
       not_180_out, not_181_out, not_182_out, not_183_out, not_184_out, not_185_out, not_186_out,
       not_187_out, not_188_out, not_189_out, not_190_out, not_191_out, not_192_out, not_193_out,
       not_194_out, not_195_out, not_196_out, not_197_out, not_198_out, not_199_out, not_200_out,
       not_201_out, not_202_out, not_203_out, not_204_out, not_205_out, not_206_out, not_207_out,
       not_208_out, not_209_out, not_210_out, not_211_out, not_212_out, not_213_out, not_214_out,
       not_215_out, not_216_out, not_217_out, not_218_out, not_219_out, not_220_out, not_221_out,
       not_222_out, not_223_out, not_224_out, not_225_out, not_226_out, not_227_out, not_228_out,
       not_229_out, not_230_out, not_231_out, not_232_out, not_233_out, not_234_out, not_235_out,
       not_236_out, not_237_out, not_238_out, not_239_out, not_240_out, not_241_out, not_242_out,
       not_243_out, not_244_out, not_245_out, not_246_out, not_247_out, not_248_out, not_249_out,
       not_250_out, not_251_out, not_252_out, not_253_out, not_254_out, not_255_out, not_256_out,
       not_257_out, not_258_out, not_259_out, not_260_out, not_261_out, not_262_out, not_263_out,
       not_264_out, not_265_out, not_266_out, not_267_out, not_268_out, not_269_out, not_270_out,
       not_271_out, not_272_out, not_273_out, not_274_out, not_275_out, not_276_out, not_277_out,
       not_278_out, not_279_out, not_280_out, not_281_out, not_282_out, not_283_out, not_284_out,
       not_285_out, not_286_out, not_287_out, not_288_out, not_289_out, not_290_out, not_291_out,
       not_292_out, not_293_out, not_294_out, not_295_out, not_296_out, not_297_out, not_298_out,
       not_299_out, not_300_out, not_301_out, not_302_out, not_303_out, not_304_out, not_305_out,
       not_306_out, not_307_out, not_308_out, not_309_out, not_310_out, not_311_out, not_312_out,
       not_313_out, not_314_out, not_315_out, not_316_out, not_317_out, not_318_out, not_319_out,
       not_320_out, not_321_out, not_322_out, not_323_out, not_324_out, not_325_out, not_326_out,
       not_327_out, not_328_out, not_329_out, not_330_out, not_331_out;

  not not_1 (not_1_out, OP5);
  not not_2 (not_2_out, OP4);
  not not_3 (not_3_out, OP3);
  not not_4 (not_4_out, OP2);
  not not_5 (not_5_out, OP1);
  not not_6 (not_6_out, OP0);
  not not_7 (not_7_out, F5);
  not not_8 (not_8_out, F4);
  not not_9 (not_9_out, F3);
  not not_10 (not_10_out, F2);
  not not_11 (not_11_out, F1);
  not not_12 (not_12_out, F0);
  not not_13 (not_13_out, OP5);
  not not_14 (not_14_out, OP4);
  not not_15 (not_15_out, OP3);
  not not_16 (not_16_out, OP2);
  not not_17 (not_17_out, OP1);
  not not_18 (not_18_out, OP0);
  not not_19 (not_19_out, F5);
  not not_20 (not_20_out, F4);
  not not_21 (not_21_out, F3);
  not not_22 (not_22_out, F2);
  not not_23 (not_23_out, OP5);
  not not_24 (not_24_out, OP4);
  not not_25 (not_25_out, OP3);
  not not_26 (not_26_out, OP2);
  not not_27 (not_27_out, OP1);
  not not_28 (not_28_out, OP0);
  not not_29 (not_29_out, F5);
  not not_30 (not_30_out, F4);
  not not_31 (not_31_out, F3);
  not not_32 (not_32_out, F2);
  not not_33 (not_33_out, F0);
  not not_34 (not_34_out, OP5);
  not not_35 (not_35_out, OP4);
  not not_36 (not_36_out, OP3);
  not not_37 (not_37_out, OP2);
  not not_38 (not_38_out, OP1);
  not not_39 (not_39_out, OP0);
  not not_40 (not_40_out, F4);
  not not_41 (not_41_out, F3);
  not not_42 (not_42_out, F2);
  not not_43 (not_43_out, F1);
  not not_44 (not_44_out, F0);
  not not_45 (not_45_out, OP5);
  not not_46 (not_46_out, OP4);
  not not_47 (not_47_out, OP3);
  not not_48 (not_48_out, OP2);
  not not_49 (not_49_out, OP1);
  not not_50 (not_50_out, OP0);
  not not_51 (not_51_out, F4);
  not not_52 (not_52_out, F3);
  not not_53 (not_53_out, F2);
  not not_54 (not_54_out, F1);
  not not_55 (not_55_out, OP5);
  not not_56 (not_56_out, OP4);
  not not_57 (not_57_out, OP3);
  not not_58 (not_58_out, OP2);
  not not_59 (not_59_out, OP1);
  not not_60 (not_60_out, OP0);
  not not_61 (not_61_out, F4);
  not not_62 (not_62_out, F3);
  not not_63 (not_63_out, F2);
  not not_64 (not_64_out, F0);
  not not_65 (not_65_out, OP5);
  not not_66 (not_66_out, OP4);
  not not_67 (not_67_out, OP3);
  not not_68 (not_68_out, OP2);
  not not_69 (not_69_out, OP1);
  not not_70 (not_70_out, OP0);
  not not_71 (not_71_out, F4);
  not not_72 (not_72_out, F3);
  not not_73 (not_73_out, F1);
  not not_74 (not_74_out, F0);
  not not_75 (not_75_out, OP5);
  not not_76 (not_76_out, OP4);
  not not_77 (not_77_out, OP3);
  not not_78 (not_78_out, OP2);
  not not_79 (not_79_out, OP1);
  not not_80 (not_80_out, OP0);
  not not_81 (not_81_out, F4);
  not not_82 (not_82_out, F3);
  not not_83 (not_83_out, F1);
  not not_84 (not_84_out, OP5);
  not not_85 (not_85_out, OP4);
  not not_86 (not_86_out, OP3);
  not not_87 (not_87_out, OP2);
  not not_88 (not_88_out, OP1);
  not not_89 (not_89_out, OP0);
  not not_90 (not_90_out, F4);
  not not_91 (not_91_out, F3);
  not not_92 (not_92_out, OP5);
  not not_93 (not_93_out, OP4);
  not not_94 (not_94_out, OP3);
  not not_95 (not_95_out, OP2);
  not not_96 (not_96_out, OP1);
  not not_97 (not_97_out, OP0);
  not not_98 (not_98_out, F4);
  not not_99 (not_99_out, F2);
  not not_100 (not_100_out, F0);
  not not_101 (not_101_out, OP5);
  not not_102 (not_102_out, OP4);
  not not_103 (not_103_out, OP3);
  not not_104 (not_104_out, OP2);
  not not_105 (not_105_out, OP1);
  not not_106 (not_106_out, OP0);
  not not_107 (not_107_out, F4);
  not not_108 (not_108_out, F2);
  not not_109 (not_109_out, OP5);
  not not_110 (not_110_out, OP4);
  not not_111 (not_111_out, OP3);
  not not_112 (not_112_out, OP2);
  not not_113 (not_113_out, OP1);
  not not_114 (not_114_out, OP0);
  not not_115 (not_115_out, F5);
  not not_116 (not_116_out, F4);
  not not_117 (not_117_out, F2);
  not not_118 (not_118_out, F1);
  not not_119 (not_119_out, F0);
  not not_120 (not_120_out, OP5);
  not not_121 (not_121_out, OP4);
  not not_122 (not_122_out, OP3);
  not not_123 (not_123_out, OP2);
  not not_124 (not_124_out, OP1);
  not not_125 (not_125_out, OP0);
  not not_126 (not_126_out, F5);
  not not_127 (not_127_out, F4);
  not not_128 (not_128_out, F1);
  not not_129 (not_129_out, F0);
  not not_130 (not_130_out, OP5);
  not not_131 (not_131_out, OP4);
  not not_132 (not_132_out, OP3);
  not not_133 (not_133_out, OP1);
  not not_134 (not_134_out, OP0);
  not not_135 (not_135_out, OP5);
  not not_136 (not_136_out, OP4);
  not not_137 (not_137_out, OP3);
  not not_138 (not_138_out, OP1);
  not not_139 (not_139_out, OP5);
  not not_140 (not_140_out, OP4);
  not not_141 (not_141_out, OP2);
  not not_142 (not_142_out, OP1);
  not not_143 (not_143_out, OP0);
  not not_144 (not_144_out, OP5);
  not not_145 (not_145_out, OP4);
  not not_146 (not_146_out, OP1);
  not not_147 (not_147_out, OP0);
  not not_148 (not_148_out, OP5);
  not not_149 (not_149_out, OP4);
  not not_150 (not_150_out, OP2);
  not not_151 (not_151_out, OP1);
  not not_152 (not_152_out, OP5);
  not not_153 (not_153_out, OP4);
  not not_154 (not_154_out, OP2);
  not not_155 (not_155_out, OP0);
  not not_156 (not_156_out, OP5);
  not not_157 (not_157_out, OP4);
  not not_158 (not_158_out, OP1);
  not not_159 (not_159_out, OP4);
  not not_160 (not_160_out, OP3);
  not not_161 (not_161_out, OP2);
  not not_162 (not_162_out, OP4);
  not not_163 (not_163_out, OP2);
  not not_164 (not_164_out, OP5);
  not not_165 (not_165_out, OP4);
  not not_166 (not_166_out, OP3);
  not not_167 (not_167_out, OP2);
  not not_168 (not_168_out, OP1);
  not not_169 (not_169_out, OP0);
  not not_170 (not_170_out, F4);
  not not_171 (not_171_out, F3);
  not not_172 (not_172_out, F0);
  not not_173 (not_173_out, OP5);
  not not_174 (not_174_out, OP4);
  not not_175 (not_175_out, OP2);
  not not_176 (not_176_out, OP4);
  not not_177 (not_177_out, OP3);
  not not_178 (not_178_out, OP2);
  not not_179 (not_179_out, OP1);
  not not_180 (not_180_out, OP0);
  not not_181 (not_181_out, OP5);
  not not_182 (not_182_out, OP4);
  not not_183 (not_183_out, OP3);
  not not_184 (not_184_out, OP2);
  not not_185 (not_185_out, OP1);
  not not_186 (not_186_out, OP5);
  not not_187 (not_187_out, OP4);
  not not_188 (not_188_out, OP3);
  not not_189 (not_189_out, OP2);
  not not_190 (not_190_out, OP1);
  not not_191 (not_191_out, OP0);
  not not_192 (not_192_out, F5);
  not not_193 (not_193_out, F4);
  not not_194 (not_194_out, F3);
  not not_195 (not_195_out, F2);
  not not_196 (not_196_out, F1);
  not not_197 (not_197_out, F0);
  not not_198 (not_198_out, OP5);
  not not_199 (not_199_out, OP4);
  not not_200 (not_200_out, OP3);
  not not_201 (not_201_out, OP2);
  not not_202 (not_202_out, OP1);
  not not_203 (not_203_out, OP0);
  not not_204 (not_204_out, F5);
  not not_205 (not_205_out, F4);
  not not_206 (not_206_out, F3);
  not not_207 (not_207_out, F2);
  not not_208 (not_208_out, OP5);
  not not_209 (not_209_out, OP4);
  not not_210 (not_210_out, OP3);
  not not_211 (not_211_out, OP2);
  not not_212 (not_212_out, OP1);
  not not_213 (not_213_out, OP0);
  not not_214 (not_214_out, F5);
  not not_215 (not_215_out, F4);
  not not_216 (not_216_out, F3);
  not not_217 (not_217_out, F2);
  not not_218 (not_218_out, F0);
  not not_219 (not_219_out, OP5);
  not not_220 (not_220_out, OP4);
  not not_221 (not_221_out, OP3);
  not not_222 (not_222_out, OP2);
  not not_223 (not_223_out, OP1);
  not not_224 (not_224_out, OP0);
  not not_225 (not_225_out, F4);
  not not_226 (not_226_out, F3);
  not not_227 (not_227_out, F2);
  not not_228 (not_228_out, F1);
  not not_229 (not_229_out, F0);
  not not_230 (not_230_out, OP5);
  not not_231 (not_231_out, OP4);
  not not_232 (not_232_out, OP3);
  not not_233 (not_233_out, OP2);
  not not_234 (not_234_out, OP1);
  not not_235 (not_235_out, OP0);
  not not_236 (not_236_out, F4);
  not not_237 (not_237_out, F3);
  not not_238 (not_238_out, F2);
  not not_239 (not_239_out, F1);
  not not_240 (not_240_out, OP5);
  not not_241 (not_241_out, OP4);
  not not_242 (not_242_out, OP3);
  not not_243 (not_243_out, OP2);
  not not_244 (not_244_out, OP1);
  not not_245 (not_245_out, OP0);
  not not_246 (not_246_out, F4);
  not not_247 (not_247_out, F3);
  not not_248 (not_248_out, F2);
  not not_249 (not_249_out, F0);
  not not_250 (not_250_out, OP5);
  not not_251 (not_251_out, OP4);
  not not_252 (not_252_out, OP3);
  not not_253 (not_253_out, OP2);
  not not_254 (not_254_out, OP1);
  not not_255 (not_255_out, OP0);
  not not_256 (not_256_out, F4);
  not not_257 (not_257_out, F3);
  not not_258 (not_258_out, F1);
  not not_259 (not_259_out, F0);
  not not_260 (not_260_out, OP5);
  not not_261 (not_261_out, OP4);
  not not_262 (not_262_out, OP3);
  not not_263 (not_263_out, OP2);
  not not_264 (not_264_out, OP1);
  not not_265 (not_265_out, OP0);
  not not_266 (not_266_out, F4);
  not not_267 (not_267_out, F3);
  not not_268 (not_268_out, F1);
  not not_269 (not_269_out, OP5);
  not not_270 (not_270_out, OP4);
  not not_271 (not_271_out, OP3);
  not not_272 (not_272_out, OP2);
  not not_273 (not_273_out, OP1);
  not not_274 (not_274_out, OP0);
  not not_275 (not_275_out, F4);
  not not_276 (not_276_out, F3);
  not not_277 (not_277_out, OP5);
  not not_278 (not_278_out, OP4);
  not not_279 (not_279_out, OP3);
  not not_280 (not_280_out, OP2);
  not not_281 (not_281_out, OP1);
  not not_282 (not_282_out, OP0);
  not not_283 (not_283_out, F4);
  not not_284 (not_284_out, F2);
  not not_285 (not_285_out, F0);
  not not_286 (not_286_out, OP5);
  not not_287 (not_287_out, OP4);
  not not_288 (not_288_out, OP3);
  not not_289 (not_289_out, OP2);
  not not_290 (not_290_out, OP1);
  not not_291 (not_291_out, OP0);
  not not_292 (not_292_out, F4);
  not not_293 (not_293_out, F2);
  not not_294 (not_294_out, OP5);
  not not_295 (not_295_out, OP4);
  not not_296 (not_296_out, OP3);
  not not_297 (not_297_out, OP2);
  not not_298 (not_298_out, OP1);
  not not_299 (not_299_out, OP0);
  not not_300 (not_300_out, F5);
  not not_301 (not_301_out, F4);
  not not_302 (not_302_out, F1);
  not not_303 (not_303_out, F0);
  not not_304 (not_304_out, OP5);
  not not_305 (not_305_out, OP4);
  not not_306 (not_306_out, OP3);
  not not_307 (not_307_out, OP1);
  not not_308 (not_308_out, OP0);
  not not_309 (not_309_out, OP5);
  not not_310 (not_310_out, OP4);
  not not_311 (not_311_out, OP3);
  not not_312 (not_312_out, OP1);
  not not_313 (not_313_out, OP4);
  not not_314 (not_314_out, OP3);
  not not_315 (not_315_out, OP2);
  not not_316 (not_316_out, OP4);
  not not_317 (not_317_out, OP2);
  not not_318 (not_318_out, OP5);
  not not_319 (not_319_out, OP4);
  not not_320 (not_320_out, OP3);
  not not_321 (not_321_out, OP2);
  not not_322 (not_322_out, OP1);
  not not_323 (not_323_out, OP0);
  not not_324 (not_324_out, F4);
  not not_325 (not_325_out, F3);
  not not_326 (not_326_out, F0);
  not not_327 (not_327_out, OP4);
  not not_328 (not_328_out, OP3);
  not not_329 (not_329_out, OP2);
  not not_330 (not_330_out, OP1);
  not not_331 (not_331_out, OP0);
  and and_1 (and_1_out, not_1_out, not_2_out, not_3_out, not_4_out, not_5_out, not_6_out, not_7_out, not_8_out, not_9_out, not_10_out, not_11_out, not_12_out);
  and and_2 (and_2_out, not_13_out, not_14_out, not_15_out, not_16_out, not_17_out, not_18_out, not_19_out, not_20_out, not_21_out, not_22_out, F1, F0);
  and and_3 (and_3_out, not_23_out, not_24_out, not_25_out, not_26_out, not_27_out, not_28_out, not_29_out, not_30_out, not_31_out, not_32_out, F1, not_33_out);
  and and_4 (and_4_out, not_34_out, not_35_out, not_36_out, not_37_out, not_38_out, not_39_out, F5, not_40_out, not_41_out, not_42_out, not_43_out, not_44_out);
  and and_5 (and_5_out, not_45_out, not_46_out, not_47_out, not_48_out, not_49_out, not_50_out, F5, not_51_out, not_52_out, not_53_out, not_54_out, F0);
  and and_6 (and_6_out, not_55_out, not_56_out, not_57_out, not_58_out, not_59_out, not_60_out, F5, not_61_out, not_62_out, not_63_out, F1, not_64_out);
  and and_7 (and_7_out, not_65_out, not_66_out, not_67_out, not_68_out, not_69_out, not_70_out, F5, not_71_out, not_72_out, F2, not_73_out, not_74_out);
  and and_8 (and_8_out, not_75_out, not_76_out, not_77_out, not_78_out, not_79_out, not_80_out, F5, not_81_out, not_82_out, F2, not_83_out, F0);
  and and_9 (and_9_out, not_84_out, not_85_out, not_86_out, not_87_out, not_88_out, not_89_out, F5, not_90_out, not_91_out, F2, F1, F0);
  and and_10 (and_10_out, not_92_out, not_93_out, not_94_out, not_95_out, not_96_out, not_97_out, F5, not_98_out, F3, not_99_out, F1, not_100_out);
  and and_11 (and_11_out, not_101_out, not_102_out, not_103_out, not_104_out, not_105_out, not_106_out, F5, not_107_out, F3, not_108_out, F1, F0);
  and and_12 (and_12_out, not_109_out, not_110_out, not_111_out, not_112_out, not_113_out, not_114_out, not_115_out, not_116_out, F3, not_117_out, not_118_out, not_119_out);
  and and_13 (and_13_out, not_120_out, not_121_out, not_122_out, not_123_out, not_124_out, not_125_out, not_126_out, not_127_out, F3, F2, not_128_out, not_129_out);
  and and_14 (and_14_out, not_130_out, not_131_out, not_132_out, OP2, not_133_out, not_134_out);
  and and_15 (and_15_out, not_135_out, not_136_out, not_137_out, OP2, not_138_out, OP0);
  and and_16 (and_16_out, not_139_out, not_140_out, OP3, not_141_out, not_142_out, not_143_out);
  and and_17 (and_17_out, not_144_out, not_145_out, OP3, OP2, not_146_out, not_147_out);
  and and_18 (and_18_out, not_148_out, not_149_out, OP3, not_150_out, not_151_out, OP0);
  and and_19 (and_19_out, not_152_out, not_153_out, OP3, not_154_out, OP1, not_155_out);
  and and_20 (and_20_out, not_156_out, not_157_out, OP3, OP2, not_158_out, OP0);
  and and_21 (and_21_out, OP5, not_159_out, not_160_out, not_161_out, OP1, OP0);
  and and_22 (and_22_out, OP5, not_162_out, OP3, not_163_out, OP1, OP0);
  and and_23 (and_23_out, not_164_out, not_165_out, not_166_out, not_167_out, not_168_out, not_169_out, F5, not_170_out, not_171_out, F2, F1, not_172_out);
  and and_24 (and_24_out, not_173_out, not_174_out, OP3, not_175_out, OP1, OP0);
  and and_25 (and_25_out, OP5, not_176_out, not_177_out, not_178_out, not_179_out, not_180_out);
  and and_26 (and_26_out, not_181_out, not_182_out, not_183_out, not_184_out, not_185_out, OP0);
  and and_27 (and_27_out, not_186_out, not_187_out, not_188_out, not_189_out, not_190_out, not_191_out, not_192_out, not_193_out, not_194_out, not_195_out, not_196_out, not_197_out);
  and and_28 (and_28_out, not_198_out, not_199_out, not_200_out, not_201_out, not_202_out, not_203_out, not_204_out, not_205_out, not_206_out, not_207_out, F1, F0);
  and and_29 (and_29_out, not_208_out, not_209_out, not_210_out, not_211_out, not_212_out, not_213_out, not_214_out, not_215_out, not_216_out, not_217_out, F1, not_218_out);
  and and_30 (and_30_out, not_219_out, not_220_out, not_221_out, not_222_out, not_223_out, not_224_out, F5, not_225_out, not_226_out, not_227_out, not_228_out, not_229_out);
  and and_31 (and_31_out, not_230_out, not_231_out, not_232_out, not_233_out, not_234_out, not_235_out, F5, not_236_out, not_237_out, not_238_out, not_239_out, F0);
  and and_32 (and_32_out, not_240_out, not_241_out, not_242_out, not_243_out, not_244_out, not_245_out, F5, not_246_out, not_247_out, not_248_out, F1, not_249_out);
  and and_33 (and_33_out, not_250_out, not_251_out, not_252_out, not_253_out, not_254_out, not_255_out, F5, not_256_out, not_257_out, F2, not_258_out, not_259_out);
  and and_34 (and_34_out, not_260_out, not_261_out, not_262_out, not_263_out, not_264_out, not_265_out, F5, not_266_out, not_267_out, F2, not_268_out, F0);
  and and_35 (and_35_out, not_269_out, not_270_out, not_271_out, not_272_out, not_273_out, not_274_out, F5, not_275_out, not_276_out, F2, F1, F0);
  and and_36 (and_36_out, not_277_out, not_278_out, not_279_out, not_280_out, not_281_out, not_282_out, F5, not_283_out, F3, not_284_out, F1, not_285_out);
  and and_37 (and_37_out, not_286_out, not_287_out, not_288_out, not_289_out, not_290_out, not_291_out, F5, not_292_out, F3, not_293_out, F1, F0);
  and and_38 (and_38_out, not_294_out, not_295_out, not_296_out, not_297_out, not_298_out, not_299_out, not_300_out, not_301_out, F3, F2, not_302_out, not_303_out);
  and and_39 (and_39_out, not_304_out, not_305_out, not_306_out, OP2, not_307_out, not_308_out);
  and and_40 (and_40_out, not_309_out, not_310_out, not_311_out, OP2, not_312_out, OP0);
  and and_41 (and_41_out, OP5, not_313_out, not_314_out, not_315_out, OP1, OP0);
  and and_42 (and_42_out, OP5, not_316_out, OP3, not_317_out, OP1, OP0);
  and and_43 (and_43_out, not_318_out, not_319_out, not_320_out, not_321_out, not_322_out, not_323_out, F5, not_324_out, not_325_out, F2, F1, not_326_out);
  and and_44 (and_44_out, OP5, not_327_out, not_328_out, not_329_out, not_330_out, not_331_out);
  or or_1 (R1_Used, and_1_out, and_2_out, and_3_out, and_4_out, and_5_out, and_6_out, and_7_out, and_8_out, and_9_out, and_10_out, and_11_out, and_12_out, and_13_out, and_14_out, and_15_out, and_16_out, and_17_out, and_18_out, and_19_out, and_20_out, and_21_out, and_22_out, and_23_out, and_24_out, and_25_out, and_26_out);
  or or_2 (R2_Used, and_27_out, and_28_out, and_29_out, and_30_out, and_31_out, and_32_out, and_33_out, and_34_out, and_35_out, and_36_out, and_37_out, and_38_out, and_39_out, and_40_out, and_41_out, and_42_out, and_43_out, and_44_out);
endmodule

module \数据相关检测  (
  input  [5:0] OP,
  input  [4:0] EX_WriteReg_num,
  input  EX_RegWrite,
  input  [4:0] MEM_WriteReg_num,
  input  MEM_RegWrite,
  input  [5:0] Func,
  input  [4:0] ID_R1_num,
  input  [4:0] ID_R2_num,
  output \数据相关 
);

  wire and_1_out, and_2_out, and_3_out, and_4_out, and_5_out, and_6_out, and_7_out, and_8_out, and_9_out,
       and_10_out, and_11_out, and_12_out, comparator_1_eq, comparator_2_eq, comparator_3_eq,
       comparator_4_eq, comparator_5_eq, comparator_6_eq, comparator_7_eq, comparator_8_eq, not_1_out,
       not_2_out, not_3_out, not_4_out, or_1_out, or_2_out, R1_USED, R2_USED;

  \源寄存器使用情况  \u_源寄存器使用情况_1  (
    .OP0(OP[0]), .OP1(OP[1]), .OP2(OP[2]), .OP3(OP[3]), .OP4(OP[4]), .OP5(OP[5]), .F0(Func[0]), .F1(Func[1]),
    .F2(Func[2]), .F3(Func[3]), .F4(Func[4]), .F5(Func[5]), .R1_Used(R1_USED), .R2_Used(R2_USED));
  Comparator #(.width(5), .mode("twosComplement")) comparator_1 (
    .a({5{1'b0}}), .b(ID_R1_num), .eq(comparator_1_eq));  // open: gt, lt
  Comparator #(.width(5), .mode("twosComplement")) comparator_2 (
    .a(EX_WriteReg_num), .b(ID_R1_num), .eq(comparator_2_eq));  // open: gt, lt
  Comparator #(.width(5), .mode("twosComplement")) comparator_3 (
    .a({5{1'b0}}), .b(ID_R2_num), .eq(comparator_3_eq));  // open: gt, lt
  Comparator #(.width(5), .mode("twosComplement")) comparator_4 (
    .a(EX_WriteReg_num), .b(ID_R2_num), .eq(comparator_4_eq));  // open: gt, lt
  Comparator #(.width(5), .mode("twosComplement")) comparator_5 (
    .a({5{1'b0}}), .b(ID_R1_num), .eq(comparator_5_eq));  // open: gt, lt
  Comparator #(.width(5), .mode("twosComplement")) comparator_6 (
    .a(MEM_WriteReg_num), .b(ID_R1_num), .eq(comparator_6_eq));  // open: gt, lt
  Comparator #(.width(5), .mode("twosComplement")) comparator_7 (
    .a({5{1'b0}}), .b(ID_R2_num), .eq(comparator_7_eq));  // open: gt, lt
  Comparator #(.width(5), .mode("twosComplement")) comparator_8 (
    .a(MEM_WriteReg_num), .b(ID_R2_num), .eq(comparator_8_eq));  // open: gt, lt
  not not_1 (not_1_out, comparator_1_eq);
  not not_2 (not_2_out, comparator_3_eq);
  not not_3 (not_3_out, comparator_5_eq);
  not not_4 (not_4_out, comparator_7_eq);
  and and_1 (and_1_out, not_1_out, comparator_2_eq);
  and and_2 (and_2_out, not_2_out, comparator_4_eq);
  and and_3 (and_3_out, not_3_out, comparator_6_eq);
  and and_4 (and_4_out, not_4_out, comparator_8_eq);
  and and_5 (and_5_out, and_1_out, R1_USED);
  and and_6 (and_6_out, and_2_out, R2_USED);
  and and_7 (and_7_out, and_3_out, R1_USED);
  and and_8 (and_8_out, and_4_out, R2_USED);
  or or_1 (or_1_out, and_5_out, and_6_out);
  or or_2 (or_2_out, and_7_out, and_8_out);
  and and_9 (and_9_out, 1'b1, EX_RegWrite);
  and and_10 (and_10_out, 1'b1, MEM_RegWrite);
  and and_11 (and_11_out, and_9_out, or_1_out);
  and and_12 (and_12_out, and_10_out, or_2_out);
  or or_3 (\数据相关 , and_11_out, and_12_out);

  // Other names for the same wires on the sheet: OP_CODE[5:0] = OP
endmodule

module Regifile2 (
  input  [31:0] Din,
  input  Clk,
  input  WE,
  input  [4:0] R1_num,
  input  [4:0] R2_num,
  input  [4:0] W_num,
  output [31:0] R1,
  output [31:0] R2
);

  wire and_1_out, and_2_out, comparator_1_eq, comparator_2_eq;
  wire [31:0] registerfile_1_p7, registerfile_1_p8;

  // RegisterFile registerfile_1: pin names not known; wires that end beside it: Din, Clk, WE, W_num, R1_num, R2_num, registerfile_1_p7, registerfile_1_p8
  Comparator #(.width(5), .mode("twosComplement")) comparator_1 (
    .a(R1_num), .b(W_num), .eq(comparator_1_eq));  // open: gt, lt
  Comparator #(.width(5), .mode("twosComplement")) comparator_2 (
    .a(R2_num), .b(W_num), .eq(comparator_2_eq));  // open: gt, lt
  and and_1 (and_1_out, comparator_1_eq, WE);
  and and_2 (and_2_out, comparator_2_eq, WE);
  Multiplexer #(.select(1), .width(32), .disabled("Z"), .enable("false")) multiplexer_1 (
    .in0(registerfile_1_p7), .in1(Din), .out(R1), .sel(and_1_out));
  Multiplexer #(.select(1), .width(32), .disabled("Z"), .enable("false")) multiplexer_2 (
    .in0(registerfile_1_p8), .in1(Din), .out(R2), .sel(and_2_out));
endmodule

module ResetPC (
  input  [31:0] in_1,
  output [31:0] out_2
);

  assign out_2 = in_1 & 32'hffff;  // AND_Gate and_1, 32 bits wide
endmodule

module LoadUse (
  input  [5:0] Ex_OP,
  input  [4:0] Ex_WriteReg_num,
  input  [4:0] Mem_WriteReg_num,
  input  Ex_RegWrite_num,
  input  Mem_RegWrite_num,
  input  MemToReg,
  input  [5:0] OP,
  input  [5:0] FUNC,
  input  [4:0] ID_R2_num,
  input  [4:0] ID_R1_num,
  output load_use,
  output [1:0] Choose_R1,
  output [1:0] Choose_R2
);

  wire and_1_out, and_2_out, and_3_out, and_4_out, and_5_out, and_6_out, and_7_out, and_8_out, and_9_out,
       and_12_out, comparator_1_eq, comparator_2_eq, comparator_3_eq, comparator_4_eq, comparator_5_eq,
       comparator_6_eq, comparator_7_eq, comparator_8_eq, comparator_9_eq, comparator_10_eq, load_use1,
       load_use2, not_1_out, not_2_out, not_3_out, not_4_out, or_2_out, or_3_out, R1_USED, R2_USED;
  wire [1:0] and_15_out, and_16_out;

  \源寄存器使用情况  \u_源寄存器使用情况_1  (
    .OP0(OP[0]), .OP1(OP[1]), .OP2(OP[2]), .OP3(OP[3]), .OP4(OP[4]), .OP5(OP[5]), .F0(FUNC[0]), .F1(FUNC[1]),
    .F2(FUNC[2]), .F3(FUNC[3]), .F4(FUNC[4]), .F5(FUNC[5]), .R1_Used(R1_USED), .R2_Used(R2_USED));
  Comparator #(.width(5), .mode("twosComplement")) comparator_1 (
    .a(Ex_WriteReg_num), .b(ID_R2_num), .eq(comparator_1_eq));  // open: gt, lt
  Comparator #(.width(5), .mode("twosComplement")) comparator_2 (
    .a(Mem_WriteReg_num), .b(ID_R2_num), .eq(comparator_2_eq));  // open: gt, lt
  Comparator #(.width(5), .mode("twosComplement")) comparator_3 (
    .a(ID_R2_num), .b({5{1'b0}}), .eq(comparator_3_eq));  // open: gt, lt
  Comparator #(.width(5), .mode("twosComplement")) comparator_4 (
    .a(Ex_WriteReg_num), .b(ID_R1_num), .eq(comparator_4_eq));  // open: gt, lt
  Comparator #(.width(5), .mode("twosComplement")) comparator_5 (
    .a(Mem_WriteReg_num), .b(ID_R1_num), .eq(comparator_5_eq));  // open: gt, lt
  Comparator #(.width(5), .mode("twosComplement")) comparator_6 (
    .a(ID_R1_num), .b({5{1'b0}}), .eq(comparator_6_eq));  // open: gt, lt
  or or_1 (load_use, load_use1, load_use2);
  not not_1 (not_1_out, comparator_3_eq);
  not not_2 (not_2_out, comparator_6_eq);
  and and_1 (and_1_out, comparator_1_eq, not_1_out);
  and and_2 (and_2_out, comparator_2_eq, not_1_out);
  and and_3 (and_3_out, comparator_4_eq, not_2_out);
  and and_4 (and_4_out, comparator_5_eq, not_2_out);
  and and_5 (and_5_out, R1_USED, and_3_out);
  and and_6 (and_6_out, and_4_out, R1_USED);
  Comparator #(.width(6), .mode("twosComplement")) comparator_7 (
    .a(Ex_OP), .b(6'b100000), .eq(comparator_7_eq));  // open: gt, lt
  Comparator #(.width(6), .mode("twosComplement")) comparator_8 (
    .a(Ex_OP), .b(6'b100011), .eq(comparator_8_eq));  // open: gt, lt
  and and_7 (and_7_out, R2_USED, and_1_out);
  and and_8 (and_8_out, and_2_out, R2_USED);
  Comparator #(.width(6), .mode("twosComplement")) comparator_9 (
    .a(Ex_OP), .b(6'b100000), .eq(comparator_9_eq));  // open: gt, lt
  Comparator #(.width(6), .mode("twosComplement")) comparator_10 (
    .a(Ex_OP), .b(6'b100011), .eq(comparator_10_eq));  // open: gt, lt
  or or_2 (or_2_out, comparator_9_eq, comparator_10_eq);
  and and_9 (and_9_out, and_5_out, Ex_RegWrite_num);
  and and_10 (and_15_out[1], Mem_RegWrite_num, and_6_out);
  and and_11 (load_use2, or_3_out, and_12_out);
  or or_3 (or_3_out, comparator_7_eq, comparator_8_eq);
  and and_12 (and_12_out, and_7_out, Ex_RegWrite_num);
  and and_13 (and_16_out[1], Mem_RegWrite_num, and_8_out);
  and and_14 (load_use1, or_2_out, and_9_out);
  not not_3 (not_3_out, or_2_out);
  not not_4 (not_4_out, or_3_out);
  and and_15 (and_15_out[0], not_3_out, and_9_out);
  and and_16 (and_16_out[0], not_4_out, and_12_out);
  Multiplexer #(.select(3), .width(2), .disabled("Z"), .enable("false")) multiplexer_1 (
    .in0(2'b00), .in1(2'b01), .in2(2'b10), .in3(2'b01), .in4(2'b00), .in5(2'b01), .in6(2'b11), .in7(2'b01),
    .out(Choose_R1), .sel({MemToReg, and_15_out}));
  Multiplexer #(.select(3), .width(2), .disabled("Z"), .enable("false")) multiplexer_2 (
    .in0(2'b00), .in1(2'b01), .in2(2'b10), .in3(2'b01), .in4(2'b00), .in5(2'b01), .in6(2'b11), .in7(2'b01),
    .out(Choose_R2), .sel({MemToReg, and_16_out}));
endmodule

module stack (
  input  [1:0] INPUT,
  input  clk,
  input  \int ,
  input  eret,
  output [1:0] out_5
);

  wire and_1_out, and_2_out, and_3_out, and_4_out, and_5_out, and_6_out, not_1_out, not_2_out, not_3_out,
       not_4_out, or_1_out;
  wire [1:0] counter_1_q, demultiplexer_1_out0, demultiplexer_1_out1, demultiplexer_1_out2, s0_q, s1_q, s2_q,
       subtractor_1_out;

  or or_1 (or_1_out, \int , eret);
  Counter #(.width(2), .max('h3), .ongoal("wrap"), .trigger("rising"), .behavior("new")) counter_1 (
    .count(or_1_out), .Q(counter_1_q), .clk(clk), .down(eret));  // open: load, D, carry, clr, preset
  Demultiplexer #(.select(2), .width(2), .tristate("false"), .disabled("Z"), .enable("false")) demultiplexer_1 (
    .out0(demultiplexer_1_out0), .out1(demultiplexer_1_out1), .out2(demultiplexer_1_out2), .in(INPUT),
    .sel(counter_1_q));  // open: out3
  not not_1 (not_1_out, counter_1_q[1]);
  and and_1 (and_1_out, not_1_out, not_2_out);
  not not_2 (not_2_out, counter_1_q[0]);
  not not_3 (not_3_out, counter_1_q[1]);
  and and_2 (and_2_out, not_3_out, counter_1_q[0]);
  and and_3 (and_3_out, counter_1_q[1], not_4_out);
  not not_4 (not_4_out, counter_1_q[0]);
  and and_4 (and_4_out, \int , and_1_out);
  Register #(.width(2), .trigger("rising"), .Select("low")) s0 (
    .D(demultiplexer_1_out0), .en(and_4_out), .Q(s0_q), .clk(clk));  // open: clr
  Register #(.width(2), .trigger("rising"), .Select("low")) s1 (
    .D(demultiplexer_1_out1), .en(and_5_out), .Q(s1_q), .clk(clk));  // open: clr
  and and_5 (and_5_out, and_2_out, \int );
  Register #(.width(2), .trigger("rising"), .Select("low")) s2 (
    .D(demultiplexer_1_out2), .en(and_6_out), .Q(s2_q), .clk(clk));  // open: clr
  and and_6 (and_6_out, and_3_out, \int );
  Multiplexer #(.select(2), .width(2), .disabled("Z"), .enable("false")) multiplexer_1 (
    .in0(s0_q), .in1(s1_q), .in2(s2_q), .in3(2'b00), .out(out_5), .sel(subtractor_1_out));
  Subtractor #(.width(2)) subtractor_1 (.a(counter_1_q), .b(2'b01), .out(subtractor_1_out));  // open: bin, bout
endmodule
